# Fritzing sketch Skeleton_Sketch (saved by Fritzing 0.9.6b)
breadboards: 1

parts:
  J2 = female pin header, 2 pins [form="♀ (female)"]
  J1 = male pin header, 2 pins [form="♂ (male)"]
  J3 = female pin header, 2 pins [form="♀ (female)"]
  J4 = male pin header, 2 pins [form="♂ (male)"]
  IC1 = Skelenton - 8 pins [chip_label=Skeleton package="DIP (Dual Inline) [THT]"]

nets:
  N1: J2.pin1, IC1.pin6
  N2: J2.pin2, IC1.pin5
  N3: J1.pin1, IC1.pin1
  GND: J1.pin2, J3.pin2, J4.pin2, IC1.pin4
  N4: J3.pin1, IC1.pin3
  N5: J4.pin1, IC1.pin2
  3.3V: IC1.pin7
  5V: IC1.pin8

custom parts:
  Skelenton - 8 pins: A DIP stand-in part for whatever IC you want. With 8 pins on a 300mil dual inline package (DIP) footprint.
