# Fritzing sketch BlockDetectorWith BD20 (saved by Fritzing 0.9.6b)
stripboards: 1

parts:
  IO1 = PCF8574N [package="DIP16 [THT]"]
  IO2 = PCF8574N [package="DIP16 [THT]"]
  IO3 = PCF8574N [package="DIP16 [THT]"]
  IO4 = PCF8574N [package="DIP16 [THT]"]
  R1 = female pin header, 6 pins [form="♀ (female)"]
  R2 = female pin header, 6 pins [form="♀ (female)"]
  J1 = male pin header, 4 pins [form="♂ (male)"]
  J2 = male pin header, 4 pins [form="♂ (male)"]
  R3 = female pin header, 6 pins [form="♀ (female)"]
  R4 = female pin header, 6 pins [form="♀ (female)"]
  R5 = female pin header, 6 pins [form="♀ (female)"]
  R6 = female pin header, 6 pins [form="♀ (female)"]
  R7 = female pin header, 6 pins [form="♀ (female)"]
  R8 = female pin header, 6 pins [form="♀ (female)"]
  J3 = male pin header, 4 pins [form="♂ (male)"]
  J4 = male pin header, 4 pins [form="♂ (male)"]
  J5 = male pin header, 4 pins [form="♂ (male)"]
  J6 = male pin header, 4 pins [form="♂ (male)"]
  J7 = male pin header, 4 pins [form="♂ (male)"]
  J8 = male pin header, 4 pins [form="♂ (male)"]
  J9 = male pin header, 2 pins [form="♂ (male)"]
  R9 = Resistor [tolerance=±5% power=0.25 resistance=10k package=THT]
  J12 = male pin header, 2 pins [form="♂ (male)"]
  J13 = male pin header, 2 pins [form="♂ (male)"]
  R10 = Resistor [tolerance=±5% power=0.25 resistance=10k package=THT]
  R11 = Resistor [tolerance=±5% power=0.25 resistance=10k package=THT]

nets:
  GND: IO1.A0, IO1.A1, IO1.GND, IO2.A1, IO2.GND, IO3.A0, IO3.GND, IO4.GND, R2.pin5, R4.pin5, R6.pin5, R8.pin5, J9.pin1, J13.pin2
  A2: IO1.A2, IO2.A2, IO3.A2, IO4.A2, J9.pin2, R9.Pin_0
  N1: IO1.P0, R2.pin1, J2.pin1
  N2: IO1.P1, R2.pin2, J2.pin2
  N3: IO1.P2, R2.pin3, J2.pin3
  N4: IO1.P3, R2.pin4, J2.pin4
  N5: IO1.P4, R1.pin5, J1.pin4
  N6: IO1.P5, R1.pin4, J1.pin3
  N7: IO1.P6, R1.pin3, J1.pin2
  N8: IO1.P7, R1.pin2, J1.pin1
  N9: IO1.INT, R1.pin1
  SCL: IO1.SCL, IO2.SCL, IO3.SCL, IO4.SCL, J12.pin1, R10.Pin_0
  SDA: IO1.SDA, IO2.SDA, IO3.SDA, IO4.SDA, J12.pin2, R11.Pin_0
  3.3V: IO1.VCC, IO2.A0, IO2.VCC, IO3.A1, IO3.VCC, IO4.A0, IO4.A1, IO4.VCC, R1.pin6, R2.pin6, R3.pin6, R4.pin6, R5.pin6, R6.pin6, R7.pin6, R8.pin6, R9.Pin_1, J13.pin1, R10.Pin_1, R11.Pin_1
  N10: IO2.P0, R4.pin1, J4.pin1
  N11: IO2.P1, R4.pin2, J4.pin2
  N12: IO2.P2, R4.pin3, J4.pin3
  N13: IO2.P3, R4.pin4, J4.pin4
  N14: IO2.P4, R3.pin5, J3.pin4
  N15: IO2.P5, R3.pin4, J3.pin3
  N16: IO2.P6, R3.pin3, J3.pin2
  N17: IO2.P7, R3.pin2, J3.pin1
  N18: IO2.INT, R3.pin1
  N19: IO3.P0, R6.pin1, J6.pin1
  N20: IO3.P1, R6.pin2, J6.pin2
  N21: IO3.P2, R6.pin3, J6.pin3
  N22: IO3.P3, R6.pin4, J6.pin4
  N23: IO3.P4, R5.pin5, J5.pin4
  N24: IO3.P5, R5.pin4, J5.pin3
  N25: IO3.P6, R5.pin3, J5.pin2
  N26: IO3.P7, R5.pin2, J5.pin1
  N27: IO3.INT, R5.pin1
  N28: IO4.P0, R8.pin1, J8.pin1
  N29: IO4.P1, R8.pin2, J8.pin2
  N30: IO4.P2, R8.pin3, J8.pin3
  N31: IO4.P3, R8.pin4, J8.pin4
  N32: IO4.P4, R7.pin5, J7.pin4
  N33: IO4.P5, R7.pin4, J7.pin3
  N34: IO4.P6, R7.pin3, J7.pin2
  N35: IO4.P7, R7.pin2, J7.pin1
  N36: IO4.INT, R7.pin1

custom parts:
  PCF8574N: Remote 8-Bit I/O Expander for I 2C Bus
