# Fritzing sketch PCF8574_ULN2803 (saved by Fritzing 0.9.6b)
circuit board: 7.42234cm x 15.5cm

parts:
  PCF8574N1 = PCF8574N [package="DIP16 [THT]"]
  ULN2803A1 = Darlington Driver [package=dil18]
  J1 = double row male pin header, 18 pins [form="♂ (male)"]
  PCF8574N8 = PCF8574N [package="DIP16 [THT]"]
  ULN2803A8 = Darlington Driver [package=dil18]
  J8 = double row male pin header, 18 pins [form="♂ (male)"]
  PCF8574N7 = PCF8574N [package="DIP16 [THT]"]
  PCF8574N2 = PCF8574N [package="DIP16 [THT]"]
  ULN2803A2 = Darlington Driver [package=dil18]
  ULN2803A7 = Darlington Driver [package=dil18]
  J7 = double row male pin header, 18 pins [form="♂ (male)"]
  J2 = double row male pin header, 18 pins [form="♂ (male)"]
  PCF8574N6 = PCF8574N [package="DIP16 [THT]"]
  PCF8574N3 = PCF8574N [package="DIP16 [THT]"]
  ULN2803A3 = Darlington Driver [package=dil18]
  ULN2803A6 = Darlington Driver [package=dil18]
  J6 = double row male pin header, 18 pins [form="♂ (male)"]
  J3 = double row male pin header, 18 pins [form="♂ (male)"]
  PCF8574N5 = PCF8574N [package="DIP16 [THT]"]
  PCF8574N4 = PCF8574N [package="DIP16 [THT]"]
  ULN2803A4 = Darlington Driver [package=dil18]
  ULN2803A6_2 = Darlington Driver [package=dil18]
  J5 = double row male pin header, 18 pins [form="♂ (male)"]
  J4 = double row male pin header, 18 pins [form="♂ (male)"]
  x3 = female pin header, 29 pins [form="♀ (female)"]  # not connected
  ESP32 = DOIT Esp32 DevKit v1 (30 pins long, 11 pins width) [part_number=ESP32S-PIN30]
  J9 = female pin header, 2 pins [form="♀ (female)"]
  HW613 = female pin header, 4 pins [form="♀ (female)" part_number=HW613-3V3]
  Q1 = Basic FET P-Channel [part_number=FQP27P06 package="TO220 [THT]"]
  C1 = Ceramic Capacitor [capacitance=100nF voltage=35V package="100 mil [THT, multilayer]"]
  C2 = Electrolytic Capacitor [capacitance=10µF voltage=10V package="100 mil [THT, electrolytic]"]
  Pad1 = Pad [width=2 height=2 connect=center]
  Pad2 = Pad [width=2 height=2 connect=center]
  LD1117 = Voltage Regulator LM1117 [package=sot223]
  A1 = olimex ESP32-POE-ISO

nets:
  GND: PCF8574N1.A0, PCF8574N1.A1, PCF8574N1.A2, PCF8574N1.GND, ULN2803A1.9, PCF8574N8.GND, ULN2803A8.9, PCF8574N7.A0, PCF8574N7.GND, PCF8574N2.A1, PCF8574N2.A2, PCF8574N2.GND, ULN2803A2.9, ULN2803A7.9, PCF8574N6.A1, PCF8574N6.GND, PCF8574N3.A0, PCF8574N3.A2, PCF8574N3.GND, ULN2803A3.9, ULN2803A6.9, PCF8574N5.A0, PCF8574N5.A1, PCF8574N5.GND, PCF8574N4.A2, PCF8574N4.GND, ULN2803A4.9, ULN2803A6_2.9, ESP32.GND, J9.pin2, HW613.pin3, Q1.gate, C1.0, C2.-, LD1117.GND, A1.Pin_3, A1.Pin_32
  N1: PCF8574N1.P0, ULN2803A1.1
  N2: PCF8574N1.P1, ULN2803A1.2
  N3: PCF8574N1.P2, ULN2803A1.3
  N4: PCF8574N1.P3, ULN2803A1.4
  N5: PCF8574N1.P4, ULN2803A1.5
  N6: PCF8574N1.P5, ULN2803A1.6
  N7: PCF8574N1.P6, ULN2803A1.7
  N8: PCF8574N1.P7, ULN2803A1.8
  SCL: PCF8574N1.SCL, PCF8574N8.SCL, PCF8574N7.SCL, PCF8574N2.SCL, PCF8574N6.SCL, PCF8574N3.SCL, PCF8574N5.SCL, PCF8574N4.SCL, ESP32.D22, A1.Pin_16, A1.Pin_27
  SDA: PCF8574N1.SDA, PCF8574N8.SDA, PCF8574N7.SDA, PCF8574N2.SDA, PCF8574N6.SDA, PCF8574N3.SDA, PCF8574N5.SDA, PCF8574N4.SDA, ESP32.D21, A1.Pin_13, A1.Pin_28
  3.3V: PCF8574N1.VCC, PCF8574N8.A0, PCF8574N8.A1, PCF8574N8.A2, PCF8574N8.VCC, PCF8574N7.A1, PCF8574N7.A2, PCF8574N7.VCC, PCF8574N2.A0, PCF8574N2.VCC, PCF8574N6.A0, PCF8574N6.A2, PCF8574N6.VCC, PCF8574N3.A1, PCF8574N3.VCC, PCF8574N5.A2, PCF8574N5.VCC, PCF8574N4.A0, PCF8574N4.A1, PCF8574N4.VCC, ESP32.3V3, C2.+, Pad1.pad, Pad2.pad, LD1117.OUT, A1.Pin_2, A1.Pin_31
  12V: ULN2803A1.10, J1.pin9, J1.pin10, J1.pin11, J1.pin12, J1.pin13, J1.pin14, J1.pin15, J1.pin16, J1.pin17, J1.pin18, ULN2803A8.10, J8.pin9, J8.pin10, J8.pin11, J8.pin12, J8.pin13, J8.pin14, J8.pin15, J8.pin16, J8.pin17, J8.pin18, ULN2803A2.10, ULN2803A7.10, J7.pin9, J7.pin10, J7.pin11, J7.pin12, J7.pin13, J7.pin14, J7.pin15, J7.pin16, J7.pin17, J7.pin18, J2.pin9, J2.pin10, J2.pin11, J2.pin12, J2.pin13, J2.pin14, J2.pin15, J2.pin16, J2.pin17, J2.pin18, ULN2803A3.10, ULN2803A6.10, J6.pin9, J6.pin10, J6.pin11, J6.pin12, J6.pin13, J6.pin14, J6.pin15, J6.pin16, J6.pin17, J6.pin18, J3.pin9, J3.pin10, J3.pin11, J3.pin12, J3.pin13, J3.pin14, J3.pin15, J3.pin16, J3.pin17, J3.pin18, ULN2803A4.10, ULN2803A6_2.10, J5.pin9, J5.pin10, J5.pin11, J5.pin12, J5.pin13, J5.pin14, J5.pin15, J5.pin16, J5.pin17, J5.pin18, J4.pin9, J4.pin10, J4.pin11, J4.pin12, J4.pin13, J4.pin14, J4.pin15, J4.pin16, J4.pin17, J4.pin18, HW613.pin2, Q1.source
  N9: ULN2803A1.11, J1.pin8
  N10: ULN2803A1.12, J1.pin7
  N11: ULN2803A1.13, J1.pin6
  N12: ULN2803A1.14, J1.pin5
  N13: ULN2803A1.15, J1.pin4
  N14: ULN2803A1.16, J1.pin3
  N15: ULN2803A1.17, J1.pin2
  N16: ULN2803A1.18, J1.pin1
  N17: PCF8574N8.P0, ULN2803A8.1
  N18: PCF8574N8.P1, ULN2803A8.2
  N19: PCF8574N8.P2, ULN2803A8.3
  N20: PCF8574N8.P3, ULN2803A8.4
  N21: PCF8574N8.P4, ULN2803A8.5
  N22: PCF8574N8.P5, ULN2803A8.6
  N23: PCF8574N8.P6, ULN2803A8.7
  N24: PCF8574N8.P7, ULN2803A8.8
  N25: ULN2803A8.11, J8.pin8
  N26: ULN2803A8.12, J8.pin7
  N27: ULN2803A8.13, J8.pin6
  N28: ULN2803A8.14, J8.pin5
  N29: ULN2803A8.15, J8.pin4
  N30: ULN2803A8.16, J8.pin3
  N31: ULN2803A8.17, J8.pin2
  N32: ULN2803A8.18, J8.pin1
  N33: PCF8574N7.P0, ULN2803A7.1
  N34: PCF8574N7.P1, ULN2803A7.2
  N35: PCF8574N7.P2, ULN2803A7.3
  N36: PCF8574N7.P3, ULN2803A7.4
  N37: PCF8574N7.P4, ULN2803A7.5
  N38: PCF8574N7.P5, ULN2803A7.6
  N39: PCF8574N7.P6, ULN2803A7.7
  N40: PCF8574N7.P7, ULN2803A7.8
  N41: PCF8574N2.P0, ULN2803A2.1
  N42: PCF8574N2.P1, ULN2803A2.2
  N43: PCF8574N2.P2, ULN2803A2.3
  N44: PCF8574N2.P3, ULN2803A2.4
  N45: PCF8574N2.P4, ULN2803A2.5
  N46: PCF8574N2.P5, ULN2803A2.6
  N47: PCF8574N2.P6, ULN2803A2.7
  N48: PCF8574N2.P7, ULN2803A2.8
  N49: ULN2803A2.11, J2.pin8
  N50: ULN2803A2.12, J2.pin7
  N51: ULN2803A2.13, J2.pin6
  N52: ULN2803A2.14, J2.pin5
  N53: ULN2803A2.15, J2.pin4
  N54: ULN2803A2.16, J2.pin3
  N55: ULN2803A2.17, J2.pin2
  N56: ULN2803A2.18, J2.pin1
  N57: ULN2803A7.11, J7.pin8
  N58: ULN2803A7.12, J7.pin7
  N59: ULN2803A7.13, J7.pin6
  N60: ULN2803A7.14, J7.pin5
  N61: ULN2803A7.15, J7.pin4
  N62: ULN2803A7.16, J7.pin3
  N63: ULN2803A7.17, J7.pin2
  N64: ULN2803A7.18, J7.pin1
  N65: PCF8574N6.P0, ULN2803A6.1
  N66: PCF8574N6.P1, ULN2803A6.2
  N67: PCF8574N6.P2, ULN2803A6.3
  N68: PCF8574N6.P3, ULN2803A6.4
  N69: PCF8574N6.P4, ULN2803A6.5
  N70: PCF8574N6.P5, ULN2803A6.6
  N71: PCF8574N6.P6, ULN2803A6.7
  N72: PCF8574N6.P7, ULN2803A6.8
  N73: PCF8574N3.P0, ULN2803A3.1
  N74: PCF8574N3.P1, ULN2803A3.2
  N75: PCF8574N3.P2, ULN2803A3.3
  N76: PCF8574N3.P3, ULN2803A3.4
  N77: PCF8574N3.P4, ULN2803A3.5
  N78: PCF8574N3.P5, ULN2803A3.6
  N79: PCF8574N3.P6, ULN2803A3.7
  N80: PCF8574N3.P7, ULN2803A3.8
  N81: ULN2803A3.11, J3.pin8
  N82: ULN2803A3.12, J3.pin7
  N83: ULN2803A3.13, J3.pin6
  N84: ULN2803A3.14, J3.pin5
  N85: ULN2803A3.15, J3.pin4
  N86: ULN2803A3.16, J3.pin3
  N87: ULN2803A3.17, J3.pin2
  N88: ULN2803A3.18, J3.pin1
  N89: ULN2803A6.11, J6.pin8
  N90: ULN2803A6.12, J6.pin7
  N91: ULN2803A6.13, J6.pin6
  N92: ULN2803A6.14, J6.pin5
  N93: ULN2803A6.15, J6.pin4
  N94: ULN2803A6.16, J6.pin3
  N95: ULN2803A6.17, J6.pin2
  N96: ULN2803A6.18, J6.pin1
  N97: PCF8574N5.P0, ULN2803A6_2.1
  N98: PCF8574N5.P1, ULN2803A6_2.2
  N99: PCF8574N5.P2, ULN2803A6_2.3
  N100: PCF8574N5.P3, ULN2803A6_2.4
  N101: PCF8574N5.P4, ULN2803A6_2.5
  N102: PCF8574N5.P5, ULN2803A6_2.6
  N103: PCF8574N5.P6, ULN2803A6_2.7
  N104: PCF8574N5.P7, ULN2803A6_2.8
  N105: PCF8574N4.P0, ULN2803A4.1
  N106: PCF8574N4.P1, ULN2803A4.2
  N107: PCF8574N4.P2, ULN2803A4.3
  N108: PCF8574N4.P3, ULN2803A4.4
  N109: PCF8574N4.P4, ULN2803A4.5
  N110: PCF8574N4.P5, ULN2803A4.6
  N111: PCF8574N4.P6, ULN2803A4.7
  N112: PCF8574N4.P7, ULN2803A4.8
  N113: ULN2803A4.11, J4.pin8
  N114: ULN2803A4.12, J4.pin7
  N115: ULN2803A4.13, J4.pin6
  N116: ULN2803A4.14, J4.pin5
  N117: ULN2803A4.15, J4.pin4
  N118: ULN2803A4.16, J4.pin3
  N119: ULN2803A4.17, J4.pin2
  N120: ULN2803A4.18, J4.pin1
  N121: ULN2803A6_2.11, J5.pin8
  N122: ULN2803A6_2.12, J5.pin7
  N123: ULN2803A6_2.13, J5.pin6
  N124: ULN2803A6_2.14, J5.pin5
  N125: ULN2803A6_2.15, J5.pin4
  N126: ULN2803A6_2.16, J5.pin3
  N127: ULN2803A6_2.17, J5.pin2
  N128: ULN2803A6_2.18, J5.pin1
  5V: ESP32.VIN, HW613.pin4, C1.1, LD1117.IN, A1.Pin_1
  N129: J9.pin1, Q1.drain

notes:
  GND
  +5V
  +12V
  EN

custom parts:
  PCF8574N: 8-bit parallel-load shift registers sekt1953@gmail.com
  DOIT Esp32 DevKit v1 (30 pins long, 11 pins width): The DOIT Esp32 DevKit v1 is one of the development board created by DOIT to evaluate the ESP-WROOM-32 module. It is based on the ESP32 microcontroller that boasts Wifi, Bluetooth, Ethernet and Low Power support all in a single chip. (vanepp) made breadboard work, adjusted pin numbering and labels and reduced size of schematic and cleaned up pcb. This chip is 30pins long (2 x15) and 11 pins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
  Voltage Regulator LM1117: Voltage Regulator LM1117 Standard adjustable voltage regulator but in SMD form. Spark Fun Electronics SKU : COM-00595
  olimex ESP32-POE-ISO: ESP32-PoE is an IoT WIFI/BLE/Ethernet development board with Power-Over-Ethernet feature.
