# Fritzing sketch Reverseprotection  (saved by Fritzing 0.9.6b)
circuit board: 5.21563cm x 2.53683cm
breadboards: 1

parts:
  Power_IN = male pin header, 2 pins [form="♂ (male)"]
  HW-613/3V3 = HW-613 [package=THT]
  FQP27P6 = FQP27P06 [package=THT]
  J1 = male pin header, 2 pins [form="♂ (male)"]

nets:
  N1: Power_IN.pin1, FQP27P6.pin2
  GND: Power_IN.pin2, HW-613/3V3.pin2, FQP27P6.pin1, J1.pin2
  3.3V: HW-613/3V3.pin1, J1.pin1
  12V: HW-613/3V3.pin3, FQP27P6.pin3

custom parts:
  HW-613: DC-DC Converter, max 24V input
  FQP27P06: Power Mosfet
