# Fritzing sketch BlockDetectormed_6_Dioder_Optokobler (saved by Fritzing 0.9.6b)
circuit board: 10.43cm x 5cm
breadboards: 1

parts:
  R8 = Resistor [tolerance=±5% power=0.25 resistance=22 package=THT]
  R6 = Resistor [tolerance=±5% power=0.25 resistance=22 package=THT]
  R4 = Resistor [tolerance=±5% power=0.25 resistance=22 package=THT]
  R2 = Resistor [tolerance=±5% power=0.25 resistance=22 package=THT]
  R7 = Resistor [tolerance=±5% power=0.25 resistance=22 package=THT]
  R5 = Resistor [tolerance=±5% power=0.25 resistance=22 package=THT]
  R3 = Resistor [tolerance=±5% power=0.25 resistance=22 package=THT]
  R1 = Resistor [tolerance=±5% power=0.25 resistance=22 package=THT]
  R12 = Resistor [tolerance=±5% power=0.25 resistance=22 package=THT]
  R17 = Resistor [tolerance=±5% power=0.25 resistance=22 package=THT]
  R10 = Resistor [tolerance=±5% power=0.25 resistance=22 package=THT]
  R16 = Resistor [tolerance=±5% power=0.25 resistance=22 package=THT]
  R13 = Resistor [tolerance=±5% power=0.25 resistance=22 package=THT]
  R11 = Resistor [tolerance=±5% power=0.25 resistance=22 package=THT]
  R14 = Resistor [tolerance=±5% power=0.25 resistance=22 package=THT]
  R15 = Resistor [tolerance=±5% power=0.25 resistance=22 package=THT]
  U3 = TLP620-4 [package="DIP (Dual Inline) [THT]"]
  U1 = TLP620-4 [package="DIP (Dual Inline) [THT]"]
  U2 = TLP620-4 [package="DIP (Dual Inline) [THT]"]
  U5 = TLP620-4 [package="DIP (Dual Inline) [THT]"]
  U6 = TLP620-4 [package="DIP (Dual Inline) [THT]"]
  R24 = Resistor [tolerance=±5% power=0.25 resistance=220 package=THT]
  R23 = Resistor [tolerance=±5% power=0.25 resistance=22 package=THT]
  R20 = Resistor [tolerance=±5% power=0.25 resistance=22 package=THT]
  R22 = Resistor [tolerance=±5% power=0.25 resistance=22 package=THT]
  R25 = Resistor [tolerance=±5% power=0.25 resistance=22 package=THT]
  R19 = Resistor [tolerance=±5% power=0.25 resistance=22 package=THT]
  R26 = Resistor [tolerance=±5% power=0.25 resistance=22 package=THT]
  R21 = Resistor [tolerance=±5% power=0.25 resistance=22 package=THT]
  U8 = TLP620-4 [package="DIP (Dual Inline) [THT]"]
  R33 = Resistor [tolerance=±5% power=0.25 resistance=22 package=THT]
  R32 = Resistor [tolerance=±5% power=0.25 resistance=22 package=THT]
  R29 = Resistor [tolerance=±5% power=0.25 resistance=22 package=THT]
  R31 = Resistor [tolerance=±5% power=0.25 resistance=22 package=THT]
  R34 = Resistor [tolerance=±5% power=0.25 resistance=22 package=THT]
  R28 = Resistor [tolerance=±5% power=0.25 resistance=22 package=THT]
  R35 = Resistor [tolerance=±5% power=0.25 resistance=22 package=THT]
  R30 = Resistor [tolerance=±5% power=0.25 resistance=22 package=THT]
  J2 = male pin header, 9 pins [form="♂ (male)"]
  J4 = male pin header, 9 pins [form="♂ (male)"]
  J6 = male pin header, 9 pins [form="♂ (male)"]
  J8 = male pin header, 9 pins [form="♂ (male)"]
  U4 = TLP620-4 [package="DIP (Dual Inline) [THT]"]
  U7 = TLP620-4 [package="DIP (Dual Inline) [THT]"]
  J1 = screw terminal, 9 pins
  J3 = screw terminal, 9 pins
  J5 = screw terminal, 9 pins
  J7 = screw terminal, 9 pins
  R9 = 8 Resistor Network [part_number="SIL 8x470R" package="SIP (Single Inline)"]
  R18 = 8 Resistor Network [part_number="SIL 8x470R" package="SIP (Single Inline)"]
  R27 = 8 Resistor Network [part_number="SIL 8x470R" package="SIP (Single Inline)"]
  R36 = 8 Resistor Network [part_number="SIL 8x470R" package="SIP (Single Inline)"]

nets:
  N1: R8.Pin_0, J1.pin8, R9.2
  N2: R8.Pin_1, U2.pin2
  N3: R6.Pin_0, J1.pin6, R9.4
  N4: R6.Pin_1, U2.pin4
  N5: R4.Pin_0, J1.pin4, R9.6
  N6: R4.Pin_1, U2.pin6
  N7: R2.Pin_0, J1.pin2, R9.8
  N8: R2.Pin_1, U2.pin8
  N9: R7.Pin_0, J1.pin7, R9.3
  N10: R7.Pin_1, U1.pin2
  N11: R5.Pin_0, J1.pin5, R9.5
  N12: R5.Pin_1, U1.pin4
  N13: R3.Pin_0, J1.pin3, R9.7
  N14: R3.Pin_1, U1.pin6
  N15: R1.Pin_0, J1.pin1, R9.9
  N16: R1.Pin_1, U1.pin8
  N17: R12.Pin_0, J3.pin3, R18.7
  N18: R12.Pin_1, U3.pin6
  N19: R17.Pin_0, J3.pin8, R18.2
  N20: R17.Pin_1, U4.pin2
  N21: R10.Pin_0, J3.pin1, R18.9
  N22: R10.Pin_1, U3.pin8
  N23: R16.Pin_0, J3.pin7, R18.3
  N24: R16.Pin_1, U3.pin2
  N25: R13.Pin_0, J3.pin4, R18.6
  N26: R13.Pin_1, U4.pin6
  N27: R11.Pin_0, J3.pin2, R18.8
  N28: R11.Pin_1, U4.pin8
  N29: R14.Pin_0, J3.pin5, R18.5
  N30: R14.Pin_1, U3.pin4
  N31: R15.Pin_0, J3.pin6, R18.4
  N32: R15.Pin_1, U4.pin4
  Line: U3.pin1, U3.pin3, U3.pin5, U3.pin7, U1.pin1, U1.pin3, U1.pin5, U1.pin7, U2.pin1, U2.pin3, U2.pin5, U2.pin7, U5.pin1, U5.pin3, U5.pin5, U5.pin7, U6.pin1, U6.pin3, U6.pin5, U6.pin7, U8.pin1, U8.pin3, U8.pin5, U8.pin7, U4.pin1, U4.pin3, U4.pin5, U4.pin7, U7.pin1, U7.pin3, U7.pin5, U7.pin7, J1.pin9, J3.pin9, J5.pin9, J7.pin9, R9.1, R18.1, R27.1, R36.1
  GND: U3.pin9, U3.pin11, U3.pin13, U3.pin15, U1.pin9, U1.pin11, U1.pin13, U1.pin15, U2.pin9, U2.pin11, U2.pin13, U2.pin15, U5.pin9, U5.pin11, U5.pin13, U5.pin15, U6.pin9, U6.pin11, U6.pin13, U6.pin15, U8.pin9, U8.pin11, U8.pin13, U8.pin15, J2.pin1, J4.pin1, J6.pin1, J8.pin1, U4.pin9, U4.pin11, U4.pin13, U4.pin15, U7.pin9, U7.pin11, U7.pin13, U7.pin15
  N33: U3.pin10, J4.pin2
  N34: U3.pin12, J4.pin4
  N35: U3.pin14, J4.pin6
  N36: U3.pin16, J4.pin8
  N37: U1.pin10, J2.pin2
  N38: U1.pin12, J2.pin4
  N39: U1.pin14, J2.pin6
  N40: U1.pin16, J2.pin8
  N41: U2.pin10, J2.pin3
  N42: U2.pin12, J2.pin5
  N43: U2.pin14, J2.pin7
  N44: U2.pin16, J2.pin9
  N45: U5.pin2, R25.Pin_1
  N46: U5.pin4, R23.Pin_1
  N47: U5.pin6, R21.Pin_1
  N48: U5.pin8, R19.Pin_1
  N49: U5.pin10, J6.pin2
  N50: U5.pin12, J6.pin4
  N51: U5.pin14, J6.pin6
  N52: U5.pin16, J6.pin8
  N53: U6.pin2, R26.Pin_1
  N54: U6.pin4, R24.Pin_1
  N55: U6.pin6, R22.Pin_1
  N56: U6.pin8, R20.Pin_1
  N57: U6.pin10, J6.pin3
  N58: U6.pin12, J6.pin5
  N59: U6.pin14, J6.pin7
  N60: U6.pin16, J6.pin9
  N61: R24.Pin_0, J5.pin6, R27.4
  N62: R23.Pin_0, J5.pin5, R27.5
  N63: R20.Pin_0, J5.pin2, R27.8
  N64: R22.Pin_0, J5.pin4, R27.6
  N65: R25.Pin_0, J5.pin7, R27.3
  N66: R19.Pin_0, J5.pin1, R27.9
  N67: R26.Pin_0, J5.pin8, R27.2
  N68: R21.Pin_0, J5.pin3, R27.7
  N69: U8.pin2, R35.Pin_1
  N70: U8.pin4, R33.Pin_1
  N71: U8.pin6, R31.Pin_1
  N72: U8.pin8, R29.Pin_1
  N73: U8.pin10, J8.pin3
  N74: U8.pin12, J8.pin5
  N75: U8.pin14, J8.pin7
  N76: U8.pin16, J8.pin9
  N77: R33.Pin_0, J7.pin6, R36.4
  N78: R32.Pin_0, J7.pin5, R36.5
  N79: R32.Pin_1, U7.pin4
  N80: R29.Pin_0, J7.pin2, R36.8
  N81: R31.Pin_0, J7.pin4, R36.6
  N82: R34.Pin_0, J7.pin7, R36.3
  N83: R34.Pin_1, U7.pin2
  N84: R28.Pin_0, J7.pin1, R36.9
  N85: R28.Pin_1, U7.pin8
  N86: R35.Pin_0, J7.pin8, R36.2
  N87: R30.Pin_0, J7.pin3, R36.7
  N88: R30.Pin_1, U7.pin6
  N89: J4.pin3, U4.pin10
  N90: J4.pin5, U4.pin12
  N91: J4.pin7, U4.pin14
  N92: J4.pin9, U4.pin16
  N93: J8.pin2, U7.pin10
  N94: J8.pin4, U7.pin12
  N95: J8.pin6, U7.pin14
  N96: J8.pin8, U7.pin16

notes:
  Block Detector for 6 Dioder & Optokobler   OMJK1949

custom parts:
  TLP620-4: Quad Photo-transistor optically coupled to two infrared emitting diodes connected in inverse parallel.
