# Fritzing sketch I2C_ IO_Interface (saved by Fritzing 0.9.6b)
circuit board: 11.17cm x 3cm

parts:
  IO1 = PCF8574N [package="DIP16 [THT]"]
  IO2 = PCF8574N [package="DIP16 [THT]"]
  IO4 = PCF8574N [package="DIP16 [THT]"]
  IO3 = PCF8574N [package="DIP16 [THT]"]
  R5 = Resistor [tolerance=±5% power=0.25 resistance=10k package=THT]
  R6 = Resistor [tolerance=±10% power=0.25 resistance=10k package=THT]
  R7 = Resistor [tolerance=±5% power=0.25 resistance=10k package=THT]
  Pad1 = Pad [width=2.54 height=2.54 connect=center]
  Pad2 = Pad [width=2.54 height=2.54 connect=center]
  J14 = male pin header, 4 pins [form="♂ (male)"]
  J13 = male pin header, 4 pins [form="♂ (male)"]
  R1 = 8 Resistor Network [part_number="SIL 8x10k" package="SIP (Single Inline)"]
  R2 = 8 Resistor Network [part_number="SIL 8x10k" package="SIP (Single Inline)"]
  R3 = 8 Resistor Network [part_number="SIL 8x10k" package="SIP (Single Inline)"]
  R4 = 8 Resistor Network [part_number="SIL 8x10k" package="SIP (Single Inline)"]
  J4 = screw terminal, 9 pins [part_number=KF128-9]
  J3 = screw terminal, 9 pins [part_number=KF128-9]
  J2 = screw terminal, 9 pins [part_number=KF128-9]
  J1 = screw terminal, 9 pins [part_number=KF128-9]

nets:
  GND: IO1.A0, IO1.A1, IO1.GND, IO2.A1, IO2.GND, IO4.GND, IO3.A0, IO3.GND, Pad1.pad, J14.pin4, J13.pin4, J4.pin1, J3.pin1, J2.pin1, J1.pin1
  A2: IO1.A2, IO2.A2, IO4.A2, IO3.A2, R7.Pin_1, Pad2.pad
  N1: IO1.P0, R1.9, J1.pin9
  N2: IO1.P1, R1.8, J1.pin8
  N3: IO1.P2, R1.7, J1.pin7
  N4: IO1.P3, R1.6, J1.pin6
  N5: IO1.P4, R1.5, J1.pin5
  N6: IO1.P5, R1.4, J1.pin4
  N7: IO1.P6, R1.3, J1.pin3
  N8: IO1.P7, R1.2, J1.pin2
  SCL: IO1.SCL, IO2.SCL, IO4.SCL, IO3.SCL, R6.Pin_1, J14.pin2, J13.pin2
  SDA: IO1.SDA, IO2.SDA, IO4.SDA, IO3.SDA, R5.Pin_1, J14.pin1, J13.pin1
  3.3V: IO1.VCC, IO2.A0, IO2.VCC, IO4.A0, IO4.A1, IO4.VCC, IO3.A1, IO3.VCC, R5.Pin_0, R6.Pin_0, R7.Pin_0, J14.pin3, J13.pin3, R1.1, R2.1, R3.1, R4.1
  N9: IO2.P0, R2.9, J2.pin9
  N10: IO2.P1, R2.8, J2.pin8
  N11: IO2.P2, R2.7, J2.pin7
  N12: IO2.P3, R2.6, J2.pin6
  N13: IO2.P4, R2.5, J2.pin5
  N14: IO2.P5, R2.4, J2.pin4
  N15: IO2.P6, R2.3, J2.pin3
  N16: IO2.P7, R2.2, J2.pin2
  N17: IO4.P0, R4.9, J4.pin9
  N18: IO4.P1, R4.8, J4.pin8
  N19: IO4.P2, R4.7, J4.pin7
  N20: IO4.P3, R4.6, J4.pin6
  N21: IO4.P4, R4.5, J4.pin5
  N22: IO4.P5, R4.4, J4.pin4
  N23: IO4.P6, R4.3, J4.pin3
  N24: IO4.P7, R4.2, J4.pin2
  N25: IO3.P0, R3.9, J3.pin9
  N26: IO3.P1, R3.8, J3.pin8
  N27: IO3.P2, R3.7, J3.pin7
  N28: IO3.P3, R3.6, J3.pin6
  N29: IO3.P4, R3.5, J3.pin5
  N30: IO3.P5, R3.4, J3.pin4
  N31: IO3.P6, R3.3, J3.pin3
  N32: IO3.P7, R3.2, J3.pin2

notes:
  SDA
  3V3
  SCL
  GND
  I2C I/O Interface  OMJK1949
  sekt1953@gmail.com

custom parts:
  PCF8574N: Remote 8-Bit I/O Expander for I 2C Bus
