# Fritzing sketch ESP32_30Pin_I2C_Board_a (saved by Fritzing 0.9.6b)
stripboards: 1

parts:
  M1 = DOIT Esp32 DevKit v1 (30 pins long, 11 pins width) [part_number=ESP32S-PIN30]
  J1 = male pin header, 6 pins [form="♂ (male)"]
  J3 = female pin header, 15 pins [form="♀ (female)"]
  J4 = male pin header, 2 pins [form="♂ (male)"]
  J2 = female pin header, 15 pins [form="♀ (female)"]
  M2 = RioRand LM2596  # not connected

nets:
  N1: M1.3V3, J1.pin2, J2.pin1
  N2: M1.GND, J1.pin6, J3.pin14, J4.pin1, J2.pin2
  N3: M1.D15, J2.pin3
  N4: M1.D2, J2.pin4
  N5: M1.D4, J2.pin5
  N6: M1.RX2, J2.pin6
  N7: M1.TX2, J2.pin7
  N8: M1.D5, J2.pin8
  N9: M1.D18, J2.pin9
  N10: M1.D19, J2.pin10
  N11: M1.D21, J1.pin3, J2.pin11
  N12: M1.RX0, J2.pin12
  N13: M1.TX0, J2.pin13
  N14: M1.D22, J1.pin4, J2.pin14
  N15: M1.D23, J2.pin15
  N16: M1.EN, J3.pin1
  N17: M1.VP, J3.pin2
  N18: M1.VN, J3.pin3
  N19: M1.D34, J3.pin4
  N20: M1.D35, J3.pin5
  N21: M1.D32, J3.pin6
  N22: M1.D33, J3.pin7
  N23: M1.D25, J3.pin8
  N24: M1.D26, J3.pin9
  N25: M1.D27, J3.pin10
  N26: M1.D14, J3.pin11
  N27: M1.D12, J3.pin12
  N28: M1.D13, J3.pin13
  N29: M1.VIN, J1.pin1, J3.pin15, J4.pin2

notes:
  GND
  +5V
  +3V3
  SDA
  SCL
  +12V
  Keypin
  +5Vin
  +5Vout
  +3V3out
  I2C_SDA
  I2C_SCL
  Key
  Green
  Yellow
  White
  Red
  Black

custom parts:
  DOIT Esp32 DevKit v1 (30 pins long, 11 pins width): The DOIT Esp32 DevKit v1 is one of the development board created by DOIT to evaluate the ESP-WROOM-32 module. It is based on the ESP32 microcontroller that boasts Wifi, Bluetooth, Ethernet and Low Power support all in a single chip. (vanepp) made breadboard work, adjusted pin numbering and labels and reduced size of schematic and cleaned up pcb. This chip is 30pins long (2 x15) and 11 pins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
