# Fritzing sketch ESP32_ESP32S_30Pin_Expansion_Board (saved by Fritzing 0.9.6b)
stripboards: 1

parts:
  M1 = DOIT Esp32 DevKit v1 (30 pins long, 11 pins width) [part_number=ESP32S-PIN30]
  J1 = male pin header, 5 pins [form="♂ (male)"]

nets:
  3V3 Output: M1.3V3, J1.pin4
  GND: M1.GND, J1.pin3
  SDA: M1.D21, J1.pin2
  SCL: M1.D22, J1.pin1
  5V Input: M1.VIN, J1.pin5

custom parts:
  DOIT Esp32 DevKit v1 (30 pins long, 11 pins width): The DOIT Esp32 DevKit v1 is one of the development board created by DOIT to evaluate the ESP-WROOM-32 module. It is based on the ESP32 microcontroller that boasts Wifi, Bluetooth, Ethernet and Low Power support all in a single chip. (vanepp) made breadboard work, adjusted pin numbering and labels and reduced size of schematic and cleaned up pcb. This chip is 30pins long (2 x15) and 11 pins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
