# Fritzing sketch mcp23017_100 (saved by Fritzing 0.9.6b)
circuit board: 18cm x 7.8cm
breadboards: 1

parts:
  Drv1 = Motor Driver 1A Dual TB6612FNG [part_number=TB6612FNG]
  U1 = Sharp PC817 [package=THT]
  U2 = Sharp PC817 [package=THT]
  U3 = Sharp PC817 [package=THT]
  U4 = Sharp PC817 [package=THT]
  R1 = Resistor [tolerance=±5% power=0.25 resistance=560 package=THT]
  R2 = Resistor [tolerance=±5% power=0.25 resistance=560 package=THT]
  R3 = Resistor [tolerance=±5% power=0.25 resistance=560 package=THT]
  R4 = Resistor [tolerance=±5% power=0.25 resistance=560 package=THT]
  IC1 = DIP - 28 pins [chip_label=MCP23017 package="DIP (Dual Inline) [THT]"]
  J1 = screw terminal, 5 pins
  J2 = screw terminal, 5 pins
  Drv3 = Motor Driver 1A Dual TB6612FNG [part_number=TB6612FNG]
  U11 = Sharp PC817 [package=THT]
  U12 = Sharp PC817 [package=THT]
  U9 = Sharp PC817 [package=THT]
  U10 = Sharp PC817 [package=THT]
  R5 = Resistor [tolerance=±5% power=0.25 resistance=560 package=THT]
  R6 = Resistor [tolerance=±5% power=0.25 resistance=560 package=THT]
  R7 = Resistor [tolerance=±5% power=0.25 resistance=560 package=THT]
  R8 = Resistor [tolerance=±5% power=0.25 resistance=560 package=THT]
  IC2 = DIP - 28 pins [chip_label=MCP23017 package="DIP (Dual Inline) [THT]"]
  J3 = screw terminal, 5 pins
  J4 = screw terminal, 5 pins
  C1 = Ceramic Capacitor [capacitance=100nF voltage=35V package="100 mil [THT, multilayer]"]
  C2 = Ceramic Capacitor [capacitance=100nF voltage=35V package="100 mil [THT, multilayer]"]
  Drv2 = Motor Driver 1A Dual TB6612FNG [part_number=TB6612FNG]
  U5 = Sharp PC817 [package=THT]
  U8 = Sharp PC817 [package=THT]
  U6 = Sharp PC817 [package=THT]
  U7 = Sharp PC817 [package=THT]
  R9 = Resistor [tolerance=±5% power=0.25 resistance=560 package=THT]
  R10 = Resistor [tolerance=±5% power=0.25 resistance=560 package=THT]
  R11 = Resistor [tolerance=±5% power=0.25 resistance=560 package=THT]
  R12 = Resistor [tolerance=±5% power=0.25 resistance=560 package=THT]
  J5 = screw terminal, 5 pins
  J6 = screw terminal, 5 pins
  Dev4 = Motor Driver 1A Dual TB6612FNG [part_number=TB6612FNG]
  U15 = Sharp PC817 [package=THT]
  U13 = Sharp PC817 [package=THT]
  U14 = Sharp PC817 [package=THT]
  U16 = Sharp PC817 [package=THT]
  R13 = Resistor [tolerance=±5% power=0.25 resistance=560 package=THT]
  R14 = Resistor [tolerance=±5% power=0.25 resistance=560 package=THT]
  R15 = Resistor [tolerance=±5% power=0.25 resistance=560 package=THT]
  R16 = Resistor [tolerance=±5% power=0.25 resistance=560 package=THT]
  J7 = screw terminal, 5 pins
  J8 = screw terminal, 5 pins
  Drv4 = Motor Driver 1A Dual TB6612FNG [part_number=TB6612FNG]
  Drv5 = Motor Driver 1A Dual TB6612FNG [part_number=TB6612FNG]
  Dev5 = Motor Driver 1A Dual TB6612FNG [part_number=TB6612FNG]
  Drv6 = Motor Driver 1A Dual TB6612FNG [part_number=TB6612FNG]
  U17 = Sharp PC817 [package=THT]
  U18 = Sharp PC817 [package=THT]
  U19 = Sharp PC817 [package=THT]
  U20 = Sharp PC817 [package=THT]
  U21 = Sharp PC817 [package=THT]
  U22 = Sharp PC817 [package=THT]
  U23 = Sharp PC817 [package=THT]
  U24 = Sharp PC817 [package=THT]
  U25 = Sharp PC817 [package=THT]
  U26 = Sharp PC817 [package=THT]
  U27 = Sharp PC817 [package=THT]
  U28 = Sharp PC817 [package=THT]
  U29 = Sharp PC817 [package=THT]
  U30 = Sharp PC817 [package=THT]
  U31 = Sharp PC817 [package=THT]
  U32 = Sharp PC817 [package=THT]
  R17 = Resistor [tolerance=±5% power=0.25 resistance=560 package=THT]
  R18 = Resistor [tolerance=±5% power=0.25 resistance=560 package=THT]
  R19 = Resistor [tolerance=±5% power=0.25 resistance=560 package=THT]
  R20 = Resistor [tolerance=±5% power=0.25 resistance=560 package=THT]
  R21 = Resistor [tolerance=±5% power=0.25 resistance=560 package=THT]
  R22 = Resistor [tolerance=±5% power=0.25 resistance=560 package=THT]
  R23 = Resistor [tolerance=±5% power=0.25 resistance=560 package=THT]
  R24 = Resistor [tolerance=±5% power=0.25 resistance=560 package=THT]
  R25 = Resistor [tolerance=±5% power=0.25 resistance=560 package=THT]
  R26 = Resistor [tolerance=±5% power=0.25 resistance=560 package=THT]
  R27 = Resistor [tolerance=±5% power=0.25 resistance=560 package=THT]
  R28 = Resistor [tolerance=±5% power=0.25 resistance=560 package=THT]
  R29 = Resistor [tolerance=±5% power=0.25 resistance=560 package=THT]
  R30 = Resistor [tolerance=±5% power=0.25 resistance=560 package=THT]
  R31 = Resistor [tolerance=±5% power=0.25 resistance=560 package=THT]
  R32 = Resistor [tolerance=±5% power=0.25 resistance=560 package=THT]
  IC4 = DIP - 28 pins [chip_label=MCP23017 package="DIP (Dual Inline) [THT]"]
  IC3 = DIP - 28 pins [chip_label=MCP23017 package="DIP (Dual Inline) [THT]"]
  J9 = screw terminal, 5 pins
  J10 = screw terminal, 5 pins
  J11 = screw terminal, 5 pins
  J12 = screw terminal, 5 pins
  J13 = screw terminal, 5 pins
  J14 = screw terminal, 5 pins
  J15 = screw terminal, 5 pins
  J16 = screw terminal, 5 pins
  C3 = Ceramic Capacitor [capacitance=100nF voltage=35V package="100 mil [THT, multilayer]"]
  C4 = Ceramic Capacitor [capacitance=100nF voltage=35V package="100 mil [THT, multilayer]"]
  J17 = female pin header, 20 pins [form="♀ (female)"]  # not connected
  J18 = male pin header, 7 pins [form="♂ (male)"]
  J20 = male pin header, 7 pins [form="♂ (male)"]

nets:
  GND: Drv1.GND, U1.Pin_2, U1.Pin_3, U2.Pin_2, U2.Pin_3, U3.Pin_2, U3.Pin_3, U4.Pin_2, U4.Pin_3, IC1.pin10, IC1.pin15, IC1.pin16, IC1.pin17, Drv3.GND, U11.Pin_2, U11.Pin_3, U12.Pin_2, U12.Pin_3, U9.Pin_2, U9.Pin_3, U10.Pin_2, U10.Pin_3, IC2.pin10, IC2.pin16, IC2.pin17, C1.1, C2.1, Drv2.GND, U5.Pin_2, U5.Pin_3, U8.Pin_2, U8.Pin_3, U6.Pin_2, U6.Pin_3, U7.Pin_2, U7.Pin_3, Dev4.GND, U15.Pin_2, U15.Pin_3, U13.Pin_2, U13.Pin_3, U14.Pin_2, U14.Pin_3, U16.Pin_2, U16.Pin_3, Drv4.GND, Drv5.GND, Dev5.GND, Drv6.GND, U17.Pin_2, U17.Pin_3, U18.Pin_2, U18.Pin_3, U19.Pin_2, U19.Pin_3, U20.Pin_2, U20.Pin_3, U21.Pin_2, U21.Pin_3, U22.Pin_2, U22.Pin_3, U23.Pin_2, U23.Pin_3, U24.Pin_2, U24.Pin_3, U25.Pin_2, U25.Pin_3, U26.Pin_2, U26.Pin_3, U27.Pin_2, U27.Pin_3, U28.Pin_2, U28.Pin_3, U29.Pin_2, U29.Pin_3, U30.Pin_2, U30.Pin_3, U31.Pin_2, U31.Pin_3, U32.Pin_2, U32.Pin_3, IC4.pin10, IC4.pin17, IC3.pin10, IC3.pin15, IC3.pin17, C3.1, C4.1, J18.pin7, J20.pin7
  N1: Drv1.B01, J1.pin4
  N2: Drv1.B02, J1.pin5
  N3: Drv1.A02, J2.pin1
  N4: Drv1.A01, J2.pin2
  VCC: Drv1.VCC, Drv1.PWMA, Drv1.STBY, Drv1.PWMB, IC1.pin9, IC1.pin18, Drv3.VCC, Drv3.PWMA, Drv3.STBY, Drv3.PWMB, IC2.pin9, IC2.pin15, IC2.pin18, C1.0, C2.0, Drv2.VCC, Drv2.PWMA, Drv2.STBY, Drv2.PWMB, Dev4.VCC, Dev4.PWMA, Dev4.STBY, Dev4.PWMB, Drv4.VCC, Drv4.PWMA, Drv4.STBY, Drv4.PWMB, Drv5.VCC, Drv5.PWMA, Drv5.STBY, Drv5.PWMB, Dev5.VCC, Dev5.PWMA, Dev5.STBY, Dev5.PWMB, Drv6.VCC, Drv6.PWMA, Drv6.STBY, Drv6.PWMB, IC4.pin9, IC4.pin15, IC4.pin16, IC4.pin18, IC3.pin9, IC3.pin16, IC3.pin18, C3.0, C4.0, J18.pin3, J20.pin3
  VM: Drv1.VM, J1.pin2, J2.pin4, Drv3.VM, J3.pin2, J4.pin4, Drv2.VM, J5.pin4, J6.pin2, Dev4.VM, J7.pin2, J8.pin4, Drv4.VM, Drv5.VM, Dev5.VM, Drv6.VM, J9.pin2, J10.pin2, J11.pin4, J12.pin2, J13.pin4, J14.pin4, J15.pin4, J16.pin2, J18.pin1, J20.pin1
  N5: Drv1.AIN2, IC1.pin25
  N6: Drv1.AIN1, IC1.pin26
  N7: Drv1.BIN1, IC1.pin27
  N8: Drv1.BIN2, IC1.pin28
  N9: U1.Pin_1, R1.Pin_1
  N10: U1.Pin_4, IC1.pin24
  N11: U2.Pin_1, R2.Pin_1
  N12: U2.Pin_4, IC1.pin23
  N13: U3.Pin_1, R3.Pin_1
  N14: U3.Pin_4, IC1.pin22
  N15: U4.Pin_1, R4.Pin_1
  N16: U4.Pin_4, IC1.pin21
  N17: R1.Pin_0, J1.pin1
  N18: R2.Pin_0, J1.pin3
  N19: R3.Pin_0, J2.pin3
  N20: R4.Pin_0, J2.pin5
  N21: IC1.GPB0, U5.Pin_4
  N22: IC1.GPB1, U6.Pin_4
  N23: IC1.GPB2, U7.Pin_4
  N24: IC1.pin4, U8.Pin_4
  N25: IC1.pin5, Drv2.AIN2
  N26: IC1.pin6, Drv2.AIN1
  N27: IC1.pin7, Drv2.BIN1
  N28: IC1.pin8, Drv2.BIN2
  SCL: IC1.pin12, IC2.pin12, IC4.pin12, IC3.pin12, J18.pin5, J20.pin5
  SDA: IC1.pin13, IC2.pin13, IC4.pin13, IC3.pin13, J18.pin4, J20.pin4
  N29: Drv3.B01, J3.pin4
  N30: Drv3.B02, J3.pin5
  N31: Drv3.A02, J4.pin1
  N32: Drv3.A01, J4.pin2
  N33: Drv3.AIN2, IC2.pin25
  N34: Drv3.AIN1, IC2.pin26
  N35: Drv3.BIN1, IC2.pin27
  N36: Drv3.BIN2, IC2.pin28
  N37: U11.Pin_1, R7.Pin_1
  N38: U11.Pin_4, IC2.pin22
  N39: U12.Pin_1, R5.Pin_1
  N40: U12.Pin_4, IC2.pin21
  N41: U9.Pin_1, R6.Pin_1
  N42: U9.Pin_4, IC2.pin24
  N43: U10.Pin_1, R8.Pin_1
  N44: U10.Pin_4, IC2.pin23
  N45: R5.Pin_0, J4.pin5
  N46: R6.Pin_0, J3.pin1
  N47: R7.Pin_0, J4.pin3
  N48: R8.Pin_0, J3.pin3
  N49: IC2.GPB0, U13.Pin_4
  N50: IC2.GPB1, U14.Pin_4
  N51: IC2.GPB2, U15.Pin_4
  N52: IC2.pin4, U16.Pin_4
  N53: IC2.pin5, Dev4.AIN2
  N54: IC2.pin6, Dev4.AIN1
  N55: IC2.pin7, Dev4.BIN1
  N56: IC2.pin8, Dev4.BIN2
  N57: Drv2.B01, J6.pin4
  N58: Drv2.B02, J6.pin5
  N59: Drv2.A02, J5.pin1
  N60: Drv2.A01, J5.pin2
  N61: U5.Pin_1, R12.Pin_1
  N62: U8.Pin_1, R10.Pin_1
  N63: U6.Pin_1, R11.Pin_1
  N64: U7.Pin_1, R9.Pin_1
  N65: R9.Pin_0, J6.pin3
  N66: R10.Pin_0, J6.pin1
  N67: R11.Pin_0, J5.pin3
  N68: R12.Pin_0, J5.pin5
  N69: Dev4.B01, J7.pin4
  N70: Dev4.B02, J7.pin5
  N71: Dev4.A02, J8.pin1
  N72: Dev4.A01, J8.pin2
  N73: U15.Pin_1, R13.Pin_1
  N74: U13.Pin_1, R16.Pin_1
  N75: U14.Pin_1, R14.Pin_1
  N76: U16.Pin_1, R15.Pin_1
  N77: R13.Pin_0, J7.pin3
  N78: R14.Pin_0, J8.pin3
  N79: R15.Pin_0, J7.pin1
  N80: R16.Pin_0, J8.pin5
  N81: Drv4.B01, J9.pin4
  N82: Drv4.B02, J9.pin5
  N83: Drv4.A02, J11.pin1
  N84: Drv4.A01, J11.pin2
  N85: Drv4.AIN2, IC3.pin25
  N86: Drv4.AIN1, IC3.pin26
  N87: Drv4.BIN1, IC3.pin27
  N88: Drv4.BIN2, IC3.pin28
  N89: Drv5.B01, J12.pin4
  N90: Drv5.B02, J12.pin5
  N91: Drv5.A02, J15.pin1
  N92: Drv5.A01, J15.pin2
  N93: Drv5.AIN2, IC3.pin5
  N94: Drv5.AIN1, IC3.pin6
  N95: Drv5.BIN1, IC3.pin7
  N96: Drv5.BIN2, IC3.pin8
  N97: Dev5.B01, J16.pin4
  N98: Dev5.B02, J16.pin5
  N99: Dev5.A02, J14.pin1
  N100: Dev5.A01, J14.pin2
  N101: Dev5.AIN2, IC4.pin5
  N102: Dev5.AIN1, IC4.pin6
  N103: Dev5.BIN1, IC4.pin7
  N104: Dev5.BIN2, IC4.pin8
  N105: Drv6.B01, J10.pin4
  N106: Drv6.B02, J10.pin5
  N107: Drv6.A02, J13.pin1
  N108: Drv6.A01, J13.pin2
  N109: Drv6.AIN2, IC4.pin25
  N110: Drv6.AIN1, IC4.pin26
  N111: Drv6.BIN1, IC4.pin27
  N112: Drv6.BIN2, IC4.pin28
  N113: U17.Pin_1, R28.Pin_1
  N114: U17.Pin_4, IC3.pin24
  N115: U18.Pin_1, R19.Pin_1
  N116: U18.Pin_4, IC4.pin24
  N117: U19.Pin_1, R21.Pin_1
  N118: U19.Pin_4, IC3.GPB2
  N119: U20.Pin_1, R29.Pin_1
  N120: U20.Pin_4, IC4.GPB0
  N121: U21.Pin_1, R25.Pin_1
  N122: U21.Pin_4, IC3.pin4
  N123: U22.Pin_1, R23.Pin_1
  N124: U22.Pin_4, IC4.pin21
  N125: U23.Pin_1, R32.Pin_1
  N126: U23.Pin_4, IC4.pin4
  N127: U24.Pin_1, R20.Pin_1
  N128: U24.Pin_4, IC4.pin22
  N129: U25.Pin_1, R26.Pin_1
  N130: U25.Pin_4, IC4.GPB2
  N131: U26.Pin_1, R31.Pin_1
  N132: U26.Pin_4, IC3.GPB0
  N133: U27.Pin_1, R24.Pin_1
  N134: U27.Pin_4, IC4.pin23
  N135: U28.Pin_1, R22.Pin_1
  N136: U28.Pin_4, IC3.pin22
  N137: U29.Pin_1, R18.Pin_1
  N138: U29.Pin_4, IC3.pin21
  N139: U30.Pin_1, R17.Pin_1
  N140: U30.Pin_4, IC3.pin23
  N141: U31.Pin_1, R30.Pin_1
  N142: U31.Pin_4, IC4.GPB1
  N143: U32.Pin_1, R27.Pin_1
  N144: U32.Pin_4, IC3.GPB1
  N145: R17.Pin_0, J9.pin3
  N146: R18.Pin_0, J11.pin5
  N147: R19.Pin_0, J10.pin1
  N148: R20.Pin_0, J13.pin3
  N149: R21.Pin_0, J12.pin3
  N150: R22.Pin_0, J11.pin3
  N151: R23.Pin_0, J13.pin5
  N152: R24.Pin_0, J10.pin3
  N153: R25.Pin_0, J12.pin1
  N154: R26.Pin_0, J16.pin3
  N155: R27.Pin_0, J15.pin3
  N156: R28.Pin_0, J9.pin1
  N157: R29.Pin_0, J14.pin5
  N158: R30.Pin_0, J14.pin3
  N159: R31.Pin_0, J15.pin5
  N160: R32.Pin_0, J16.pin1
  N161: J18.pin2, J20.pin2

custom parts:
  DIP - 28 pins: A DIP stand-in part for whatever IC you want. With 28 pins on a 300mil dual inline package (DIP) footprint.
