# Fritzing sketch mcp23017_300 (saved by Fritzing 0.9.6b)
circuit board: 10.9cm x 4cm
breadboards: 1

parts:
  IC1 = MCP20017 [part_number=MCP23017 package="DIP (Dual Inline) [THT]"]
  IC2 = MCP20017 [part_number=MCP23017 package="DIP (Dual Inline) [THT]"]
  J1 = screw terminal, 9 pins
  J2 = screw terminal, 9 pins
  J3 = screw terminal, 9 pins
  J4 = screw terminal, 9 pins
  J5 = rounded female pin header, 3 pins [form="♀ (female rounded)"]
  J6 = rounded female pin header, 3 pins [form="♀ (female rounded)"]
  J7 = male pin header, 6 pins [form="♂ (male)"]
  J8 = screw terminal, 9 pins
  J9 = screw terminal, 9 pins
  J10 = screw terminal, 9 pins
  J11 = screw terminal, 9 pins
  J12 = male pin header, 6 pins [form="♂ (male)"]
  C2 = Ceramic Capacitor [capacitance=100nF voltage=35V package="100 mil [THT, multilayer]"]
  C1 = Ceramic Capacitor [capacitance=100nF voltage=35V package="100 mil [THT, multilayer]"]
  R1 = Resistor [tolerance=±5% power=0.25 resistance=10k package=THT]
  R2 = Resistor [tolerance=±5% power=0.25 resistance=10k package=THT]

nets:
  N1: IC1.GPB0, J2.pin9, J9.pin9
  N2: IC1.GPB1, J2.pin8, J9.pin8
  N3: IC1.GPB2, J2.pin7, J9.pin7
  N4: IC1.GPB3, J2.pin6, J9.pin6
  N5: IC1.GPB04, J2.pin5, J9.pin5
  N6: IC1.GPB5, J2.pin4, J9.pin4
  N7: IC1.GPB6, J2.pin3, J9.pin3
  N8: IC1.GPB8, J2.pin2, J9.pin2
  3V3: IC1.VDD, IC1.RESET, IC2.VDD, IC2.A0, IC2.RESET, J5.pin1, J6.pin1, J7.pin2, J12.pin2, C2.0, C1.0, R1.Pin_0, R2.Pin_0
  GND: IC1.GND, IC1.A0, IC2.GND, J1.pin1, J2.pin1, J3.pin1, J4.pin1, J5.pin3, J6.pin3, J7.pin6, J8.pin1, J9.pin1, J10.pin1, J11.pin1, J12.pin6, C2.1, C1.1
  SCL: IC1.SCL, IC2.SCL, J7.pin4, J12.pin4, R2.Pin_1
  SDA: IC1.SDA, IC2.SDA, J7.pin3, J12.pin3, R1.Pin_1
  A1.: IC1.A1, IC2.A1, J6.pin2
  A2.: IC1.A2, IC2.A2, J5.pin2
  N9: IC1.GPA0, J1.pin9, J8.pin9
  N10: IC1.GPA1, J1.pin8, J8.pin8
  N11: IC1.GPA2, J1.pin7, J8.pin7
  N12: IC1.GPA3, J1.pin6, J8.pin6
  N13: IC1.GPA4, J1.pin5, J8.pin5
  N14: IC1.GPA5, J1.pin4, J8.pin4
  N15: IC1.GPA6, J1.pin3, J8.pin3
  N16: IC1.GPA7, J1.pin2, J8.pin2
  N17: IC2.GPB0, J4.pin9, J11.pin9
  N18: IC2.GPB1, J4.pin8, J11.pin8
  N19: IC2.GPB2, J4.pin7, J11.pin7
  N20: IC2.GPB3, J4.pin6, J11.pin6
  N21: IC2.GPB04, J4.pin5, J11.pin5
  N22: IC2.GPB5, J4.pin4, J11.pin4
  N23: IC2.GPB6, J4.pin3, J11.pin3
  N24: IC2.GPB8, J4.pin2, J11.pin2
  N25: IC2.GPA0, J3.pin9, J10.pin9
  N26: IC2.GPA1, J3.pin8, J10.pin8
  N27: IC2.GPA2, J3.pin7, J10.pin7
  N28: IC2.GPA3, J3.pin6, J10.pin6
  N29: IC2.GPA4, J3.pin5, J10.pin5
  N30: IC2.GPA5, J3.pin4, J10.pin4
  N31: IC2.GPA6, J3.pin3, J10.pin3
  N32: IC2.GPA7, J3.pin2, J10.pin2
  Ext.: J7.pin1, J12.pin1

notes:
  A2
  A1
  00
  01
  02
  03
  04
  05
  06
  07
  GND
  10
  09
  14
  11
  13
  15
  12
  08
  3V3
  SDA
  SCL
  Key
  Ext.
  sekt1953@gmail.com

custom parts:
  MCP20017: MCP23017, 28 pins on a 300mil dual inline package (DIP) footprint. 16-Bit I/O Expander with I2C Serial Interface
