# Fritzing sketch mcp23017_Proto_001a (saved by Fritzing 0.9.6b)
stripboards: 1

parts:
  J1 = screw terminal, 9 pins
  J2 = screw terminal, 9 pins
  J3 = screw terminal, 9 pins
  J4 = screw terminal, 9 pins
  R1 = Resistor [tolerance=±5% power=0.25 resistance=10k package=THT]
  R2 = Resistor [tolerance=±5% power=0.25 resistance=10k package=THT]
  IC1 = MCP20017 [part_number=MCP23017 package="DIP (Dual Inline) [THT]"]
  IC2 = MCP20017 [part_number=MCP23017 package="DIP (Dual Inline) [THT]"]
  J5 = male pin header, 5 pins [form="♂ (male)"]
  J6 = male pin header, 5 pins [form="♂ (male)"]
  C1 = Ceramic Capacitor [capacitance=100nF voltage=35V package="100 mil [THT, multilayer]"]
  C2 = Ceramic Capacitor [capacitance=100nF voltage=35V package="100 mil [THT, multilayer]"]

nets:
  GND/Key: J1.pin1, J2.pin1, J3.pin9, J4.pin9, IC1.GND, IC1.A0, IC1.A1, IC1.A2, IC2.GND, IC2.A1, IC2.A2, J5.pin1, J5.pin2, J6.pin1, J6.pin2, C1.1, C2.1
  N1: J1.pin2, IC2.GPB0
  N2: J1.pin3, IC2.GPB1
  N3: J1.pin4, IC2.GPB2
  N4: J1.pin5, IC2.GPB3
  N5: J1.pin6, IC2.GPB04
  N6: J1.pin7, IC2.GPB5
  N7: J1.pin8, IC2.GPB6
  N8: J1.pin9, IC2.GPB8
  N9: J2.pin2, IC1.GPB0
  N10: J2.pin3, IC1.GPB1
  N11: J2.pin4, IC1.GPB2
  N12: J2.pin5, IC1.GPB3
  N13: J2.pin6, IC1.GPB04
  N14: J2.pin7, IC1.GPB5
  N15: J2.pin8, IC1.GPB6
  N16: J2.pin9, IC1.GPB8
  N17: J3.pin1, IC1.GPA0
  N18: J3.pin2, IC1.GPA1
  N19: J3.pin3, IC1.GPA2
  N20: J3.pin4, IC1.GPA3
  N21: J3.pin5, IC1.GPA4
  N22: J3.pin6, IC1.GPA5
  N23: J3.pin7, IC1.GPA6
  N24: J3.pin8, IC1.GPA7
  N25: J4.pin1, IC2.GPA0
  N26: J4.pin2, IC2.GPA1
  N27: J4.pin3, IC2.GPA2
  N28: J4.pin4, IC2.GPA3
  N29: J4.pin5, IC2.GPA4
  N30: J4.pin6, IC2.GPA5
  N31: J4.pin7, IC2.GPA6
  N32: J4.pin8, IC2.GPA7
  3.3V/VCC: R1.Pin_0, R2.Pin_0, IC1.VDD, IC1.RESET, IC2.VDD, IC2.A0, IC2.RESET, J5.pin5, J6.pin5, C1.0, C2.0
  SDA: R1.Pin_1, IC1.SDA, IC2.SDA, J5.pin4, J6.pin4
  SCL: R2.Pin_1, IC1.SCL, IC2.SCL, J5.pin3, J6.pin3

notes:
  GND
  Key
  SCL
  SDA
  3V3
  GPA7
  GPA6
  GPA5
  GPA4
  GPA3
  GPA2
  GPA1
  GPA0
  GPB7
  GPB1
  GPB0
  GPB2
  GPB5
  GPB4
  GPB3
  GPB6
  ADDR x00
  ADDR x01

custom parts:
  MCP20017: MCP23017, 28 pins on a 300mil dual inline package (DIP) footprint. 16-Bit I/O Expander with I2C Serial Interface
