# Fritzing sketch mcp23017_Proto_001b (saved by Fritzing 0.9.6b)
stripboards: 1

parts:
  J1 = screw terminal, 9 pins
  J2 = screw terminal, 9 pins
  J3 = screw terminal, 9 pins
  J4 = screw terminal, 9 pins
  R1 = Resistor [tolerance=±5% power=0.25 resistance=10k package=THT]
  R2 = Resistor [tolerance=±5% power=0.25 resistance=10k package=THT]
  IC3 = MCP20017 [part_number=MCP23017 package="DIP (Dual Inline) [THT]"]
  IC4 = MCP20017 [part_number=MCP23017 package="DIP (Dual Inline) [THT]"]
  J5 = male pin header, 5 pins [form="♂ (male)"]
  J6 = male pin header, 5 pins [form="♂ (male)"]
  C1 = Ceramic Capacitor [capacitance=100nF voltage=35V package="100 mil [THT, multilayer]"]
  C2 = Ceramic Capacitor [capacitance=100nF voltage=35V package="100 mil [THT, multilayer]"]

nets:
  GND/Key: J1.pin1, J2.pin1, J3.pin9, J4.pin9, IC3.GND, IC3.A0, IC3.A2, IC4.GND, IC4.A2, J5.pin1, J5.pin2, J6.pin1, J6.pin2, C1.1, C2.1
  N1: J1.pin2, IC4.GPB0
  N2: J1.pin3, IC4.GPB1
  N3: J1.pin4, IC4.GPB2
  N4: J1.pin5, IC4.GPB3
  N5: J1.pin6, IC4.GPB04
  N6: J1.pin7, IC4.GPB5
  N7: J1.pin8, IC4.GPB6
  N8: J1.pin9, IC4.GPB8
  N9: J2.pin2, IC3.GPB0
  N10: J2.pin3, IC3.GPB1
  N11: J2.pin4, IC3.GPB2
  N12: J2.pin5, IC3.GPB3
  N13: J2.pin6, IC3.GPB04
  N14: J2.pin7, IC3.GPB5
  N15: J2.pin8, IC3.GPB6
  N16: J2.pin9, IC3.GPB8
  N17: J3.pin1, IC3.GPA0
  N18: J3.pin2, IC3.GPA1
  N19: J3.pin3, IC3.GPA2
  N20: J3.pin4, IC3.GPA3
  N21: J3.pin5, IC3.GPA4
  N22: J3.pin6, IC3.GPA5
  N23: J3.pin7, IC3.GPA6
  N24: J3.pin8, IC3.GPA7
  N25: J4.pin1, IC4.GPA0
  N26: J4.pin2, IC4.GPA1
  N27: J4.pin3, IC4.GPA2
  N28: J4.pin4, IC4.GPA3
  N29: J4.pin5, IC4.GPA4
  N30: J4.pin6, IC4.GPA5
  N31: J4.pin7, IC4.GPA6
  N32: J4.pin8, IC4.GPA7
  3.3V/VCC: R1.Pin_0, R2.Pin_0, IC3.VDD, IC3.A1, IC3.RESET, IC4.VDD, IC4.A0, IC4.A1, IC4.RESET, J5.pin5, J6.pin5, C1.0, C2.0
  SDA: R1.Pin_1, IC3.SDA, IC4.SDA, J5.pin4, J6.pin4
  SCL: R2.Pin_1, IC3.SCL, IC4.SCL, J5.pin3, J6.pin3

notes:
  GND
  Key
  SCL
  SDA
  3V3
  GPA7
  GPA6
  GPA5
  GPA4
  GPA3
  GPA2
  GPA1
  GPA0
  GPB7
  GPB1
  GPB0
  GPB2
  GPB5
  GPB4
  GPB3
  GPB6
  ADDR x02
  ADDR x03

custom parts:
  MCP20017: MCP23017, 28 pins on a 300mil dual inline package (DIP) footprint. 16-Bit I/O Expander with I2C Serial Interface
