# Fritzing sketch mcp23017_Proto_002 (saved by Fritzing 0.9.6b)
stripboards: 1

parts:
  IC2 = IC, DIP package, 28 pins [chip_label=MCP23017 part_number=MCP23017]
  IC3 = IC, DIP package, 28 pins [chip_label=MCP23017 part_number=MCP23017]
  IC4 = IC, DIP package, 28 pins [chip_label=MCP23017 part_number=MCP23017]
  J2 = screw terminal, 9 pins  # not connected
  J3 = screw terminal, 9 pins
  J4 = screw terminal, 9 pins
  J5 = screw terminal, 9 pins
  J6 = screw terminal, 9 pins
  J7 = screw terminal, 9 pins
  J8 = screw terminal, 9 pins
  J9 = screw terminal, 9 pins
  C1 = Ceramic Capacitor [capacitance=100nF voltage=35V package="100 mil [THT, multilayer]"]
  C2 = Ceramic Capacitor [capacitance=100nF voltage=35V package="100 mil [THT, multilayer]"]
  C3 = Ceramic Capacitor [capacitance=100nF voltage=35V package="100 mil [THT, multilayer]"]
  C4 = Ceramic Capacitor [capacitance=100nF voltage=35V package="100 mil [THT, multilayer]"]
  R1 = Resistor [tolerance=±5% power=0.25 resistance=10k package=THT]
  R2 = Resistor [tolerance=±5% power=0.25 resistance=10k package=THT]
  J10 = male pin header, 3 pins [form="♂ (male)"]
  J11 = male pin header, 6 pins [form="♂ (male)"]
  J12 = male pin header, 6 pins [form="♂ (male)"]
  IC1 = IC, DIP package, 28 pins [chip_label=MCP23017 part_number=MCP23017]

nets:
  N1: IC2.pin1, J4.pin2
  N2: IC2.pin2, J4.pin3
  N3: IC2.pin3, J4.pin4
  N4: IC2.pin4, J4.pin5
  N5: IC2.pin5, J4.pin6
  N6: IC2.pin6, J4.pin7
  N7: IC2.pin7, J4.pin8
  N8: IC2.pin8, J4.pin9
  N9: IC2.pin9, IC2.pin15, IC2.pin18, IC3.pin9, IC3.pin16, IC3.pin18, IC4.pin9, IC4.pin15, IC4.pin16, IC4.pin18, C1.0, C2.0, C3.0, C4.0, R1.Pin_1, R2.Pin_1, J10.pin3, J11.pin5, J12.pin5, IC1.pin9, IC1.pin18
  N10: IC2.pin10, IC2.pin16, IC3.pin10, IC3.pin15, IC4.pin10, J3.pin1, J4.pin1, J5.pin1, J6.pin1, J7.pin9, J8.pin9, J9.pin9, C1.1, C2.1, C3.1, C4.1, J10.pin1, J11.pin1, J12.pin1, IC1.pin10, IC1.pin15, IC1.pin16
  N11: IC2.pin12, IC2.pin13, IC3.pin12, IC3.pin13, IC4.pin12, IC4.pin13, R1.Pin_0, R2.Pin_0, J11.pin4, J12.pin3, J12.pin4, IC1.pin13
  N12: IC2.pin17, IC3.pin17, IC4.pin17, J10.pin2, IC1.pin17
  N13: IC2.pin21, J7.pin1
  N14: IC2.pin22, J7.pin2
  N15: IC2.pin23, J7.pin3
  N16: IC2.pin24, J7.pin4
  N17: IC2.pin25, J7.pin5
  N18: IC2.pin26, J7.pin6
  N19: IC2.pin27, J7.pin7
  N20: IC2.pin28, J7.pin8
  N21: IC3.pin1, J5.pin2
  N22: IC3.pin2, J5.pin3
  N23: IC3.pin3, J5.pin4
  N24: IC3.pin4, J5.pin5
  N25: IC3.pin5, J5.pin6
  N26: IC3.pin6, J5.pin7
  N27: IC3.pin7, J5.pin8
  N28: IC3.pin8, J5.pin9
  N29: IC3.pin21, J8.pin1
  N30: IC3.pin22, J8.pin2
  N31: IC3.pin23, J8.pin3
  N32: IC3.pin24, J8.pin4
  N33: IC3.pin25, J8.pin5
  N34: IC3.pin26, J8.pin6
  N35: IC3.pin27, J8.pin7
  N36: IC3.pin28, J8.pin8
  N37: IC4.pin1, J6.pin2
  N38: IC4.pin2, J6.pin3
  N39: IC4.pin3, J6.pin4
  N40: IC4.pin4, J6.pin5
  N41: IC4.pin5, J6.pin6
  N42: IC4.pin6, J6.pin7
  N43: IC4.pin7, J6.pin8
  N44: IC4.pin8, J6.pin9
  N45: IC4.pin21, J9.pin1
  N46: IC4.pin22, J9.pin2
  N47: IC4.pin23, J9.pin3
  N48: IC4.pin24, J9.pin4
  N49: IC4.pin25, J9.pin5
  N50: IC4.pin26, J9.pin6
  N51: IC4.pin27, J9.pin7
  N52: IC4.pin28, J9.pin8
  N53: J3.pin2, IC1.pin1
  N54: J3.pin3, IC1.pin2
  N55: J3.pin4, IC1.pin3
  N56: J3.pin5, IC1.pin4
  N57: J3.pin6, IC1.pin5
  N58: J3.pin7, IC1.pin6
  N59: J3.pin8, IC1.pin7
  N60: J3.pin9, IC1.pin8
  N61: J11.pin3, IC1.pin12
  N62: J11.pin6, J12.pin6

notes:
  5V
  3V3
  SDA
  SCL
  Key
  GND
  Low
  A2
  High
