# Fritzing sketch mcp23017_Proto_003 (saved by Fritzing 0.9.6b)
stripboards: 1

parts:
  J2 = screw terminal, 9 pins
  J3 = screw terminal, 9 pins
  J4 = screw terminal, 9 pins
  J5 = screw terminal, 9 pins
  J6 = screw terminal, 9 pins
  J7 = screw terminal, 9 pins
  J8 = screw terminal, 9 pins
  J9 = screw terminal, 9 pins
  C1 = Ceramic Capacitor [capacitance=100nF voltage=35V package="100 mil [THT, multilayer]"]
  C2 = Ceramic Capacitor [capacitance=100nF voltage=35V package="100 mil [THT, multilayer]"]
  R1 = Resistor [tolerance=±5% power=0.25 resistance=10k package=THT]
  R2 = Resistor [tolerance=±5% power=0.25 resistance=10k package=THT]
  J10 = male pin header, 3 pins [form="♂ (male)"]
  J11 = male pin header, 6 pins [form="♂ (male)"]
  J12 = male pin header, 6 pins [form="♂ (male)"]
  J13 = female pin header, 4 pins [form="♀ (female)"]
  C4 = Ceramic Capacitor [capacitance=100nF voltage=35V package="100 mil [THT, multilayer]"]
  IC1 = MCP20017 [part_number=MCP23017 package="DIP (Dual Inline) [THT]"]
  IC2 = MCP20017 [part_number=MCP23017 package="DIP (Dual Inline) [THT]"]
  IC3 = MCP20017 [part_number=MCP23017 package="DIP (Dual Inline) [THT]"]
  C3 = Ceramic Capacitor [capacitance=100nF voltage=35V package="100 mil [THT, multilayer]"]
  IC4 = MCP20017 [part_number=MCP23017 package="DIP (Dual Inline) [THT]"]

nets:
  N1: J2.pin1, IC1.GPA0
  N2: J2.pin2, IC1.GPA1
  N3: J2.pin3, IC1.GPA2
  N4: J2.pin4, IC1.GPA3
  N5: J2.pin5, IC1.GPA4
  N6: J2.pin6, IC1.GPA5
  N7: J2.pin7, IC1.GPA6
  N8: J2.pin8, IC1.GPA7
  GND: J2.pin9, J3.pin1, J4.pin1, J5.pin1, J6.pin1, J7.pin9, J8.pin9, J9.pin9, C1.1, C2.1, J10.pin1, J11.pin1, J12.pin1, J13.pin1, C4.1, IC1.GND, IC1.A0, IC1.A1, IC2.GND, IC2.A1, IC3.GND, IC3.A0, C3.1, IC4.GND
  N9: J3.pin2, IC1.GPB0
  N10: J3.pin3, IC1.GPB1
  N11: J3.pin4, IC1.GPB2
  N12: J3.pin5, IC1.GPB3
  N13: J3.pin6, IC1.GPB04
  N14: J3.pin7, IC1.GPB5
  N15: J3.pin8, IC1.GPB6
  N16: J3.pin9, IC1.GPB8
  N17: J4.pin2, IC2.GPB0
  N18: J4.pin3, IC2.GPB1
  N19: J4.pin4, IC2.GPB2
  N20: J4.pin5, IC2.GPB3
  N21: J4.pin6, IC2.GPB04
  N22: J4.pin7, IC2.GPB5
  N23: J4.pin8, IC2.GPB6
  N24: J4.pin9, IC2.GPB8
  N25: J5.pin2, IC3.GPB0
  N26: J5.pin3, IC3.GPB1
  N27: J5.pin4, IC3.GPB2
  N28: J5.pin5, IC3.GPB3
  N29: J5.pin6, IC3.GPB04
  N30: J5.pin7, IC3.GPB5
  N31: J5.pin8, IC3.GPB6
  N32: J5.pin9, IC3.GPB8
  N33: J6.pin2, IC4.GPB0
  N34: J6.pin3, IC4.GPB1
  N35: J6.pin4, IC4.GPB2
  N36: J6.pin5, IC4.GPB3
  N37: J6.pin6, IC4.GPB04
  N38: J6.pin7, IC4.GPB5
  N39: J6.pin8, IC4.GPB6
  N40: J6.pin9, IC4.GPB8
  N41: J7.pin1, IC2.GPA0
  N42: J7.pin2, IC2.GPA1
  N43: J7.pin3, IC2.GPA2
  N44: J7.pin4, IC2.GPA3
  N45: J7.pin5, IC2.GPA4
  N46: J7.pin6, IC2.GPA5
  N47: J7.pin7, IC2.GPA6
  N48: J7.pin8, IC2.GPA7
  N49: J8.pin1, IC3.GPA0
  N50: J8.pin2, IC3.GPA1
  N51: J8.pin3, IC3.GPA2
  N52: J8.pin4, IC3.GPA3
  N53: J8.pin5, IC3.GPA4
  N54: J8.pin6, IC3.GPA5
  N55: J8.pin7, IC3.GPA6
  N56: J8.pin8, IC3.GPA7
  N57: J9.pin1, IC4.GPA0
  N58: J9.pin2, IC4.GPA1
  N59: J9.pin3, IC4.GPA2
  N60: J9.pin4, IC4.GPA3
  N61: J9.pin5, IC4.GPA4
  N62: J9.pin6, IC4.GPA5
  N63: J9.pin7, IC4.GPA6
  N64: J9.pin8, IC4.GPA7
  3.3V/VCC: C1.0, C2.0, R1.Pin_1, R2.Pin_1, J10.pin3, J11.pin5, J12.pin5, J13.pin2, C4.0, IC1.VDD, IC1.RESET, IC2.VDD, IC2.A0, IC2.RESET, IC3.VDD, IC3.A1, IC3.RESET, C3.0, IC4.VDD, IC4.A0, IC4.A1, IC4.RESET
  SCL: R1.Pin_0, J11.pin3, J12.pin3, J13.pin3, IC1.SCL, IC2.SCL, IC3.SCL, IC4.SCL
  SDA: R2.Pin_0, J11.pin4, J12.pin4, J13.pin4, IC1.SDA, IC2.SDA, IC3.SDA, IC4.SDA
  A2: J10.pin2, IC1.A2, IC2.A2, IC3.A2, IC4.A2
  Key: J11.pin2
  N65: J11.pin6, J12.pin6

notes:
  3V3 Ext.
  3V3
  SDA
  SCL
  Key
  GND
  Low
  A2
  High
  Black : GND
  Green: 3V3
  White: SCL
  Yellow: SDA
  Pink: A2
  Red: 3V3 Extern
  Display
  I2C

custom parts:
  MCP20017: MCP23017, 28 pins on a 300mil dual inline package (DIP) footprint. 16-Bit I/O Expander with I2C Serial Interface
