# Fritzing sketch L9110_00 (saved by Fritzing 0.9.6b)
stripboards: 1

parts:
  IC2 = L9110 [chip_label=IC package="DIP (Dual Inline) [THT]"]
  IC3 = L9110 [chip_label=IC package="DIP (Dual Inline) [THT]"]
  IC4 = L9110 [chip_label=IC package="DIP (Dual Inline) [THT]"]
  IC5 = L9110 [chip_label=IC package="DIP (Dual Inline) [THT]"]
  J1 = male pin header, 2 pins [form="♂ (male)"]
  J2 = male pin header, 2 pins [form="♂ (male)"]
  J3 = male pin header, 2 pins [form="♂ (male)"]
  J4 = male pin header, 2 pins [form="♂ (male)"]
  J5 = male pin header, 1 pin [form="♂ (male)"]
  J9 = male pin header, 1 pin [form="♂ (male)"]
  J10 = male pin header, 1 pin [form="♂ (male)"]
  J11 = male pin header, 1 pin [form="♂ (male)"]
  J12 = male pin header, 1 pin [form="♂ (male)"]
  J13 = male pin header, 1 pin [form="♂ (male)"]
  J14 = male pin header, 1 pin [form="♂ (male)"]
  J15 = male pin header, 1 pin [form="♂ (male)"]
  J8 = male pin header, 3 pins [form="♂ (male)"]
  R1 = Resistor [tolerance=±5% power=0.25 resistance=10k package=THT]
  R9 = Resistor [tolerance=±5% power=0.25 resistance=10k package=THT]
  R10 = Resistor [tolerance=±5% power=0.25 resistance=10k package=THT]
  R11 = Resistor [tolerance=±5% power=0.25 resistance=10k package=THT]
  R12 = Resistor [tolerance=±5% power=0.25 resistance=10k package=THT]
  R13 = Resistor [tolerance=±5% power=0.25 resistance=10k package=THT]
  R14 = Resistor [tolerance=±5% power=0.25 resistance=10k package=THT]
  R15 = Resistor [tolerance=±5% power=0.25 resistance=10k package=THT]
  Part1 = Motor Driver 1A Dual TB6612FNG  # not connected
  Part2 = Motor Driver 1A Dual TB6612FNG  # not connected
  Part3 = Motor Driver 1A Dual TB6612FNG  # not connected
  Part4 = Motor Driver 1A Dual TB6612FNG  # not connected
  Part5 = Motor Driver 1A Dual TB6612FNG  # not connected

nets:
  N1: IC2.OA, J9.pin1
  VCC: IC2.Vcc, IC3.Vcc, IC4.Vcc, IC5.Vcc, J8.pin1
  N2: IC2.OB, J5.pin1
  GND: IC2.GND, IC3.GND, IC4.GND, IC5.GND, J8.pin2
  N3: IC2.IA, J1.pin1, R1.Pin_0
  N4: IC2.IB, R12.Pin_0
  N5: IC3.OA, J11.pin1
  N6: IC3.OB, J10.pin1
  N7: IC3.IA, J2.pin1, R9.Pin_0
  N8: IC3.IB, J2.pin2, R13.Pin_0
  N9: IC4.OA, J13.pin1
  N10: IC4.OB, J12.pin1
  N11: IC4.IA, J3.pin1, R10.Pin_0
  N12: IC4.IB, J3.pin2, R14.Pin_0
  N13: IC5.OA, J15.pin1
  N14: IC5.OB, J14.pin1
  N15: IC5.IA, J4.pin1, R11.Pin_0
  N16: IC5.IB, J4.pin2, R15.Pin_0
  N17: J8.pin3, R1.Pin_1, R9.Pin_1, R10.Pin_1, R11.Pin_1, R12.Pin_1, R13.Pin_1, R14.Pin_1, R15.Pin_1

notes:
  12V Gul
  GND Sort
  3V3 Grøn
  Motor
  Input

custom parts:
  L9110: L9110 The ASIC device control and drive motor design two-channel push-pull power amplifier discrete circuits integrated into a monolithic IC, peripheral devices and reduce the cost, improve the reliability of the whole.
