# Fritzing sketch LedStripDriver (saved by Fritzing 0.9.6b)
circuit board: 5.7cm x 6cm

parts:
  R3 = Resistor [tolerance=±5% power=0.25 resistance=10 package=THT]
  Q1 = Basic FET N-Channel [part_number=IRFZ44 package="TO220 [THT]"]
  R2 = 8 Resistor Network [part_number="SIL 8x470R" package="SIP (Single Inline)"]
  R5 = Resistor [tolerance=±5% power=0.25 resistance=10 package=THT]
  R7 = Resistor [tolerance=±5% power=0.25 resistance=10 package=THT]
  R10 = Resistor [tolerance=±5% power=0.25 resistance=10 package=THT]
  R4 = Resistor [tolerance=±5% power=0.25 resistance=10 package=THT]
  R6 = Resistor [tolerance=±5% power=0.25 resistance=10 package=THT]
  R9 = Resistor [tolerance=±5% power=0.25 resistance=10 package=THT]
  R10_2 = Resistor [tolerance=±5% power=0.25 resistance=10 package=THT]
  Q2 = Basic FET N-Channel [part_number=IRFZ44 package="TO220 [THT]"]
  Q3 = Basic FET N-Channel [part_number=IRFZ44 package="TO220 [THT]"]
  Q4 = Basic FET N-Channel [part_number=IRFZ44 package="TO220 [THT]"]
  Q5 = Basic FET N-Channel [part_number=IRFZ44 package="TO220 [THT]"]
  Q6 = Basic FET N-Channel [part_number=IRFZ44 package="TO220 [THT]"]
  Q7 = Basic FET N-Channel [part_number=IRFZ44 package="TO220 [THT]"]
  Q8 = Basic FET N-Channel [part_number=IRFZ44 package="TO220 [THT]"]
  R1 = 8 Resistor Network [part_number="SIL 8x10K" package="SIP (Single Inline)"]
  IC1 = ULN2803A [package=THT]
  J5 = female pin header, 2 pins [form="♀ (female)"]
  J2 = male pin header, 4 pins [form="♂ (male)"]
  J1 = male pin header, 4 pins [form="♂ (male)"]
  R18 = Resistor [tolerance=±5% power=0.25 resistance=10 package=THT]
  R16 = Resistor [tolerance=±5% power=0.25 resistance=10 package=THT]
  R14 = Resistor [tolerance=±5% power=0.25 resistance=10 package=THT]
  R12 = Resistor [tolerance=±5% power=0.25 resistance=10 package=THT]
  R17 = Resistor [tolerance=±5% power=0.25 resistance=10 package=THT]
  R15 = Resistor [tolerance=±5% power=0.25 resistance=10 package=THT]
  R13 = Resistor [tolerance=±5% power=0.25 resistance=10 package=THT]
  R11 = Resistor [tolerance=±5% power=0.25 resistance=10 package=THT]
  Q16 = Basic FET N-Channel [part_number=IRFZ44 package="TO220 [THT]"]
  Q15 = Basic FET N-Channel [part_number=IRFZ44 package="TO220 [THT]"]
  Q14 = Basic FET N-Channel [part_number=IRFZ44 package="TO220 [THT]"]
  Q13 = Basic FET N-Channel [part_number=IRFZ44 package="TO220 [THT]"]
  Q12 = Basic FET N-Channel [part_number=IRFZ44 package="TO220 [THT]"]
  Q11 = Basic FET N-Channel [part_number=IRFZ44 package="TO220 [THT]"]
  Q10 = Basic FET N-Channel [part_number=IRFZ44 package="TO220 [THT]"]
  Q9 = Basic FET N-Channel [part_number=IRFZ44 package="TO220 [THT]"]
  R19 = 8 Resistor Network [part_number="SIL 8x10K" package="SIP (Single Inline)"]
  R20 = 8 Resistor Network [part_number="SIL 8x470R" package="SIP (Single Inline)"]
  IC2 = ULN2803A [package=THT]
  J3 = male pin header, 4 pins [form="♂ (male)"]
  J4 = male pin header, 4 pins [form="♂ (male)"]
  J6 = female pin header, 2 pins [form="♀ (female)"]
  J8 = female pin header, 5 pins [form="♀ (female)"]
  J7 = female pin header, 5 pins [form="♀ (female)"]
  J10 = female pin header, 5 pins [form="♀ (female)"]
  J9 = female pin header, 5 pins [form="♀ (female)"]

nets:
  N1: R3.Pin_0, R2.9, IC1.Out_1
  N2: R3.Pin_1, Q1.gate
  GND: Q1.drain, Q2.drain, Q3.drain, Q4.drain, Q5.drain, Q6.drain, Q7.drain, Q8.drain, IC1.0V, J5.pin2, Q16.drain, Q15.drain, Q14.drain, Q13.drain, Q12.drain, Q11.drain, Q10.drain, Q9.drain, IC2.0V, J6.pin2
  N3: Q1.source, J7.pin2
  12V: R2.1, R1.1, IC1.COM_-_Common, J5.pin1, R19.1, R20.1, IC2.COM_-_Common, J6.pin1, J8.pin1, J7.pin1, J10.pin1, J9.pin1
  N4: R2.2, R10_2.Pin_0, IC1.Out_8
  N5: R2.3, R10.Pin_0, IC1.Out_7
  N6: R2.4, R9.Pin_0, IC1.Out_6
  N7: R2.5, R7.Pin_0, IC1.Out_5
  N8: R2.6, R6.Pin_0, IC1.Out_4
  N9: R2.7, R5.Pin_0, IC1.Out_3
  N10: R2.8, R4.Pin_0, IC1.Out_2
  N11: R5.Pin_1, Q3.gate
  N12: R7.Pin_1, Q5.gate
  N13: R10.Pin_1, Q7.gate
  N14: R4.Pin_1, Q2.gate
  N15: R6.Pin_1, Q4.gate
  N16: R9.Pin_1, Q6.gate
  N17: R10_2.Pin_1, Q8.gate
  N18: Q2.source, J7.pin3
  N19: Q3.source, J7.pin4
  N20: Q4.source, J7.pin5
  N21: Q5.source, J8.pin2
  N22: Q6.source, J8.pin3
  N23: Q7.source, J8.pin4
  N24: Q8.source, J8.pin5
  N25: R1.2, IC1.In_8, J2.pin4
  N26: R1.3, IC1.In_7, J2.pin3
  N27: R1.4, IC1.In_6, J2.pin2
  N28: R1.5, IC1.In_5, J2.pin1
  N29: R1.6, IC1.In_4, J1.pin4
  N30: R1.7, IC1.In_3, J1.pin3
  N31: R1.8, IC1.In_2, J1.pin2
  N32: R1.9, IC1.In_1, J1.pin1
  N33: R18.Pin_0, R20.2, IC2.Out_8
  N34: R18.Pin_1, Q16.gate
  N35: R16.Pin_0, R20.4, IC2.Out_6
  N36: R16.Pin_1, Q14.gate
  N37: R14.Pin_0, R20.6, IC2.Out_4
  N38: R14.Pin_1, Q12.gate
  N39: R12.Pin_0, R20.8, IC2.Out_2
  N40: R12.Pin_1, Q10.gate
  N41: R17.Pin_0, R20.3, IC2.Out_7
  N42: R17.Pin_1, Q15.gate
  N43: R15.Pin_0, R20.5, IC2.Out_5
  N44: R15.Pin_1, Q13.gate
  N45: R13.Pin_0, R20.7, IC2.Out_3
  N46: R13.Pin_1, Q11.gate
  N47: R11.Pin_0, R20.9, IC2.Out_1
  N48: R11.Pin_1, Q9.gate
  N49: Q16.source, J10.pin5
  N50: Q15.source, J10.pin4
  N51: Q14.source, J10.pin3
  N52: Q13.source, J10.pin2
  N53: Q12.source, J9.pin5
  N54: Q11.source, J9.pin4
  N55: Q10.source, J9.pin3
  N56: Q9.source, J9.pin2
  N57: R19.2, IC2.In_8, J4.pin4
  N58: R19.3, IC2.In_7, J4.pin3
  N59: R19.4, IC2.In_6, J4.pin2
  N60: R19.5, IC2.In_5, J4.pin1
  N61: R19.6, IC2.In_4, J3.pin4
  N62: R19.7, IC2.In_3, J3.pin3
  N63: R19.8, IC2.In_2, J3.pin2
  N64: R19.9, IC2.In_1, J3.pin1

notes:
  LED strip driver
  sekt1953@gmail.com  omjk1949
