# Fritzing sketch LedStripDriver_002 (saved by Fritzing 0.9.6b)
circuit board: 5.4cm x 6cm

parts:
  R3 = Resistor [tolerance=±5% power=0.25 resistance=10 package=THT]
  Q1 = Basic FET N-Channel [part_number=IRFZ44 package="TO220 [THT]"]
  R2 = 8 Resistor Network [part_number="SIL 8x470R" package="SIP (Single Inline)"]
  R5 = Resistor [tolerance=±5% power=0.25 resistance=10 package=THT]
  R7 = Resistor [tolerance=±5% power=0.25 resistance=10 package=THT]
  R10 = Resistor [tolerance=±5% power=0.25 resistance=10 package=THT]
  R4 = Resistor [tolerance=±5% power=0.25 resistance=10 package=THT]
  R6 = Resistor [tolerance=±5% power=0.25 resistance=10 package=THT]
  R9 = Resistor [tolerance=±5% power=0.25 resistance=10 package=THT]
  R10_2 = Resistor [tolerance=±5% power=0.25 resistance=10 package=THT]
  Q2 = Basic FET N-Channel [part_number=IRFZ44 package="TO220 [THT]"]
  Q3 = Basic FET N-Channel [part_number=IRFZ44 package="TO220 [THT]"]
  Q5 = Basic FET N-Channel [part_number=IRFZ44 package="TO220 [THT]"]
  Q6 = Basic FET N-Channel [part_number=IRFZ44 package="TO220 [THT]"]
  Q7 = Basic FET N-Channel [part_number=IRFZ44 package="TO220 [THT]"]
  Q8 = Basic FET N-Channel [part_number=IRFZ44 package="TO220 [THT]"]
  IC1 = ULN2803A [package=THT]
  J5 = female pin header, 2 pins [form="♀ (female)"]
  J2 = male pin header, 4 pins [form="♂ (male)"]
  J1 = male pin header, 4 pins [form="♂ (male)"]
  R18 = Resistor [tolerance=±5% power=0.25 resistance=10 package=THT]
  R16 = Resistor [tolerance=±5% power=0.25 resistance=10 package=THT]
  R14 = Resistor [tolerance=±5% power=0.25 resistance=10 package=THT]
  R12 = Resistor [tolerance=±5% power=0.25 resistance=10 package=THT]
  R17 = Resistor [tolerance=±5% power=0.25 resistance=10 package=THT]
  R15 = Resistor [tolerance=±5% power=0.25 resistance=10 package=THT]
  R13 = Resistor [tolerance=±5% power=0.25 resistance=10 package=THT]
  R11 = Resistor [tolerance=±5% power=0.25 resistance=10 package=THT]
  Q16 = Basic FET N-Channel [part_number=IRFZ44 package="TO220 [THT]"]
  Q15 = Basic FET N-Channel [part_number=IRFZ44 package="TO220 [THT]"]
  Q14 = Basic FET N-Channel [part_number=IRFZ44 package="TO220 [THT]"]
  Q13 = Basic FET N-Channel [part_number=IRFZ44 package="TO220 [THT]"]
  Q12 = Basic FET N-Channel [part_number=IRFZ44 package="TO220 [THT]"]
  Q11 = Basic FET N-Channel [part_number=IRFZ44 package="TO220 [THT]"]
  Q10 = Basic FET N-Channel [part_number=IRFZ44 package="TO220 [THT]"]
  R20 = 8 Resistor Network [part_number="SIL 8x470R" package="SIP (Single Inline)"]
  IC2 = ULN2803A [package=THT]
  J3 = male pin header, 4 pins [form="♂ (male)"]
  J4 = male pin header, 4 pins [form="♂ (male)"]
  J6 = female pin header, 2 pins [form="♀ (female)"]
  J8 = female pin header, 5 pins [form="♀ (female)"]
  J7 = female pin header, 5 pins [form="♀ (female)"]
  J10 = female pin header, 5 pins [form="♀ (female)"]
  J9 = female pin header, 5 pins [form="♀ (female)"]
  Q4 = Basic FET N-Channel [part_number=IRFZ44 package="TO220 [THT]"]
  Q09 = Basic FET N-Channel [part_number=IRFZ44 package="TO220 [THT]"]

nets:
  N1: R3.Pin_0, R2.9, IC1.Out_1
  N2: R3.Pin_1, Q1.gate
  N3: Q1.drain, J7.pin2
  GND: Q1.source, Q2.source, Q3.source, Q5.source, Q6.source, Q7.source, Q8.source, IC1.0V, J5.pin2, Q16.source, Q15.source, Q14.source, Q13.source, Q12.source, Q11.source, Q10.source, IC2.0V, J6.pin2, Q4.source, Q09.source
  12V: R2.1, IC1.COM_-_Common, J5.pin1, R20.1, IC2.COM_-_Common, J6.pin1, J8.pin1, J7.pin1, J10.pin1, J9.pin1
  N4: R2.2, R10_2.Pin_0, IC1.Out_8
  N5: R2.3, R10.Pin_0, IC1.Out_7
  N6: R2.4, R9.Pin_0, IC1.Out_6
  N7: R2.5, R7.Pin_0, IC1.Out_5
  N8: R2.6, R6.Pin_0, IC1.Out_4
  N9: R2.7, R5.Pin_0, IC1.Out_3
  N10: R2.8, R4.Pin_0, IC1.Out_2
  N11: R5.Pin_1, Q3.gate
  N12: R7.Pin_1, Q5.gate
  N13: R10.Pin_1, Q7.gate
  N14: R4.Pin_1, Q2.gate
  N15: R6.Pin_1, Q4.gate
  N16: R9.Pin_1, Q6.gate
  N17: R10_2.Pin_1, Q8.gate
  N18: Q2.drain, J7.pin3
  N19: Q3.drain, J7.pin4
  N20: Q5.drain, J8.pin2
  N21: Q6.drain, J8.pin3
  N22: Q7.drain, J8.pin4
  N23: Q8.drain, J8.pin5
  N24: IC1.In_1, J1.pin1
  N25: IC1.In_2, J1.pin2
  N26: IC1.In_3, J1.pin3
  N27: IC1.In_4, J1.pin4
  N28: IC1.In_5, J2.pin1
  N29: IC1.In_6, J2.pin2
  N30: IC1.In_7, J2.pin3
  N31: IC1.In_8, J2.pin4
  N32: R18.Pin_0, R20.2, IC2.Out_8
  N33: R18.Pin_1, Q16.gate
  N34: R16.Pin_0, R20.4, IC2.Out_6
  N35: R16.Pin_1, Q14.gate
  N36: R14.Pin_0, R20.6, IC2.Out_4
  N37: R14.Pin_1, Q12.gate
  N38: R12.Pin_0, R20.8, IC2.Out_2
  N39: R12.Pin_1, Q10.gate
  N40: R17.Pin_0, R20.3, IC2.Out_7
  N41: R17.Pin_1, Q15.gate
  N42: R15.Pin_0, R20.5, IC2.Out_5
  N43: R15.Pin_1, Q13.gate
  N44: R13.Pin_0, R20.7, IC2.Out_3
  N45: R13.Pin_1, Q11.gate
  N46: R11.Pin_0, R20.9, IC2.Out_1
  N47: R11.Pin_1, Q09.gate
  N48: Q16.drain, J10.pin5
  N49: Q15.drain, J10.pin4
  N50: Q14.drain, J10.pin3
  N51: Q13.drain, J10.pin2
  N52: Q12.drain, J9.pin5
  N53: Q11.drain, J9.pin4
  N54: Q10.drain, J9.pin3
  N55: IC2.In_1, J3.pin1
  N56: IC2.In_2, J3.pin2
  N57: IC2.In_3, J3.pin3
  N58: IC2.In_4, J3.pin4
  N59: IC2.In_5, J4.pin1
  N60: IC2.In_6, J4.pin2
  N61: IC2.In_7, J4.pin3
  N62: IC2.In_8, J4.pin4
  N63: J7.pin5, Q4.drain
  N64: J9.pin2, Q09.drain

notes:
  LED strip driver 002
  sekt1953@gmail.com  omjk1949
  +
  GND
  20240807 2021
