# Fritzing sketch mcp23017_002 (saved by Fritzing 0.9.6b)
circuit board: 10cm x 5cm
breadboards: 1

parts:
  IC1 = DIP - 28 pins [chip_label=IC package="DIP (Dual Inline) [THT]"]
  IO1 = ULN2803A [form="♂ (male)" package=THT]
  C1 = Ceramic Capacitor [capacitance=100nF voltage=35V package="100 mil [THT, multilayer]"]
  J1 = screw terminal, 9 pins
  J2 = screw terminal, 9 pins
  IC2 = DIP - 28 pins [chip_label=IC package="DIP (Dual Inline) [THT]"]  # not connected

nets:
  N1: IC1.GPB0, J2.pin9
  N2: IC1.GPB1, J2.pin8
  N3: IC1.GPB2, J2.pin7
  N4: IC1.pin4, J2.pin6
  N5: IC1.pin5, J2.pin5
  N6: IC1.pin6, J2.pin4
  N7: IC1.pin7, J2.pin3
  N8: IC1.pin8, J2.pin2
  N9: IC1.pin9, IO1.pin10, C1.0, J1.pin1
  N10: IC1.pin10, IO1.pin9, C1.1, J2.pin1
  N11: IC1.pin21, IO1.pin18
  N12: IC1.pin22, IO1.pin17
  N13: IC1.pin23, IO1.pin16
  N14: IC1.pin24, IO1.pin15
  N15: IC1.pin25, IO1.pin14
  N16: IC1.pin26, IO1.pin13
  N17: IC1.pin27, IO1.pin12
  N18: IC1.pin28, IO1.pin11
  N19: IO1.pin1, J1.pin9
  N20: IO1.pin2, J1.pin8
  N21: IO1.pin3, J1.pin7
  N22: IO1.pin4, J1.pin6
  N23: IO1.pin5, J1.pin5
  N24: IO1.pin6, J1.pin4
  N25: IO1.pin7, J1.pin3
  N26: IO1.pin8, J1.pin2

custom parts:
  DIP - 28 pins: A DIP stand-in part for whatever IC you want. With 28 pins on a 300mil dual inline package (DIP) footprint.
  ULN2803A: Generic male header
