# Fritzing sketch mcp23017_200 (saved by Fritzing 0.9.6b)
circuit board: 16.51cm x 3.31cm
breadboards: 1

parts:
  IC1 = DIP - 28 pins [chip_label=IC part_number=MCP23017 package="DIP (Dual Inline) [THT]"]
  IC2 = DIP - 28 pins [chip_label=IC part_number=MCP23017 package="DIP (Dual Inline) [THT]"]
  IC3 = DIP - 28 pins [chip_label=IC part_number=MCP23017 package="DIP (Dual Inline) [THT]"]
  IC4 = DIP - 28 pins [chip_label=IC part_number=MCP23017 package="DIP (Dual Inline) [THT]"]
  C1 = Ceramic Capacitor [capacitance=100nF voltage=35V package="100 mil [THT, multilayer]"]
  C2 = Ceramic Capacitor [capacitance=100nF voltage=35V package="100 mil [THT, multilayer]"]
  C3 = Ceramic Capacitor [capacitance=100nF voltage=35V package="100 mil [THT, multilayer]"]
  C4 = Ceramic Capacitor [capacitance=100nF voltage=35V package="100 mil [THT, multilayer]"]
  J1 = screw terminal, 9 pins
  J2 = screw terminal, 9 pins
  J4 = screw terminal, 9 pins
  J3 = screw terminal, 9 pins
  J6 = screw terminal, 9 pins
  J5 = screw terminal, 9 pins
  J8 = screw terminal, 9 pins
  J7 = screw terminal, 9 pins
  J9 = male pin header, 6 pins [form="♂ (male)"]
  J10 = male pin header, 6 pins [form="♂ (male)"]
  J11 = male pin header, 3 pins [form="♂ (male)"]
  R1 = Resistor [tolerance=±5% power=0.25 resistance=10k package=THT]
  R2 = Resistor [tolerance=±5% power=0.25 resistance=10k package=THT]

nets:
  N1: IC1.GPB0, J2.pin8
  N2: IC1.GPB1, J2.pin7
  N3: IC1.GPB2, J2.pin6
  N4: IC1.pin4, J2.pin5
  N5: IC1.pin5, J2.pin4
  N6: IC1.pin6, J2.pin3
  N7: IC1.pin7, J2.pin2
  N8: IC1.pin8, J2.pin1
  N9: IC1.pin9, IC1.pin18, IC2.pin9, IC2.pin15, IC2.pin18, IC3.pin9, IC3.pin16, IC3.pin18, IC4.pin9, IC4.pin15, IC4.pin16, IC4.pin18, C1.0, C2.0, C3.0, C4.0, J9.pin2, J10.pin2, J11.pin1, R1.Pin_1, R2.Pin_1
  N10: IC1.pin10, IC1.pin15, IC1.pin16, IC2.pin10, IC2.pin16, IC3.pin10, IC3.pin15, IC4.pin10, C1.1, C2.1, C3.1, C4.1, J1.pin9, J2.pin9, J4.pin9, J3.pin9, J6.pin9, J5.pin9, J8.pin9, J7.pin9, J9.pin6, J10.pin6, J11.pin3
  N11: IC1.pin12, IC2.pin12, IC3.pin12, IC4.pin12, J9.pin4, J10.pin4, R1.Pin_0
  N12: IC1.pin13, IC2.pin13, IC3.pin13, IC4.pin13, J9.pin3, J10.pin3, R2.Pin_0
  N13: IC1.pin17, IC2.pin17, IC3.pin17, IC4.pin17, J11.pin2
  N14: IC1.pin21, J1.pin8
  N15: IC1.pin22, J1.pin7
  N16: IC1.pin23, J1.pin6
  N17: IC1.pin24, J1.pin5
  N18: IC1.pin25, J1.pin4
  N19: IC1.pin26, J1.pin3
  N20: IC1.pin27, J1.pin2
  N21: IC1.pin28, J1.pin1
  N22: IC2.GPB0, J4.pin8
  N23: IC2.GPB1, J4.pin7
  N24: IC2.GPB2, J4.pin6
  N25: IC2.pin4, J4.pin5
  N26: IC2.pin5, J4.pin4
  N27: IC2.pin6, J4.pin3
  N28: IC2.pin7, J4.pin2
  N29: IC2.pin8, J4.pin1
  N30: IC2.pin21, J3.pin8
  N31: IC2.pin22, J3.pin7
  N32: IC2.pin23, J3.pin6
  N33: IC2.pin24, J3.pin5
  N34: IC2.pin25, J3.pin4
  N35: IC2.pin26, J3.pin3
  N36: IC2.pin27, J3.pin2
  N37: IC2.pin28, J3.pin1
  N38: IC3.GPB0, J6.pin8
  N39: IC3.GPB1, J6.pin7
  N40: IC3.GPB2, J6.pin6
  N41: IC3.pin4, J6.pin5
  N42: IC3.pin5, J6.pin4
  N43: IC3.pin6, J6.pin3
  N44: IC3.pin7, J6.pin2
  N45: IC3.pin8, J6.pin1
  N46: IC3.pin21, J5.pin8
  N47: IC3.pin22, J5.pin7
  N48: IC3.pin23, J5.pin6
  N49: IC3.pin24, J5.pin5
  N50: IC3.pin25, J5.pin4
  N51: IC3.pin26, J5.pin3
  N52: IC3.pin27, J5.pin2
  N53: IC3.pin28, J5.pin1
  N54: IC4.GPB0, J8.pin8
  N55: IC4.GPB1, J8.pin7
  N56: IC4.GPB2, J8.pin6
  N57: IC4.pin4, J8.pin5
  N58: IC4.pin5, J8.pin4
  N59: IC4.pin6, J8.pin3
  N60: IC4.pin7, J8.pin2
  N61: IC4.pin8, J8.pin1
  N62: IC4.pin21, J7.pin8
  N63: IC4.pin22, J7.pin7
  N64: IC4.pin23, J7.pin6
  N65: IC4.pin24, J7.pin5
  N66: IC4.pin25, J7.pin4
  N67: IC4.pin26, J7.pin3
  N68: IC4.pin27, J7.pin2
  N69: IC4.pin28, J7.pin1
  N70: J9.pin1, J10.pin1

notes:
  H
  L
  3V3
  SDA
  SCL
  GND
  Key
  MCP23017_200.fzz
  sekt1953@gmail.com   OMJK
  A7
  A6
  A5
  A4
  A3
  A2
  A1
  A0
  G
  B7
  B6
  B5
  B4
  B1
  B0
  B2
  B3

custom parts:
  DIP - 28 pins: A DIP stand-in part for whatever IC you want. With 28 pins on a 300mil dual inline package (DIP) footprint.
