# Fritzing sketch mcp23017_Finn_001 (saved by Fritzing 0.9.6b)
circuit board: 10cm x 6cm

parts:
  J1 = screw terminal, 9 pins
  J2 = screw terminal, 9 pins
  J3 = screw terminal, 9 pins
  J4 = screw terminal, 9 pins
  R1 = Resistor [tolerance=±5% power=0.25 resistance=10k package=THT]
  R2 = Resistor [tolerance=±5% power=0.25 resistance=10k package=THT]
  C2 = Ceramic Capacitor [capacitance=100nF voltage=35V package="100 mil [THT, multilayer]"]
  IC1 = IC, DIP package, 28 pins [chip_label=MCP23017 part_number=MCP23017]
  IC2 = IC, DIP package, 28 pins [chip_label=MCP23017 part_number=MCP23017]
  C3 = Ceramic Capacitor [capacitance=100nF voltage=35V package="100 mil [THT, multilayer]"]

nets:
  N1: J1.pin1, IC2.pin8
  N2: J1.pin2, IC2.pin7
  N3: J1.pin3, IC2.pin6
  N4: J1.pin4, IC2.pin5
  N5: J1.pin5, IC2.pin4
  N6: J1.pin6, IC2.pin3
  N7: J1.pin7, IC2.pin2
  N8: J1.pin8, IC2.pin1
  3.3V: J1.pin9, J4.pin1, R1.Pin_0, R2.Pin_0, C2.0, IC1.pin9, IC1.pin18, IC2.pin9, IC2.pin15, IC2.pin18, C3.0
  N9: J2.pin1, IC1.pin8
  N10: J2.pin2, IC1.pin7
  N11: J2.pin3, IC1.pin6
  N12: J2.pin4, IC1.pin5
  N13: J2.pin5, IC1.pin4
  N14: J2.pin6, IC1.pin3
  N15: J2.pin7, IC1.pin2
  N16: J2.pin8, IC1.pin1
  N17: J2.pin9, J3.pin1
  N18: J3.pin2, IC1.pin28
  N19: J3.pin3, IC1.pin27
  N20: J3.pin4, IC1.pin26
  N21: J3.pin5, IC1.pin25
  N22: J3.pin6, IC1.pin24
  N23: J3.pin7, IC1.pin23
  N24: J3.pin8, IC1.pin22
  N25: J3.pin9, IC1.pin21
  N26: J4.pin2, IC2.pin28
  N27: J4.pin3, IC2.pin27
  N28: J4.pin4, IC2.pin26
  N29: J4.pin5, IC2.pin25
  N30: J4.pin6, IC2.pin24
  N31: J4.pin7, IC2.pin23
  N32: J4.pin8, IC2.pin22
  N33: J4.pin9, IC2.pin21
  SDA: R1.Pin_1, IC1.pin13, IC2.pin13
  SCL: R2.Pin_1, IC1.pin12, IC2.pin12
  GND: C2.1, IC1.pin10, IC1.pin15, IC1.pin16, IC1.pin17, IC2.pin10, IC2.pin16, IC2.pin17, C3.1

notes:
  GND
  Key
  SCL
  SDA
  3V3
  5V
  GPA7
  GPA6
  GPA5
  GPA4
  GPA3
  GPA2
  GPA1
  GPA0
  GPB7
  GPB1
  GPB0
  GPB2
  GPB5
  GPB4
  GPB3
  GPB6
