# Fritzing sketch Olddriver (saved by Fritzing 0.9.6b)
circuit board: 10.079cm x 5.67402cm
breadboards: 1

parts:
  Q3 = NPN-Transistor [package="TO92 [THT]"]
  Q2 = NPN-Transistor [package="TO92 [THT]"]
  Q4 = NPN-Transistor [package="TO92 [THT]"]
  U1 = TLP620-4 [package="DIP (Dual Inline) [THT]"]
  R1 = Resistor [tolerance=±5% power=0.25 resistance=10k package=THT]
  R2 = Resistor [tolerance=±5% power=0.25 resistance=10k package=THT]
  R3 = Resistor [tolerance=±5% power=0.25 resistance=10k package=THT]
  R4 = Resistor [tolerance=±5% power=0.25 resistance=10k package=THT]
  R5 = Resistor [tolerance=±5% power=0.25 resistance=10k package=THT]
  R6 = Resistor [tolerance=±5% power=0.25 resistance=10k package=THT]
  R7 = Resistor [tolerance=±5% power=0.25 resistance=10k package=THT]
  R8 = Resistor [tolerance=±5% power=0.25 resistance=10k package=THT]
  Q1 = NPN-Transistor [part_number=BD135 package="TO92 [THT]"]
  R9 = Resistor [tolerance=±5% power=0.25 resistance=1k package=THT]
  R10 = Resistor [tolerance=±5% power=0.25 resistance=220 package=THT]
  R11 = Resistor [tolerance=±5% power=0.25 resistance=220 package=THT]
  R12 = Resistor [tolerance=±5% power=0.25 resistance=220 package=THT]
  J1 = screw terminal, 8 pins
  J2 = screw terminal, 6 pins

nets:
  GND: Q3.E, Q2.E, Q4.E, R2.Pin_1, R4.Pin_1, R6.Pin_1, R8.Pin_1, Q1.E, J2.pin6
  N1: Q3.B, R5.Pin_1
  N2: Q3.C, J2.pin4
  N3: Q2.B, R3.Pin_1
  N4: Q2.C, J2.pin3
  N5: Q4.B, R7.Pin_1
  N6: Q4.C, J2.pin5
  N7: U1.pin1, R9.Pin_1
  N8: U1.pin2, J1.pin2
  N9: U1.pin3, R10.Pin_1
  N10: U1.pin4, J1.pin4
  N11: U1.pin5, R11.Pin_1
  N12: U1.pin6, J1.pin6
  N13: U1.pin7, R12.Pin_1
  N14: U1.pin8, J1.pin8
  N15: U1.pin9, R7.Pin_0, R8.Pin_0
  N16: U1.pin10, U1.pin12, U1.pin14, U1.pin16, J2.pin1
  N17: U1.pin11, R5.Pin_0, R6.Pin_0
  N18: U1.pin13, R3.Pin_0, R4.Pin_0
  N19: U1.pin15, R1.Pin_0, R2.Pin_0
  N20: R1.Pin_1, Q1.B
  N21: Q1.C, J2.pin2
  N22: R9.Pin_0, J1.pin1
  N23: R10.Pin_0, J1.pin3
  N24: R11.Pin_0, J1.pin5
  N25: R12.Pin_0, J1.pin7

custom parts:
  TLP620-4: Quad Photo-transistor optically coupled to two infrared emitting diodes connected in inverse parallel.
