# Fritzing sketch SignalDriver_001 (saved by Fritzing 0.9.6b)
circuit board: 3.7cm x 6.1cm

parts:
  R3 = Resistor [tolerance=±5% power=0.25 resistance=220 package=THT]
  R5 = Resistor [tolerance=±5% power=0.25 resistance=220 package=THT]
  R7 = Resistor [tolerance=±5% power=0.25 resistance=220 package=THT]
  R10 = Resistor [tolerance=±5% power=0.25 resistance=220 package=THT]
  R4 = Resistor [tolerance=±5% power=0.25 resistance=10 package=THT]
  R6 = Resistor [tolerance=±5% power=0.25 resistance=220 package=THT]
  R9 = Resistor [tolerance=±5% power=0.25 resistance=220 package=THT]
  R10_2 = Resistor [tolerance=±5% power=0.25 resistance=220 package=THT]
  IC1 = ULN2803A [package=THT]
  J5 = female pin header, 2 pins [form="♀ (female)"]
  J2 = male pin header, 4 pins [form="♂ (male)"]
  J1 = male pin header, 4 pins [form="♂ (male)"]
  R18 = Resistor [tolerance=±5% power=0.25 resistance=220 package=THT]
  R16 = Resistor [tolerance=±5% power=0.25 resistance=220 package=THT]
  R14 = Resistor [tolerance=±5% power=0.25 resistance=220 package=THT]
  R12 = Resistor [tolerance=±5% power=0.25 resistance=220 package=THT]
  R17 = Resistor [tolerance=±5% power=0.25 resistance=220 package=THT]
  R15 = Resistor [tolerance=±5% power=0.25 resistance=220 package=THT]
  R13 = Resistor [tolerance=±5% power=0.25 resistance=220 package=THT]
  R11 = Resistor [tolerance=±5% power=0.25 resistance=220 package=THT]
  IC2 = ULN2803A [package=THT]
  J3 = male pin header, 4 pins [form="♂ (male)"]
  J4 = male pin header, 4 pins [form="♂ (male)"]
  J6 = female pin header, 2 pins [form="♀ (female)"]
  J7 = screw terminal, 9 pins
  J8 = screw terminal, 9 pins
  J9 = screw terminal, 9 pins
  J10 = screw terminal, 9 pins

nets:
  N1: R3.Pin_0, IC1.Out_1
  N2: R3.Pin_1, J7.pin1, J8.pin1
  N3: R5.Pin_0, IC1.Out_3
  N4: R5.Pin_1, J7.pin3, J8.pin3
  N5: R7.Pin_0, IC1.Out_5
  N6: R7.Pin_1, J7.pin5, J8.pin5
  N7: R10.Pin_0, IC1.Out_7
  N8: R10.Pin_1, J7.pin7, J8.pin7
  N9: R4.Pin_0, IC1.Out_2
  N10: R4.Pin_1, J7.pin2, J8.pin2
  N11: R6.Pin_0, IC1.Out_4
  N12: R6.Pin_1, J7.pin4, J8.pin4
  N13: R9.Pin_0, IC1.Out_6
  N14: R9.Pin_1, J7.pin6, J8.pin6
  N15: R10_2.Pin_0, IC1.Out_8
  N16: R10_2.Pin_1, J7.pin8, J8.pin8
  N17: IC1.In_1, J1.pin1
  N18: IC1.In_2, J1.pin2
  N19: IC1.In_3, J1.pin3
  N20: IC1.In_4, J1.pin4
  N21: IC1.In_5, J2.pin1
  N22: IC1.In_6, J2.pin2
  N23: IC1.In_7, J2.pin3
  N24: IC1.In_8, J2.pin4
  GND: IC1.0V, J5.pin2, IC2.0V, J6.pin2
  V-LED: IC1.COM_-_Common, J5.pin1, IC2.COM_-_Common, J6.pin1, J7.pin9, J8.pin9, J9.pin9, J10.pin9
  N25: R18.Pin_0, IC2.Out_8
  N26: R18.Pin_1, J9.pin8, J10.pin8
  N27: R16.Pin_0, IC2.Out_6
  N28: R16.Pin_1, J9.pin6, J10.pin6
  N29: R14.Pin_0, IC2.Out_4
  N30: R14.Pin_1, J9.pin4, J10.pin4
  N31: R12.Pin_0, IC2.Out_2
  N32: R12.Pin_1, J9.pin2, J10.pin2
  N33: R17.Pin_0, IC2.Out_7
  N34: R17.Pin_1, J9.pin7, J10.pin7
  N35: R15.Pin_0, IC2.Out_5
  N36: R15.Pin_1, J9.pin5, J10.pin5
  N37: R13.Pin_0, IC2.Out_3
  N38: R13.Pin_1, J9.pin3, J10.pin3
  N39: R11.Pin_0, IC2.Out_1
  N40: R11.Pin_1, J9.pin1, J10.pin1
  N41: IC2.In_1, J3.pin1
  N42: IC2.In_2, J3.pin2
  N43: IC2.In_3, J3.pin3
  N44: IC2.In_4, J3.pin4
  N45: IC2.In_5, J4.pin1
  N46: IC2.In_6, J4.pin2
  N47: IC2.In_7, J4.pin3
  N48: IC2.In_8, J4.pin4

notes:
  Signal Led Driver
  20240810 1415
  sekt1953@gmail.com
  +
  -
