# Fritzing sketch Sporbesat_003 (saved by Fritzing 0.9.6b)
breadboards: 1

parts:
  D1 = Rectifier Diode [part_number=1N4001 package="300 mil [THT]"]
  D2 = Rectifier Diode [part_number=1N4001 package="300 mil [THT]"]
  D3 = Rectifier Diode [part_number=1N4001 package="300 mil [THT]"]
  D4 = Rectifier Diode [part_number=1N4001 package="300 mil [THT]"]
  R1 = Resistor [tolerance=±5% power=0.25 resistance=100 package=THT]
  U1 = TLP620 [package="DIP (Dual Inline) [THT]"]
  D5 = Rectifier Diode [part_number=1N4001 package="300 mil [THT]"]
  D6 = Rectifier Diode [part_number=1N4001 package="300 mil [THT]"]
  D7 = Rectifier Diode [part_number=1N4001 package="300 mil [THT]"]
  D8 = Rectifier Diode [part_number=1N4001 package="300 mil [THT]"]
  R2 = Resistor [tolerance=±5% power=0.25 resistance=100 package=THT]
  Q1 = PNP-Transistor [part_number=BC557 package="TO92 [THT]"]
  R3 = Resistor [tolerance=±5% power=0.25 resistance=220 package=THT]
  LED1 = LED - 5mm [color="Red (633nm)" current=0.030 package="5 mm [THT]"]
  U3 = Sharp PC817 [part_number=PC8x7 package=THT]

nets:
  N1: D1.cathode, D2.anode, D3.anode, D4.cathode
  DCC in: D1.anode, D2.cathode, R1.Pin_0, D6.anode, D8.cathode, Q1.E
  Skinne afsnit: D3.cathode, D4.anode, U1.pin2, D5.anode, D7.cathode, R2.Pin_0
  N2: R1.Pin_1, U1.pin1
  N3: D5.cathode, D6.cathode, D7.anode, D8.anode
  N4: R2.Pin_1, Q1.B
  N5: Q1.C, R3.Pin_0
  N6: R3.Pin_1, LED1.anode
  N7: LED1.cathode, U3.Pin_1
  GND: U3.Pin_2

notes:
  +
  -
  AC

custom parts:
  TLP620: Photo-transistor optically coupled to two infrared emitting diodes connected in inverse parallel.
