# Fritzing sketch L9110H-Interface _v02 (saved by Fritzing 0.9.6b)
stripboards: 1

parts:
  J1 = female pin header, 40 pins [form="♀ (female)"]
  IO1 = ULN2803A [form="♂ (male)" package=THT]
  IO2 = ULN2803A [form="♂ (male)" package=THT]
  IO3 = ULN2803A [form="♂ (male)" package=THT]
  IO4 = ULN2803A [form="♂ (male)" package=THT]
  J2 = male pin header, 8 pins [form="♂ (male)"]
  J3 = male pin header, 8 pins [form="♂ (male)"]
  J4 = male pin header, 8 pins [form="♂ (male)"]
  J5 = male pin header, 8 pins [form="♂ (male)"]
  DC1 = HW-613 [package=THT]  # not connected
  Reset = Pushbutton [package=THT]
  J7 = male pin header, 2 pins [form="♂ (male)"]
  J6 = Screw terminal - 2 pins [package=THT]
  J8 = male pin header, 2 pins [form="♂ (male)"]
  J9 = male pin header, 2 pins [form="♂ (male)"]
  J10 = male pin header, 2 pins [form="♂ (male)"]
  J11 = male pin header, 2 pins [form="♂ (male)"]
  J12 = male pin header, 2 pins [form="♂ (male)"]
  J13 = male pin header, 2 pins [form="♂ (male)"]
  J14 = male pin header, 2 pins [form="♂ (male)"]
  J15 = male pin header, 2 pins [form="♂ (male)"]
  J16 = female pin header, 4 pins [form="♀ (female)"]

nets:
  N1: J1.pin1, IO4.pin8
  N2: J1.pin2, IO4.pin7
  N3: J1.pin3, IO4.pin6
  N4: J1.pin4, IO4.pin5
  N5: J1.pin5, IO4.pin4
  N6: J1.pin6, IO4.pin3
  N7: J1.pin7, IO4.pin2
  N8: J1.pin8, IO4.pin1
  N9: J1.pin9, J1.pin10, IO3.pin9, IO4.pin9
  N10: J1.pin11, IO3.pin8
  N11: J1.pin12, IO3.pin7
  N12: J1.pin13, IO3.pin6
  N13: J1.pin14, IO3.pin5
  N14: J1.pin15, IO3.pin4
  N15: J1.pin16, IO3.pin3
  N16: J1.pin17, IO3.pin2
  N17: J1.pin18, IO3.pin1
  N18: J1.pin19, J1.pin20, IO2.pin9
  N19: J1.pin21, IO2.pin8
  N20: J1.pin22, IO2.pin7
  N21: J1.pin23, IO2.pin6
  N22: J1.pin24, IO2.pin5
  N23: J1.pin25, IO2.pin4
  N24: J1.pin26, IO2.pin3
  N25: J1.pin27, IO2.pin2
  N26: J1.pin28, IO2.pin1
  N27: J1.pin29, J1.pin30, IO1.pin9
  N28: J1.pin31, IO1.pin8
  N29: J1.pin32, IO1.pin7
  N30: J1.pin33, IO1.pin6
  N31: J1.pin34, IO1.pin5
  N32: J1.pin35, IO1.pin4
  N33: J1.pin36, IO1.pin3
  N34: J1.pin37, IO1.pin2
  N35: J1.pin38, IO1.pin1
  GND: J1.pin39, Reset.leg1, J7.pin2, J6.pin2, J8.pin1, J9.pin1, J10.pin1, J11.pin1, J12.pin1, J13.pin1, J14.pin1, J15.pin1, J16.pin2
  12V: IO1.pin10, IO2.pin10, IO3.pin10, IO4.pin10, J6.pin1, J8.pin2, J9.pin2, J10.pin2, J11.pin2, J12.pin2, J13.pin2, J14.pin2, J15.pin2, J16.pin3
  N36: IO1.pin11, J2.pin1
  N37: IO1.pin12, J2.pin2
  N38: IO1.pin13, J2.pin3
  N39: IO1.pin14, J2.pin4
  N40: IO1.pin15, J2.pin5
  N41: IO1.pin16, J2.pin6
  N42: IO1.pin17, J2.pin7
  N43: IO1.pin18, J2.pin8
  N44: IO2.pin11, J3.pin1
  N45: IO2.pin12, J3.pin2
  N46: IO2.pin13, J3.pin3
  N47: IO2.pin14, J3.pin4
  N48: IO2.pin15, J3.pin5
  N49: IO2.pin16, J3.pin6
  N50: IO2.pin17, J3.pin7
  N51: IO2.pin18, J3.pin8
  N52: IO3.pin11, J4.pin1
  N53: IO3.pin12, J4.pin2
  N54: IO3.pin13, J4.pin3
  N55: IO3.pin14, J4.pin4
  N56: IO3.pin15, J4.pin5
  N57: IO3.pin16, J4.pin6
  N58: IO3.pin17, J4.pin7
  N59: IO3.pin18, J4.pin8
  N60: IO4.pin11, J5.pin1
  N61: IO4.pin12, J5.pin2
  N62: IO4.pin13, J5.pin3
  N63: IO4.pin14, J5.pin4
  N64: IO4.pin15, J5.pin5
  N65: IO4.pin16, J5.pin6
  N66: IO4.pin17, J5.pin7
  N67: IO4.pin18, J5.pin8
  N68: Reset.leg0, J16.pin4
  5V: J7.pin1, J16.pin1

custom parts:
  ULN2803A: Generic male header
  HW-613: DC-DC Converter, max 24V input
