# Fritzing sketch SporskifteDriver_002 (saved by Fritzing 0.9.6b)
circuit board: 14cm x 5.5cm
breadboards: 1

parts:
  Part1 = Motor Driver 1A Dual TB6612FNG [part_number=TB6612FNG]
  U2 = TLP620-4 [part_number=PC847 package="DIP (Dual Inline) [THT]"]
  U1 = TLP620-4 [part_number=PC847 package="DIP (Dual Inline) [THT]"]
  R1 = Resistor [tolerance=±5% power=0.25 resistance=220 package=THT]
  R2 = Resistor [tolerance=±5% power=0.25 resistance=220 package=THT]
  R3 = Resistor [tolerance=±5% power=0.25 resistance=220 package=THT]
  R4 = Resistor [tolerance=±5% power=0.25 resistance=220 package=THT]
  R5 = Resistor [tolerance=±5% power=0.25 resistance=220 package=THT]
  R6 = Resistor [tolerance=±5% power=0.25 resistance=220 package=THT]
  R7 = Resistor [tolerance=±5% power=0.25 resistance=220 package=THT]
  R8 = Resistor [tolerance=±5% power=0.25 resistance=220 package=THT]
  Part2 = Motor Driver 1A Dual TB6612FNG [part_number=TB6612FNG]
  J9 = screw terminal, 5 pins
  J10 = screw terminal, 5 pins
  J11 = screw terminal, 5 pins
  J12 = screw terminal, 5 pins
  U3 = TLP620-4 [part_number=PC847 package="DIP (Dual Inline) [THT]"]
  U4 = TLP620-4 [part_number=PC847 package="DIP (Dual Inline) [THT]"]
  Part4 = Motor Driver 1A Dual TB6612FNG [part_number=TB6612FNG]
  Part3 = Motor Driver 1A Dual TB6612FNG [part_number=TB6612FNG]
  J13 = screw terminal, 5 pins
  J14 = screw terminal, 5 pins
  J15 = screw terminal, 5 pins
  J16 = screw terminal, 5 pins
  R9 = Resistor [tolerance=±5% power=0.25 resistance=220 package=THT]
  R10 = Resistor [tolerance=±5% power=0.25 resistance=220 package=THT]
  R11 = Resistor [tolerance=±5% power=0.25 resistance=220 package=THT]
  R12 = Resistor [tolerance=±5% power=0.25 resistance=220 package=THT]
  R13 = Resistor [tolerance=±5% power=0.25 resistance=220 package=THT]
  R14 = Resistor [tolerance=±5% power=0.25 resistance=220 package=THT]
  R15 = Resistor [tolerance=±5% power=0.25 resistance=220 package=THT]
  R16 = Resistor [tolerance=±5% power=0.25 resistance=220 package=THT]
  J17 = screw terminal, 5 pins
  J18 = screw terminal, 5 pins
  J19 = screw terminal, 5 pins
  J20 = screw terminal, 5 pins
  J21 = screw terminal, 5 pins
  J22 = screw terminal, 5 pins
  J23 = screw terminal, 5 pins
  J24 = screw terminal, 5 pins
  J5 = male pin header, 40 pins [form="♂ (male)"]
  J25 = screw terminal, 4 pins
  J26 = screw terminal, 4 pins

nets:
  GND: Part1.GND, U2.pin2, U2.pin4, U2.pin6, U2.pin8, U2.pin9, U2.pin11, U2.pin13, U2.pin15, U1.pin2, U1.pin4, U1.pin6, U1.pin8, U1.pin9, U1.pin11, U1.pin13, U1.pin15, Part2.GND, U3.pin2, U3.pin4, U3.pin6, U3.pin8, U3.pin9, U3.pin11, U3.pin13, U3.pin15, U4.pin2, U4.pin4, U4.pin6, U4.pin8, U4.pin9, U4.pin11, U4.pin13, U4.pin15, Part4.GND, Part3.GND, J5.pin10, J5.pin20, J5.pin30, J5.pin40
  N1: Part1.B01, J10.pin4, J21.pin4
  N2: Part1.B02, J10.pin5, J21.pin5
  N3: Part1.A02, J9.pin4, J24.pin4
  N4: Part1.A01, J9.pin5, J24.pin5
  VCC: Part1.VCC, Part1.STBY, Part2.VCC, Part2.STBY, Part4.VCC, Part4.STBY, Part3.VCC, Part3.STBY, J5.pin1
  VM: Part1.VM, Part2.VM, J9.pin3, J10.pin3, J11.pin3, J12.pin3, Part4.VM, Part3.VM, J13.pin3, J14.pin3, J15.pin3, J16.pin3, J17.pin3, J18.pin3, J19.pin3, J20.pin3, J21.pin3, J22.pin3, J23.pin3, J24.pin3, J5.pin11
  N5: Part1.PWMA, Part1.PWMB
  IO_00: Part1.AIN2, J5.pin2
  IO_01: Part1.AIN1, J5.pin3
  IO_02: Part1.BIN1, J5.pin4
  IO_03: Part1.BIN2, J5.pin5
  N6: U2.pin1, R5.Pin_1
  N7: U2.pin3, R6.Pin_1
  N8: U2.pin5, R7.Pin_1
  N9: U2.pin7, R8.Pin_1
  IO_0F: U2.pin10, J5.pin19
  IO_0D: U2.pin12, J5.pin17
  IO_0B: U2.pin14, J5.pin15
  IO_09: U2.pin16, J5.pin13
  N10: U1.pin1, R1.Pin_1
  N11: U1.pin3, R2.Pin_1
  N12: U1.pin5, R3.Pin_1
  N13: U1.pin7, R4.Pin_1
  IO_0E: U1.pin10, J5.pin18
  IO_0C: U1.pin12, J5.pin16
  IO_0A: U1.pin14, J5.pin14
  IO_08: U1.pin16, J5.pin12
  N14: R1.Pin_0, J9.pin2, J24.pin2
  N15: R2.Pin_0, J9.pin1, J24.pin1
  N16: R3.Pin_0, J10.pin2, J21.pin2
  N17: R4.Pin_0, J10.pin1, J21.pin1
  N18: R5.Pin_0, J11.pin2, J23.pin2
  N19: R6.Pin_0, J11.pin1, J23.pin1
  N20: R7.Pin_0, J12.pin2, J22.pin2
  N21: R8.Pin_0, J12.pin1, J22.pin1
  N22: Part2.B01, J12.pin4, J22.pin4
  N23: Part2.B02, J12.pin5, J22.pin5
  N24: Part2.A02, J11.pin4, J23.pin4
  N25: Part2.A01, J11.pin5, J23.pin5
  N26: Part2.PWMA, Part2.PWMB
  IO_04: Part2.AIN2, J5.pin6
  IO_05: Part2.AIN1, J5.pin7
  IO_06: Part2.BIN1, J5.pin8
  IO_07: Part2.BIN2, J5.pin9
  N27: U3.pin1, R11.Pin_1
  N28: U3.pin3, R12.Pin_1
  N29: U3.pin5, R9.Pin_1
  N30: U3.pin7, R10.Pin_1
  IO_16: U3.pin10, J5.pin28
  IO_14: U3.pin12, J5.pin26
  IO_12: U3.pin14, J5.pin24
  IO_10: U3.pin16, J5.pin22
  N31: U4.pin1, R15.Pin_1
  N32: U4.pin3, R14.Pin_1
  N33: U4.pin5, R13.Pin_1
  N34: U4.pin7, R16.Pin_1
  IO_17: U4.pin10, J5.pin29
  IO_15: U4.pin12, J5.pin27
  IO_13: U4.pin14, J5.pin25
  IO_11: U4.pin16, J5.pin23
  N35: Part4.B01, J13.pin4, J18.pin4
  N36: Part4.B02, J13.pin5, J18.pin5
  N37: Part4.A02, J16.pin4, J19.pin4
  N38: Part4.A01, J16.pin5, J19.pin5
  N39: Part4.PWMA, Part4.PWMB
  IO_1C: Part4.AIN2, J5.pin36
  IO_1D: Part4.AIN1, J5.pin37
  IO_1E: Part4.BIN1, J5.pin38
  IO_1F: Part4.BIN2, J5.pin39
  N40: Part3.B01, J14.pin4, J17.pin4
  N41: Part3.B02, J14.pin5, J17.pin5
  N42: Part3.A02, J15.pin4, J20.pin4
  N43: Part3.A01, J15.pin5, J20.pin5
  N44: Part3.PWMA, Part3.PWMB
  IO_18: Part3.AIN2, J5.pin32
  IO_19: Part3.AIN1, J5.pin33
  IO_1A: Part3.BIN1, J5.pin34
  IO_1B: Part3.BIN2, J5.pin35
  N45: J13.pin1, R10.Pin_0, J18.pin1
  N46: J13.pin2, R9.Pin_0, J18.pin2
  N47: J14.pin1, R16.Pin_0, J17.pin1
  N48: J14.pin2, R13.Pin_0, J17.pin2
  N49: J15.pin1, R14.Pin_0, J20.pin1
  N50: J15.pin2, R15.Pin_0, J20.pin2
  N51: J16.pin1, R12.Pin_0, J19.pin1
  N52: J16.pin2, R11.Pin_0, J19.pin2
  N53: J25.pin1, J26.pin1
  N54: J25.pin2, J26.pin2
  N55: J25.pin3, J26.pin3
  N56: J25.pin4, J26.pin4

notes:
  12V
  3V3
  GND
  EXT
  A01
  1_A02
  1_B02
  1_B01
  SPc
  B02
  B01
  2_A01
  2_A02
  A02
  3_B02
  3_B01
  4_B01
  4_A01
  4_B02
  4_A02
  SP+
  SP-
  SporskifteDriver_002
  20240814 2202
  sekt1953@gmail.com

custom parts:
  TLP620-4: Quad Photo-transistor optically coupled to two infrared emitting diodes connected in inverse parallel.
