# Fritzing sketch TB6612FNG_00 (saved by Fritzing 0.9.6b)
stripboards: 1

parts:
  Part1 = Motor Driver 1A Dual TB6612FNG  # not connected
  J1 = screw terminal, 4 pins  # not connected
  J2 = male pin header, 3 pins [form="♂ (male)"]  # not connected
  J3 = male pin header, 3 pins [form="♂ (male)"]  # not connected
  Part2 = Motor Driver 1A Dual TB6612FNG  # not connected
  Part3 = Motor Driver 1A Dual TB6612FNG  # not connected
  Part4 = Motor Driver 1A Dual TB6612FNG  # not connected
  J4 = screw terminal, 4 pins  # not connected
  J5 = screw terminal, 4 pins  # not connected
  J6 = screw terminal, 4 pins  # not connected
  J8 = male pin header, 3 pins [form="♂ (male)"]  # not connected
  J9 = male pin header, 3 pins [form="♂ (male)"]  # not connected
  J10 = male pin header, 3 pins [form="♂ (male)"]  # not connected
  J11 = male pin header, 3 pins [form="♂ (male)"]  # not connected
  J12 = male pin header, 3 pins [form="♂ (male)"]  # not connected
  J13 = male pin header, 3 pins [form="♂ (male)"]  # not connected
  C1 = Electrolytic Capacitor [capacitance=1mF voltage=35V package="100 mil [THT, electrolytic]"]
  C2 = Electrolytic Capacitor [capacitance=1µF voltage=35V package="100 mil [THT, electrolytic]"]
  J14 = male pin header, 3 pins [form="♂ (male)"]

nets:
  N1: C1.-, C2.-, J14.pin2
  N2: C1.+, J14.pin3
  N3: C2.+, J14.pin1

notes:
  PWMA
  AIN2
  AIN1
  BIN1
  BIN2
  PWMB
  GND
  +3V3
  +12V
  A01
  A02
  B01
  B02
