# Fritzing sketch TB6612FNG_01 (saved by Fritzing 0.9.6b)
stripboards: 1

parts:
  Part1 = Motor Driver 1A Dual TB6612FNG  # not connected
  Part2 = Motor Driver 1A Dual TB6612FNG  # not connected
  Part3 = Motor Driver 1A Dual TB6612FNG  # not connected
  Part4 = Motor Driver 1A Dual TB6612FNG  # not connected
  Part5 = Motor Driver 1A Dual TB6612FNG  # not connected
  J1 = male pin header, 2 pins [form="♂ (male)"]
  J2 = male pin header, 2 pins [form="♂ (male)"]
  J3 = male pin header, 4 pins [form="♂ (male)"]
  J4 = male pin header, 2 pins [form="♂ (male)"]
  J5 = male pin header, 2 pins [form="♂ (male)"]
  J6 = male pin header, 4 pins [form="♂ (male)"]
  J7 = male pin header, 2 pins [form="♂ (male)"]
  J8 = male pin header, 2 pins [form="♂ (male)"]
  J9 = male pin header, 4 pins [form="♂ (male)"]
  J10 = male pin header, 2 pins [form="♂ (male)"]
  J11 = male pin header, 2 pins [form="♂ (male)"]
  J12 = male pin header, 4 pins [form="♂ (male)"]
  J13 = male pin header, 2 pins [form="♂ (male)"]
  J14 = male pin header, 2 pins [form="♂ (male)"]
  J15 = male pin header, 4 pins [form="♂ (male)"]
  J19 = female pin header, 8 pins [form="♀ (female)"]
  J20 = female pin header, 8 pins [form="♀ (female)"]
  J23 = female pin header, 8 pins [form="♀ (female)"]
  J24 = female pin header, 8 pins [form="♀ (female)"]
  J25 = female pin header, 8 pins [form="♀ (female)"]
  J26 = female pin header, 8 pins [form="♀ (female)"]
  J21 = female pin header, 8 pins [form="♀ (female)"]
  J22 = female pin header, 8 pins [form="♀ (female)"]
  J18 = female pin header, 8 pins [form="♀ (female)"]
  J17 = female pin header, 8 pins [form="♀ (female)"]
  J28 = male pin header, 4 pins [form="♂ (male)"]
  DC1 = HW-613 [package=THT]  # not connected
  J29 = male pin header, 2 pins [form="♂ (male)"]
  J30 = male pin header, 4 pins [form="♂ (male)"]
  J16 = male pin header, 4 pins [form="♂ (male)"]

nets:
  N1: J1.pin1, J26.pin2
  N2: J1.pin2, J26.pin3
  N3: J2.pin1, J26.pin5
  N4: J2.pin2, J26.pin6
  N5: J3.pin1, J25.pin4
  N6: J3.pin2, J25.pin5
  N7: J3.pin3, J25.pin6
  N8: J3.pin4, J25.pin7
  N9: J4.pin1, J24.pin2
  N10: J4.pin2, J24.pin3
  N11: J5.pin1, J24.pin5
  N12: J5.pin2, J24.pin6
  N13: J6.pin1, J23.pin4
  N14: J6.pin2, J23.pin5
  N15: J6.pin3, J23.pin6
  N16: J6.pin4, J23.pin7
  N17: J7.pin1, J22.pin2
  N18: J7.pin2, J22.pin3
  N19: J8.pin1, J22.pin5
  N20: J8.pin2, J22.pin6
  N21: J9.pin1, J21.pin4
  N22: J9.pin2, J21.pin5
  N23: J9.pin3, J21.pin6
  N24: J9.pin4, J21.pin7
  N25: J10.pin1, J20.pin5
  N26: J10.pin2, J20.pin6
  N27: J11.pin1, J20.pin2
  N28: J11.pin2, J20.pin3
  N29: J12.pin1, J19.pin4
  N30: J12.pin2, J19.pin5
  N31: J12.pin3, J19.pin6
  N32: J12.pin4, J19.pin7
  N33: J13.pin1, J18.pin5
  N34: J13.pin2, J18.pin6
  N35: J14.pin1, J18.pin2
  N36: J14.pin2, J18.pin3
  N37: J15.pin1, J17.pin4
  N38: J15.pin2, J17.pin5
  N39: J15.pin3, J17.pin6
  N40: J15.pin4, J17.pin7
  N41: J19.pin1, J23.pin1, J25.pin1, J21.pin1, J17.pin1, J28.pin3, J29.pin1, J30.pin4, J16.pin3, J16.pin4
  N42: J19.pin2, J20.pin1, J20.pin4, J20.pin7, J23.pin2, J24.pin1, J24.pin4, J24.pin7, J25.pin2, J26.pin1, J26.pin4, J26.pin7, J21.pin2, J22.pin1, J22.pin4, J22.pin7, J18.pin1, J18.pin4, J18.pin7, J17.pin2, J28.pin1, J30.pin1, J16.pin1
  N43: J19.pin3, J19.pin8, J20.pin8, J23.pin3, J23.pin8, J24.pin8, J25.pin3, J25.pin8, J26.pin8, J21.pin3, J21.pin8, J22.pin8, J18.pin8, J17.pin3, J17.pin8, J28.pin2, J29.pin2, J30.pin2, J16.pin2

notes:
  Input
  Motor
  3v3
  GND
  12V
  HV-613 3v3
  Key
  Power In
  Power Out
  B01
  B02
  A02
  A01

custom parts:
  HW-613: DC-DC Converter, max 24V input
