# Fritzing sketch Occupied_Hp_Proto (saved by Fritzing 0.9.6b)
stripboards: 1

parts:
  M1 = DOIT Esp32 DevKit v1 (30 pins long, 11 pins width) [part_number=ESP32S-PIN30]
  DC1 = HW-613 [package=THT]
  IO0 = PCF8574N [package="DIP16 [THT]"]
  IO1 = PCF8574N [package="DIP16 [THT]"]
  IO2 = PCF8574N [package="DIP16 [THT]"]
  IO3 = PCF8574N [package="DIP16 [THT]"]
  IO7 = PCF8574N [package="DIP16 [THT]"]
  IO6 = PCF8574N [package="DIP16 [THT]"]
  IO5 = PCF8574N [package="DIP16 [THT]"]
  IO4 = PCF8574N [package="DIP16 [THT]"]
  J1 = male pin header, 3 pins [form="♂ (male)"]
  D1 = Rectifier Diode [part_number=1N4001 package="300 mil [THT]"]
  J2 = male pin header, 4 pins [form="♂ (male)"]
  J3 = male pin header, 4 pins [form="♂ (male)"]
  J4 = male pin header, 4 pins [form="♂ (male)"]
  J5 = male pin header, 4 pins [form="♂ (male)"]
  J6 = male pin header, 4 pins [form="♂ (male)"]
  J7 = male pin header, 4 pins [form="♂ (male)"]
  J8 = male pin header, 4 pins [form="♂ (male)"]
  J9 = male pin header, 4 pins [form="♂ (male)"]
  J10 = male pin header, 4 pins [form="♂ (male)"]
  J11 = male pin header, 4 pins [form="♂ (male)"]
  R1 = Resistor [tolerance=±5% power=0.25 resistance=4.7k package=THT]
  R2 = Resistor [tolerance=±5% power=0.25 resistance=4.7k package=THT]
  J12 = male pin header, 8 pins [form="♂ (male)"]
  J13 = male pin header, 8 pins [form="♂ (male)"]
  J14 = male pin header, 8 pins [form="♂ (male)"]
  J15 = male pin header, 8 pins [form="♂ (male)"]
  J16 = male pin header, 8 pins [form="♂ (male)"]
  J17 = male pin header, 8 pins [form="♂ (male)"]
  J18 = male pin header, 8 pins [form="♂ (male)"]
  J19 = male pin header, 8 pins [form="♂ (male)"]
  J20 = male pin header, 4 pins [form="♂ (male)"]
  J21 = male pin header, 4 pins [form="♂ (male)"]
  J22 = male pin header, 4 pins [form="♂ (male)"]
  J23 = male pin header, 4 pins [form="♂ (male)"]
  J24 = male pin header, 4 pins [form="♂ (male)"]
  J25 = male pin header, 4 pins [form="♂ (male)"]
  J26 = male pin header, 4 pins [form="♂ (male)"]
  J27 = male pin header, 4 pins [form="♂ (male)"]
  J28 = male pin header, 4 pins [form="♂ (male)"]
  J29 = male pin header, 4 pins [form="♂ (male)"]
  J30 = male pin header, 4 pins [form="♂ (male)"]
  J31 = male pin header, 4 pins [form="♂ (male)"]
  J32 = male pin header, 4 pins [form="♂ (male)"]
  J33 = male pin header, 4 pins [form="♂ (male)"]
  J34 = male pin header, 4 pins [form="♂ (male)"]
  J35 = male pin header, 4 pins [form="♂ (male)"]
  J36 = male pin header, 4 pins [form="♂ (male)"]
  J37 = male pin header, 4 pins [form="♂ (male)"]
  J38 = male pin header, 4 pins [form="♂ (male)"]
  J39 = male pin header, 4 pins [form="♂ (male)"]
  J40 = male pin header, 4 pins [form="♂ (male)"]
  J41 = male pin header, 4 pins [form="♂ (male)"]

nets:
  3,3V: M1.3V3, DC1.pin1, IO0.VCC, IO1.A0, IO1.VCC, IO2.A1, IO2.VCC, IO3.A0, IO3.A1, IO3.VCC, IO7.A0, IO7.A1, IO7.A2, IO7.VCC, IO6.A1, IO6.A2, IO6.VCC, IO5.A0, IO5.A2, IO5.VCC, IO4.A2, IO4.VCC, R1.Pin_0, R2.Pin_0
  GND: M1.GND, DC1.pin2, IO0.A0, IO0.A1, IO0.A2, IO0.GND, IO1.A1, IO1.A2, IO1.GND, IO2.A0, IO2.A2, IO2.GND, IO3.A2, IO3.GND, IO7.GND, IO6.A0, IO6.GND, IO5.A1, IO5.GND, IO4.A0, IO4.A1, IO4.GND, J1.pin3
  SDA: M1.D21, IO0.SDA, IO1.SDA, IO2.SDA, IO3.SDA, IO7.SDA, IO6.SDA, IO5.SDA, IO4.SDA, R1.Pin_1
  SCL: M1.D22, IO0.SCL, IO1.SCL, IO2.SCL, IO3.SCL, IO7.SCL, IO6.SCL, IO5.SCL, IO4.SCL, R2.Pin_1
  N1: DC1.pin3, D1.cathode
  N2: DC1.pin4, J1.pin1
  N3: IO0.P0, J2.pin1
  N4: IO0.P1, J2.pin2
  N5: IO0.P2, J2.pin3
  N6: IO0.P3, J2.pin4
  N7: IO0.P4, J3.pin4
  N8: IO0.P5, J3.pin3
  N9: IO0.P6, J3.pin2
  N10: IO0.P7, J3.pin1
  N11: IO1.P0, J4.pin1
  N12: IO1.P1, J4.pin2
  N13: IO1.P2, J4.pin3
  N14: IO1.P3, J4.pin4
  N15: IO1.P4, J5.pin4
  N16: IO1.P5, J5.pin3
  N17: IO1.P6, J5.pin2
  N18: IO1.P7, J5.pin1
  N19: IO2.P0, J6.pin1
  N20: IO2.P1, J6.pin2
  N21: IO2.P2, J6.pin3
  N22: IO2.P3, J6.pin4
  N23: IO2.P4, J7.pin4
  N24: IO2.P5, J7.pin3
  N25: IO2.P6, J7.pin2
  N26: IO2.P7, J7.pin1
  N27: IO3.P0, J9.pin4
  N28: IO3.P1, J9.pin3
  N29: IO3.P2, J9.pin2
  N30: IO3.P3, J9.pin1
  N31: IO3.P4, J8.pin1
  N32: IO3.P5, J8.pin2
  N33: IO3.P6, J8.pin3
  N34: IO3.P7, J8.pin4
  N35: IO7.P0, J41.pin4
  N36: IO7.P1, J41.pin3
  N37: IO7.P2, J41.pin2
  N38: IO7.P3, J41.pin1
  N39: IO7.P4, J40.pin1
  N40: IO7.P5, J40.pin2
  N41: IO7.P6, J40.pin3
  N42: IO7.P7, J40.pin4
  N43: IO6.P0, J39.pin4
  N44: IO6.P1, J39.pin3
  N45: IO6.P2, J39.pin2
  N46: IO6.P3, J39.pin1
  N47: IO6.P4, J38.pin1
  N48: IO6.P5, J38.pin2
  N49: IO6.P6, J38.pin3
  N50: IO6.P7, J38.pin4
  N51: IO5.P0, J28.pin4
  N52: IO5.P1, J28.pin3
  N53: IO5.P2, J28.pin2
  N54: IO5.P3, J28.pin1
  N55: IO5.P4, J29.pin1
  N56: IO5.P5, J29.pin2
  N57: IO5.P6, J29.pin3
  N58: IO5.P7, J29.pin4
  N59: IO4.P0, J10.pin1
  N60: IO4.P1, J10.pin2
  N61: IO4.P2, J10.pin3
  N62: IO4.P3, J10.pin4
  N63: IO4.P4, J11.pin4
  N64: IO4.P5, J11.pin3
  N65: IO4.P6, J11.pin2
  N66: IO4.P7, J11.pin1
  N67: J1.pin2, D1.anode
  N68: J12.pin1, J36.pin1
  N69: J12.pin2, J36.pin2
  N70: J12.pin3, J36.pin3
  N71: J12.pin4, J36.pin4
  N72: J12.pin5, J37.pin1
  N73: J12.pin6, J37.pin2
  N74: J12.pin7, J37.pin3
  N75: J12.pin8, J37.pin4
  N76: J13.pin1, J34.pin1
  N77: J13.pin2, J34.pin2
  N78: J13.pin3, J34.pin3
  N79: J13.pin4, J34.pin4
  N80: J13.pin5, J35.pin1
  N81: J13.pin6, J35.pin2
  N82: J13.pin7, J35.pin3
  N83: J13.pin8, J35.pin4
  N84: J14.pin1, J32.pin1
  N85: J14.pin2, J32.pin2
  N86: J14.pin3, J32.pin3
  N87: J14.pin4, J32.pin4
  N88: J14.pin5, J33.pin1
  N89: J14.pin6, J33.pin2
  N90: J14.pin7, J33.pin3
  N91: J14.pin8, J33.pin4
  N92: J15.pin1, J30.pin1
  N93: J15.pin2, J30.pin2
  N94: J15.pin3, J30.pin3
  N95: J15.pin4, J30.pin4
  N96: J15.pin5, J31.pin1
  N97: J15.pin6, J31.pin2
  N98: J15.pin7, J31.pin3
  N99: J15.pin8, J31.pin4
  N100: J16.pin1, J26.pin1
  N101: J16.pin2, J26.pin2
  N102: J16.pin3, J26.pin3
  N103: J16.pin4, J26.pin4
  N104: J16.pin5, J27.pin1
  N105: J16.pin6, J27.pin2
  N106: J16.pin7, J27.pin3
  N107: J16.pin8, J27.pin4
  N108: J17.pin1, J24.pin1
  N109: J17.pin2, J24.pin2
  N110: J17.pin3, J24.pin3
  N111: J17.pin4, J24.pin4
  N112: J17.pin5, J25.pin1
  N113: J17.pin6, J25.pin2
  N114: J17.pin7, J25.pin3
  N115: J17.pin8, J25.pin4
  N116: J18.pin1, J22.pin1
  N117: J18.pin2, J22.pin2
  N118: J18.pin3, J22.pin3
  N119: J18.pin4, J22.pin4
  N120: J18.pin5, J23.pin1
  N121: J18.pin6, J23.pin2
  N122: J18.pin7, J23.pin3
  N123: J18.pin8, J23.pin4
  N124: J19.pin1, J20.pin1
  N125: J19.pin2, J20.pin2
  N126: J19.pin3, J20.pin3
  N127: J19.pin4, J20.pin4
  N128: J19.pin5, J21.pin1
  N129: J19.pin6, J21.pin2
  N130: J19.pin7, J21.pin3
  N131: J19.pin8, J21.pin4

custom parts:
  DOIT Esp32 DevKit v1 (30 pins long, 11 pins width): The DOIT Esp32 DevKit v1 is one of the development board created by DOIT to evaluate the ESP-WROOM-32 module. It is based on the ESP32 microcontroller that boasts Wifi, Bluetooth, Ethernet and Low Power support all in a single chip. (vanepp) made breadboard work, adjusted pin numbering and labels and reduced size of schematic and cleaned up pcb. This chip is 30pins long (2 x15) and 11 pins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
  HW-613: DC-DC Converter, max 24V input
  PCF8574N: Remote 8-Bit I/O Expander for I 2C Bus
