# Fritzing sketch Occupied-test (saved by Fritzing 0.9.6b)
breadboards: 1

parts:
  R1 = Resistor [tolerance=±5% power=0.25 resistance=470 package=THT]
  D1 = Rectifier Diode [part_number=1N4001 package="300 mil [THT]"]
  D2 = Rectifier Diode [part_number=1N4001 package="300 mil [THT]"]
  D3 = Rectifier Diode [part_number=1N4001 package="300 mil [THT]"]
  D4 = Rectifier Diode [part_number=1N4001 package="300 mil [THT]"]
  D5 = Rectifier Diode [part_number=1N4001 package="300 mil [THT]"]
  D6 = Rectifier Diode [part_number=1N4001 package="300 mil [THT]"]
  R2 = Resistor [tolerance=±5% power=0.25 resistance=2.2k package=THT]
  Q1 = PNP-Transistor [package="TO92 [THT]"]
  R3 = Resistor [tolerance=±5% power=0.25 resistance=47k package=THT]
  R4 = Resistor [tolerance=±5% power=0.25 resistance=2.2k package=THT]
  U2 = Sharp PC817 [package=THT]
  R5 = Resistor [tolerance=±5% power=0.25 resistance=22 package=THT]
  U3 = Sharp PC817 [package=THT]
  J1 = female pin header, 1 pin [form="♀ (female)"]
  J2 = female pin header, 1 pin [form="♀ (female)"]
  J3 = female pin header, 1 pin [form="♀ (female)"]
  J4 = female pin header, 1 pin [form="♀ (female)"]

nets:
  N1: R1.Pin_0, Q1.E, U3.Pin_1, J4.pin1
  DCC Line: R1.Pin_1, D3.anode, D6.cathode, R2.Pin_0, R3.Pin_0, R5.Pin_1
  DCC: D1.cathode, D4.anode, J1.pin1
  N2: D1.anode, D2.cathode, D4.cathode, D5.anode, J2.pin1
  N3: D2.anode, D3.cathode, D5.cathode, D6.anode, J3.pin1
  DCC N: R2.Pin_1, U2.Pin_2
  N4: Q1.B, R3.Pin_1
  N5: Q1.C, R4.Pin_0
  N6: R4.Pin_1, U2.Pin_1
  N7: R5.Pin_0, U3.Pin_2

notes:
  7mA
  15,4V
  3,29V ~ 2,1V
  5mA
  hfe 150
