# Fritzing sketch styring (saved by Fritzing 0.9.6b)
circuit board: 8.4519cm x 6.10241cm
breadboards: 1

parts:
  J1 = male pin header, 6 pins [form="♂ (male)"]
  J2 = male pin header, 3 pins [form="♂ (male)"]
  J3 = male pin header, 5 pins [form="♂ (male)"]
  R1 = Resistor [tolerance=±5% power=0.25 resistance=1k package=THT]
  R2 = Resistor [tolerance=±5% power=0.25 resistance=1k package=THT]
  R3 = Resistor [tolerance=±5% power=0.25 resistance=1k package=THT]
  R4 = Resistor [tolerance=±5% power=0.25 resistance=1k package=THT]
  D1 = Rectifier Diode [part_number=1N4001 package="300 mil [THT]"]
  D2 = Rectifier Diode [part_number=1N4001 package="300 mil [THT]"]
  D3 = Rectifier Diode [part_number=1N4001 package="300 mil [THT]"]
  D4 = Rectifier Diode [part_number=1N4001 package="300 mil [THT]"]
  D5 = Rectifier Diode [part_number=1N4001 package="300 mil [THT]"]
  R5 = Resistor [tolerance=±5% power=0.25 resistance=4.7k package=THT]
  R6 = Resistor [tolerance=±5% power=0.25 resistance=4.7k package=THT]
  Q1 = NPN-Transistor [package="TO92 [THT]"]
  Q2 = NPN-Transistor [package="TO92 [THT]"]
  Q3 = NPN-Transistor [package="TO92 [THT]"]
  Q4 = NPN-Transistor [package="TO92 [THT]"]
  Q5 = NPN-Transistor [package="TO92 [THT]"]
  Q6 = NPN-Transistor [package="TO92 [THT]"]
  Q7 = NPN-Transistor [package="TO92 [THT]"]
  Q8 = NPN-Transistor [package="TO92 [THT]"]
  D6 = Rectifier Diode [part_number=1N4001 package="300 mil [THT]"]
  D7 = Rectifier Diode [part_number=1N4001 package="300 mil [THT]"]
  D8 = Rectifier Diode [part_number=1N4001 package="300 mil [THT]"]
  D9 = Rectifier Diode [part_number=1N4001 package="300 mil [THT]"]
  R7 = Resistor [tolerance=±5% power=0.25 resistance=1k package=THT]
  R8 = Resistor [tolerance=±5% power=0.25 resistance=1k package=THT]
  R9 = Resistor [tolerance=±5% power=0.25 resistance=1k package=THT]
  R10 = Resistor [tolerance=±5% power=0.25 resistance=1k package=THT]
  R11 = Resistor [tolerance=±5% power=0.25 resistance=1k package=THT]
  R12 = Resistor [tolerance=±5% power=0.25 resistance=1k package=THT]
  R13 = Resistor [tolerance=±5% power=0.25 resistance=1k package=THT]
  R14 = Resistor [tolerance=±5% power=0.25 resistance=1k package=THT]
  LED1 = LED - 5mm [color="Red (633nm)" current=0.030 package="5 mm [THT]"]
  R15 = Resistor [tolerance=±5% power=0.25 resistance=330 package=THT]
  D10 = Rectifier Diode [part_number=1N4001 package="300 mil [THT]"]
  D11 = Rectifier Diode [part_number=1N4001 package="300 mil [THT]"]
  R16 = Resistor [tolerance=±5% power=0.25 resistance=4.7k package=THT]
  R17 = Resistor [tolerance=±5% power=0.25 resistance=4.7k package=THT]

nets:
  N1: J1.pin1, D1.anode, Q1.C
  5V: J1.pin2, J1.pin5, J2.pin3, D1.cathode, D2.cathode, D3.cathode
  N2: J1.pin3, D2.anode, Q2.C
  N3: J1.pin4, D3.anode, Q3.C
  N4: J1.pin6, Q4.C
  GND: J2.pin1, J2.pin2, J3.pin5, R5.Pin_1, R6.Pin_1, Q1.E, Q2.E, Q3.E, Q4.E, Q5.E, Q6.E, Q7.E, Q8.E, R7.Pin_0, R10.Pin_0, R11.Pin_0, R13.Pin_0, R15.Pin_0, R16.Pin_0, R17.Pin_0
  N5: J3.pin1, R12.Pin_0, R16.Pin_1
  N6: J3.pin2, R14.Pin_0, R17.Pin_1
  N7: J3.pin3, R3.Pin_1, D5.anode, R6.Pin_0, D11.anode
  N8: J3.pin4, R2.Pin_1, D4.anode, R5.Pin_0, D10.anode
  N9: R1.Pin_0, Q1.B
  N10: R1.Pin_1, R4.Pin_1, D6.cathode, D7.cathode, D8.cathode, D9.cathode, LED1.anode
  N11: R2.Pin_0, Q2.B
  N12: R3.Pin_0, Q3.B
  N13: R4.Pin_0, Q4.B
  N14: D4.cathode, R9.Pin_0, D11.cathode
  N15: D5.cathode, R8.Pin_0, D10.cathode
  N16: Q5.B, R8.Pin_1
  N17: Q5.C, D6.anode, R7.Pin_1
  N18: Q6.B, R9.Pin_1
  N19: Q6.C, D7.anode, R10.Pin_1
  N20: Q7.B, R14.Pin_1
  N21: Q7.C, D8.anode, R11.Pin_1
  N22: Q8.B, R12.Pin_1
  N23: Q8.C, D9.anode, R13.Pin_1
  N24: LED1.cathode, R15.Pin_1

notes:
  ULN2064B
  TIP120
