# Fritzing sketch IHC_Replacment_001 (saved by Fritzing 0.9.6b)
circuit board: 14.98cm x 8.2cm
breadboards: 1

parts:
  IO1 = PCF8574N [package="DIP16 [THT]"]
  IO2 = ULN2803A [form="♂ (male)" package=THT]
  J2 = screw terminal, 9 pins
  DC1 = HW-613 [part_number=HW-613 package=THT]
  IO3 = PCF8574N [package="DIP16 [THT]"]
  IO4 = ULN2803A [form="♂ (male)" package=THT]
  J3 = screw terminal, 9 pins
  M1 = DOIT Esp32 DevKit v1 (30 pins long, 11 pins width) [part_number=ESP32S-PIN30]
  J5 = screw terminal, 9 pins
  J6 = screw terminal, 9 pins
  Q1 = FQP27P06 [package=THT]  # not connected
  J15 = female pin header, 4 pins [form="♀ (female)"]
  J16 = female pin header, 4 pins [form="♀ (female)"]
  J1 = Screw terminal - 2 pins [package=THT]
  U2 = TLP620-4 [package="DIP (Dual Inline) [THT]"]
  R1 = Resistor [tolerance=±5% power=0.25 resistance=220 package=THT]
  R2 = Resistor [tolerance=±5% power=0.25 resistance=220 package=THT]
  R3 = Resistor [tolerance=±5% power=0.25 resistance=220 package=THT]
  R4 = Resistor [tolerance=±5% power=0.25 resistance=220 package=THT]
  J4 = screw terminal, 9 pins
  U3 = TLP620-4 [package="DIP (Dual Inline) [THT]"]
  IO5 = PCF8574N [package="DIP16 [THT]"]
  R10 = Resistor SIP 4x470Ω - 5 pins [package="SIP (Single Inline) [THT]"]
  R11 = Resistor SIP 4x470Ω - 5 pins [package="SIP (Single Inline) [THT]"]
  U4 = TLP620-4 [package="DIP (Dual Inline) [THT]"]
  R15 = Resistor [tolerance=±5% resistance=220 power=0.25 package="0805 [SMD]"]
  R8 = Resistor [tolerance=±5% resistance=220 power=0.25 package="0805 [SMD]"]
  R14 = Resistor [tolerance=±5% resistance=220 power=0.25 package="0805 [SMD]"]
  R7 = Resistor [tolerance=±5% resistance=220 power=0.25 package="0805 [SMD]"]
  R13 = Resistor [tolerance=±5% resistance=220 power=0.25 package="0805 [SMD]"]
  R6 = Resistor [tolerance=±5% resistance=220 power=0.25 package="0805 [SMD]"]
  R12 = Resistor [tolerance=±5% resistance=220 power=0.25 package="0805 [SMD]"]
  R5 = Resistor [tolerance=±5% resistance=220 power=0.25 package="0805 [SMD]"]
  J17 = screw terminal, 9 pins
  U5 = TLP620-4 [package="DIP (Dual Inline) [THT]"]
  R16 = Resistor [tolerance=±5% resistance=220 power=0.25 package="0805 [SMD]"]
  R17 = Resistor [tolerance=±5% resistance=220 power=0.25 package="0805 [SMD]"]
  R18 = Resistor [tolerance=±5% resistance=220 power=0.25 package="0805 [SMD]"]
  R19 = Resistor [tolerance=±5% resistance=220 power=0.25 package="0805 [SMD]"]
  R20 = Resistor [tolerance=±5% resistance=220 power=0.25 package="0805 [SMD]"]
  R21 = Resistor [tolerance=±5% resistance=220 power=0.25 package="0805 [SMD]"]
  R22 = Resistor [tolerance=±5% resistance=220 power=0.25 package="0805 [SMD]"]
  R23 = Resistor [tolerance=±5% resistance=220 power=0.25 package="0805 [SMD]"]
  U6 = TLP620-4 [package="DIP (Dual Inline) [THT]"]

nets:
  GND: IO1.A0, IO1.A1, IO1.A2, IO1.GND, IO2.pin9, IO3.GND, IO4.pin9, M1.GND, J15.pin2, J16.pin2, IO5.A1, IO5.A2, IO5.GND
  N1: IO1.P0, IO2.pin1
  N2: IO1.P1, IO2.pin2
  N3: IO1.P2, IO2.pin3
  N4: IO1.P3, IO2.pin4
  N5: IO1.P4, IO2.pin5
  N6: IO1.P5, IO2.pin6
  N7: IO1.P6, IO2.pin7
  N8: IO1.P7, IO2.pin8
  SCL: IO1.SCL, IO3.SCL, M1.D22, J15.pin4, J16.pin4
  SDA: IO1.SDA, IO3.SDA, M1.D21, J15.pin1, J16.pin1, IO5.SDA
  3.3V: IO1.VCC, IO3.A0, IO3.A1, IO3.A2, IO3.VCC, M1.3V3, J15.pin3, J16.pin3, IO5.A0, R11.pin1
  N9: IO2.pin10, J2.pin9, J5.pin9, J6.pin9, J4.pin9
  N10: IO2.pin11, J2.pin8
  N11: IO2.pin12, J2.pin7
  N12: IO2.pin13, J2.pin6
  N13: IO2.pin14, J2.pin5
  N14: IO2.pin15, J2.pin4
  N15: IO2.pin16, J2.pin3
  N16: IO2.pin17, J2.pin2
  N17: IO2.pin18, J2.pin1
  N18: DC1.pin2, J1.pin1
  N19: IO3.P0, IO4.pin1
  N20: IO3.P1, IO4.pin2
  N21: IO3.P2, IO4.pin3
  N22: IO3.P3, IO4.pin4
  N23: IO3.P4, IO4.pin5
  N24: IO3.P5, IO4.pin6
  N25: IO3.P6, IO4.pin7
  N26: IO3.P7, IO4.pin8
  N27: IO4.pin10, J3.pin9
  N28: IO4.pin11, J3.pin8
  N29: IO4.pin12, J3.pin7
  N30: IO4.pin13, J3.pin6
  N31: IO4.pin14, J3.pin5
  N32: IO4.pin15, J3.pin4
  N33: IO4.pin16, J3.pin3
  N34: IO4.pin17, J3.pin2
  N35: IO4.pin18, J3.pin1
  N36: J5.pin1, R5.Pin_0
  N37: J5.pin2, U4.pin7, R12.Pin_0, R12.Pin_1
  N38: J5.pin3, R6.Pin_0
  N39: J5.pin4, R13.Pin_1
  N40: J5.pin5, R7.Pin_0
  N41: J5.pin6, R14.Pin_1
  N42: J5.pin7, R8.Pin_0
  N43: J5.pin8, R15.Pin_1
  N44: U2.pin1, R4.Pin_1
  N45: U2.pin3, R3.Pin_1
  N46: U2.pin5, R2.Pin_1
  N47: U2.pin7, R1.Pin_0, R1.Pin_1, J4.pin1
  N48: U2.pin10, IO5.P7, R10.pin2
  N49: U2.pin12, IO5.P6, R10.pin3
  N50: U2.pin14, IO5.P5, R10.pin4
  N51: U2.pin16, IO5.P4, R10.pin5
  N52: R2.Pin_0, J4.pin3
  N53: R3.Pin_0, J4.pin5
  N54: R4.Pin_0, J4.pin7
  N55: U3.pin1, R8.Pin_1
  N56: U3.pin2, U3.pin4, U3.pin6, U3.pin8, U4.pin2, U4.pin4, U4.pin6, U4.pin8
  N57: U3.pin3, R7.Pin_1
  N58: U3.pin5, R6.Pin_1
  N59: U3.pin7, R5.Pin_1
  N60: IO5.P0, R11.pin5
  N61: IO5.P1, R11.pin4
  N62: IO5.P2, R11.pin3
  N63: IO5.P3, R11.pin2
  N64: IO5.VCC, R10.pin1
  N65: U4.pin1, R15.Pin_0
  N66: U4.pin3, R14.Pin_0
  N67: U4.pin5, R13.Pin_0
  N68: J17.pin1, R16.Pin_0
  N69: J17.pin2, R17.Pin_0
  N70: J17.pin3, R18.Pin_0
  N71: J17.pin4, R19.Pin_0
  N72: J17.pin5, R20.Pin_0
  N73: J17.pin6, R21.Pin_0
  N74: J17.pin7, R22.Pin_0
  N75: J17.pin8, R23.Pin_0
  N76: U5.pin1, R22.Pin_1
  N77: U5.pin3, R20.Pin_1
  N78: U5.pin5, R18.Pin_1
  N79: U5.pin7, R16.Pin_1
  N80: R17.Pin_1, U6.pin7
  N81: R19.Pin_1, U6.pin5
  N82: R21.Pin_1, U6.pin3
  N83: R23.Pin_1, U6.pin1

notes:
  SDA
  SCL
  3V3

custom parts:
  PCF8574N: Remote 8-Bit I/O Expander for I 2C Bus
  ULN2803A: Generic male header
  HW-613: DC-DC Converter, max 24V input
  DOIT Esp32 DevKit v1 (30 pins long, 11 pins width): The DOIT Esp32 DevKit v1 is one of the development board created by DOIT to evaluate the ESP-WROOM-32 module. It is based on the ESP32 microcontroller that boasts Wifi, Bluetooth, Ethernet and Low Power support all in a single chip. (vanepp) made breadboard work, adjusted pin numbering and labels and reduced size of schematic and cleaned up pcb. This chip is 30pins long (2 x15) and 11 pins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
  FQP27P06: Power Mosfet
  TLP620-4: Quad Photo-transistor optically coupled to two infrared emitting diodes connected in inverse parallel.
  Resistor SIP 4x470Ω - 5 pins: A SIP stand-in part for whatever you want. With 5 pins on a 300 mil single inline package (SIP) footprint.
