# Fritzing sketch IHC_Replacment_002 (saved by Fritzing 0.9.6b)
circuit board: 7.12cm x 8.38cm
breadboards: 1

parts:
  U1 = TLP620-4 [package="DIP (Dual Inline) [THT]"]
  J2 = screw terminal, 9 pins
  J1 = screw terminal, 9 pins
  A1 = PFC8575 module
  R24 = 8 Resistor Network [part_number=4.7kΩ package="SIP (Single Inline)"]
  R15 = Resistor [tolerance=±5% resistance=220 power=0.25 package="0805 [SMD]"]
  R8 = Resistor [tolerance=±5% resistance=220 power=0.25 package="0805 [SMD]"]
  R14 = Resistor [tolerance=±5% resistance=220 power=0.25 package="0805 [SMD]"]
  R7 = Resistor [tolerance=±5% resistance=220 power=0.25 package="0805 [SMD]"]
  R13 = Resistor [tolerance=±5% resistance=220 power=0.25 package="0805 [SMD]"]
  R6 = Resistor [tolerance=±5% resistance=220 power=0.25 package="0805 [SMD]"]
  R12 = Resistor [tolerance=±5% resistance=220 power=0.25 package="0805 [SMD]"]
  R5 = Resistor [tolerance=±5% resistance=220 power=0.25 package="0805 [SMD]"]
  R16 = Resistor [tolerance=±5% resistance=220 power=0.25 package="0805 [SMD]"]
  R17 = Resistor [tolerance=±5% resistance=220 power=0.25 package="0805 [SMD]"]
  R18 = Resistor [tolerance=±5% resistance=220 power=0.25 package="0805 [SMD]"]
  R19 = Resistor [tolerance=±5% resistance=220 power=0.25 package="0805 [SMD]"]
  R20 = Resistor [tolerance=±5% resistance=220 power=0.25 package="0805 [SMD]"]
  R21 = Resistor [tolerance=±5% resistance=220 power=0.25 package="0805 [SMD]"]
  R22 = Resistor [tolerance=±5% resistance=220 power=0.25 package="0805 [SMD]"]
  R23 = Resistor [tolerance=±5% resistance=220 power=0.25 package="0805 [SMD]"]
  R25 = 8 Resistor Network [part_number=4.7kΩ package="SIP (Single Inline)"]
  U4 = TLP620-4 [package="DIP (Dual Inline) [THT]"]
  U3 = TLP620-4 [package="DIP (Dual Inline) [THT]"]
  U2 = TLP620-4 [package="DIP (Dual Inline) [THT]"]
  J20 = female pin header, 30 pins [form="♀ (female)"]  # not connected
  A2 = PFC8575 module
  R26 = 8 Resistor Network [part_number=4.7kΩ package="SIP (Single Inline)"]
  R27 = 8 Resistor Network [part_number=4.7kΩ package="SIP (Single Inline)"]
  R28 = Resistor [tolerance=±5% resistance=220 power=0.25 package="0805 [SMD]"]
  R29 = Resistor [tolerance=±5% resistance=220 power=0.25 package="0805 [SMD]"]
  R30 = Resistor [tolerance=±5% resistance=220 power=0.25 package="0805 [SMD]"]
  R31 = Resistor [tolerance=±5% resistance=220 power=0.25 package="0805 [SMD]"]
  R32 = Resistor [tolerance=±5% resistance=220 power=0.25 package="0805 [SMD]"]
  R33 = Resistor [tolerance=±5% resistance=220 power=0.25 package="0805 [SMD]"]
  R34 = Resistor [tolerance=±5% resistance=220 power=0.25 package="0805 [SMD]"]
  R35 = Resistor [tolerance=±5% resistance=220 power=0.25 package="0805 [SMD]"]
  R36 = Resistor [tolerance=±5% resistance=220 power=0.25 package="0805 [SMD]"]
  R37 = Resistor [tolerance=±5% resistance=220 power=0.25 package="0805 [SMD]"]
  R38 = Resistor [tolerance=±5% resistance=220 power=0.25 package="0805 [SMD]"]
  R39 = Resistor [tolerance=±5% resistance=220 power=0.25 package="0805 [SMD]"]
  R40 = Resistor [tolerance=±5% resistance=220 power=0.25 package="0805 [SMD]"]
  R41 = Resistor [tolerance=±5% resistance=220 power=0.25 package="0805 [SMD]"]
  R42 = Resistor [tolerance=±5% resistance=220 power=0.25 package="0805 [SMD]"]
  R43 = Resistor [tolerance=±5% resistance=220 power=0.25 package="0805 [SMD]"]
  U5 = TLP620-4 [package="DIP (Dual Inline) [THT]"]
  U6 = TLP620-4 [package="DIP (Dual Inline) [THT]"]
  U7 = TLP620-4 [package="DIP (Dual Inline) [THT]"]
  U8 = TLP620-4 [package="DIP (Dual Inline) [THT]"]
  J21 = screw terminal, 9 pins
  J22 = screw terminal, 9 pins

nets:
  5V: U1.pin1, U1.pin3, U1.pin5, U1.pin7, U4.pin1, U4.pin3, U4.pin5, U4.pin7, U3.pin1, U3.pin3, U3.pin5, U3.pin7, U2.pin1, U2.pin3, U2.pin5, U2.pin7, U7.pin1, U7.pin3, U7.pin5, U7.pin7, U8.pin1, U8.pin3, U8.pin5, U8.pin7
  N1: U1.pin2, R8.Pin_0
  N2: U1.pin4, R7.Pin_0
  N3: U1.pin6, R6.Pin_0
  N4: U1.pin8, R5.Pin_0
  GND: U1.pin9, U1.pin11, U1.pin13, U1.pin15, J2.pin1, J1.pin1, U4.pin9, U4.pin11, U4.pin13, U4.pin15, U3.pin9, U3.pin11, U3.pin13, U3.pin15, U2.pin9, U2.pin11, U2.pin13, U2.pin15, U7.pin9, U7.pin11, U7.pin13, U7.pin15, U8.pin9, U8.pin11, U8.pin13, U8.pin15, J21.pin1
  N5: U1.pin10, A1.Pin_18, R24.2
  N6: U1.pin12, A1.Pin_16, R24.4
  N7: U1.pin14, A1.Pin_14, R24.6
  N8: U1.pin16, A1.Pin_12, R24.8
  N9: J2.pin2, R16.Pin_1
  N10: J2.pin3, R17.Pin_1
  N11: J2.pin4, R18.Pin_1
  N12: J2.pin5, R19.Pin_1
  N13: J2.pin6, R20.Pin_1
  N14: J2.pin7, R21.Pin_1
  N15: J2.pin8, R22.Pin_1
  N16: J2.pin9, R23.Pin_1
  N17: J1.pin2, R5.Pin_1
  N18: J1.pin3, R12.Pin_1
  N19: J1.pin4, R6.Pin_1
  N20: J1.pin5, R13.Pin_1
  N21: J1.pin6, R7.Pin_1
  N22: J1.pin7, R14.Pin_1
  N23: J1.pin8, R8.Pin_1
  N24: J1.pin9, R15.Pin_1
  3.3V: A1.Pin_2, A1.Pin_19, R24.1, R25.1
  N25: A1.Pin_3, R25.2, U3.pin16
  N26: A1.Pin_4, R25.3, U4.pin16
  N27: A1.Pin_5, R25.4, U3.pin14
  N28: A1.Pin_6, R25.5, U4.pin14
  N29: A1.Pin_7, R25.6, U3.pin12
  N30: A1.Pin_8, R25.7, U4.pin12
  N31: A1.Pin_9, R25.8, U3.pin10
  N32: A1.Pin_10, R25.9, U4.pin10
  N33: A1.Pin_11, R24.9, U2.pin16
  N34: A1.Pin_13, R24.7, U2.pin14
  N35: A1.Pin_15, R24.5, U2.pin12
  N36: A1.Pin_17, R24.3, U2.pin10
  N37: R15.Pin_0, U2.pin2
  N38: R14.Pin_0, U2.pin4
  N39: R13.Pin_0, U2.pin6
  N40: R12.Pin_0, U2.pin8
  N41: R16.Pin_0, U4.pin8
  N42: R17.Pin_0, U3.pin8
  N43: R18.Pin_0, U4.pin6
  N44: R19.Pin_0, U3.pin6
  N45: R20.Pin_0, U4.pin4
  N46: R21.Pin_0, U3.pin4
  N47: R22.Pin_0, U4.pin2
  N48: R23.Pin_0, U3.pin2
  N49: A2.Pin_2, A2.Pin_19, R26.1, R27.1
  N50: A2.Pin_3, R26.2, U5.pin16
  N51: A2.Pin_4, R26.3, U6.pin16
  N52: A2.Pin_5, R26.4, U5.pin14
  N53: A2.Pin_6, R26.5, U6.pin14
  N54: A2.Pin_7, R26.6, U5.pin12
  N55: A2.Pin_8, R26.7, U6.pin12
  N56: A2.Pin_9, R26.8, U5.pin10
  N57: A2.Pin_10, R26.9, U6.pin10
  N58: A2.Pin_11, R27.9, U7.pin16
  N59: A2.Pin_12, R27.8, U8.pin16
  N60: A2.Pin_13, R27.7, U7.pin14
  N61: A2.Pin_14, R27.6, U8.pin14
  N62: A2.Pin_15, R27.5, U7.pin12
  N63: A2.Pin_16, R27.4, U8.pin12
  N64: A2.Pin_17, R27.3, U7.pin10
  N65: A2.Pin_18, R27.2, U8.pin10
  N66: R28.Pin_0, U7.pin2
  N67: R28.Pin_1, J21.pin9
  N68: R29.Pin_0, U8.pin2
  N69: R29.Pin_1, J21.pin8
  N70: R30.Pin_0, U7.pin4
  N71: R30.Pin_1, J21.pin7
  N72: R31.Pin_0, U8.pin4
  N73: R31.Pin_1, J21.pin6
  N74: R32.Pin_0, U7.pin6
  N75: R32.Pin_1, J21.pin5
  N76: R33.Pin_0, U8.pin6
  N77: R33.Pin_1, J21.pin4
  N78: R34.Pin_0, U7.pin8
  N79: R34.Pin_1, J21.pin3
  N80: R35.Pin_0, U8.pin8
  N81: R35.Pin_1, J21.pin2
  N82: R36.Pin_0, U6.pin8
  N83: R36.Pin_1, J22.pin2
  N84: R37.Pin_0, U5.pin8
  N85: R37.Pin_1, J22.pin3
  N86: R38.Pin_0, U6.pin6
  N87: R38.Pin_1, J22.pin4
  N88: R39.Pin_0, U5.pin6
  N89: R39.Pin_1, J22.pin5
  N90: R40.Pin_0, U6.pin4
  N91: R40.Pin_1, J22.pin6
  N92: R41.Pin_0, U5.pin4
  N93: R41.Pin_1, J22.pin7
  N94: R42.Pin_0, U6.pin2
  N95: R42.Pin_1, J22.pin8
  N96: R43.Pin_0, U5.pin2
  N97: R43.Pin_1, J22.pin9
  N98: U5.pin1, U5.pin3, U5.pin5, U5.pin7, U6.pin1, U6.pin3, U6.pin5, U6.pin7
  N99: U5.pin9, U5.pin11, U5.pin13, U5.pin15, U6.pin9, U6.pin11, U6.pin13, U6.pin15, J22.pin1

custom parts:
  TLP620-4: Quad Photo-transistor optically coupled to two infrared emitting diodes connected in inverse parallel.
  PFC8575 module: PCF8575 IO Expander Module I2C To 16IO.
