# Fritzing sketch Sporbesat_002 (saved by Fritzing 0.9.6b)
circuit board: 8.46667cm x 5.64444cm
breadboards: 1

parts:
  10k = Resistor [tolerance=±5% power=0.25 resistance=10k package=THT]
  Q1 = PNP-Transistor [part_number=BC557 package="TO92 [THT]"]
  D1 = Rectifier Diode [part_number=1N4001 package="300 mil [THT]"]
  D2 = Rectifier Diode [part_number=1N5400 package="300 mil [THT]"]
  J1 = screw terminal, 3 pins
  IO1 = PCF8574N [package="DIP16 [THT]"]
  R2 = Resistor [tolerance=±5% power=0.25 resistance=10k package=THT]
  LED1 = LED - 3mm [color="Red (633nm)" current=0.030 package="3 mm [THT]"]
  Q2 = NPN-Transistor [part_number=BC547 package="TO92 [THT]"]
  R3 = Resistor [tolerance=±5% power=0.25 resistance=10k package=THT]
  LED2 = LED - 5mm [color="Red (633nm)" current=0.030 package="5 mm [THT]"]
  U6 = TLP620-2 [package="DIP (Dual Inline) [THT]"]
  J2 = screw terminal, 3 pins
  J3 = screw terminal, 3 pins
  R4 = Resistor [tolerance=±5% power=0.25 resistance=10k package=THT]

nets:
  N1: 10k.Pin_0, Q1.C
  N2: 10k.Pin_1, LED1.anode
  DCCin: Q1.E, D1.anode, D2.cathode, J1.pin1, Q2.E
  Skinne: Q1.B, D1.cathode, D2.anode, J1.pin3, Q2.B
  GND: J1.pin2, IO1.GND, U6.pin_2, U6.pin_4, U6.pin_5, U6.pin_7, J2.pin3, J3.pin3
  N3: IO1.P0, R2.Pin_0, U6.pin_8
  N4: IO1.P1, U6.pin_6, R4.Pin_0
  3.3V: IO1.VCC, R2.Pin_1, R4.Pin_1
  N5: LED1.cathode, U6.pin_3, J2.pin2, J3.pin2
  N6: Q2.C, R3.Pin_0
  N7: R3.Pin_1, LED2.cathode
  N8: LED2.anode, U6.pin_1, J2.pin1, J3.pin1

custom parts:
  PCF8574N: Remote 8-Bit I/O Expander for I 2C Bus
  TLP620-2: Dual Photo-transistor optically coupled to two infrared emitting diodes connected in inverse parallel.
