# Fritzing sketch Occupied-v3 (saved by Fritzing 0.9.6b)
circuit board: 10cm x 5cm
breadboards: 1

parts:
  U1 = TLP620-4 [package="DIP (Dual Inline) [THT]"]
  U2 = TLP620-4 [package="DIP (Dual Inline) [THT]"]
  IO2 = PCF8574N [package="DIP16 [THT]"]
  J2b = female pin header, 9 pins [form="♀ (female)"]
  R19 = Resistor [tolerance=±5% power=0.25 resistance=4.7k package=THT]
  R20 = Resistor [tolerance=±5% power=0.25 resistance=4.7k package=THT]
  R16 = Resistor [tolerance=±5% power=0.25 resistance=22 package=THT]
  R14 = Resistor [tolerance=±5% power=0.25 resistance=22 package=THT]
  R12 = Resistor [tolerance=±5% power=0.25 resistance=22 package=THT]
  R10 = Resistor [tolerance=±5% power=0.25 resistance=22 package=THT]
  R9 = Resistor [tolerance=±5% power=0.25 resistance=22 package=THT]
  R11 = Resistor [tolerance=±5% power=0.25 resistance=22 package=THT]
  R13 = Resistor [tolerance=±5% power=0.25 resistance=22 package=THT]
  R15 = Resistor [tolerance=±5% power=0.25 resistance=22 package=THT]
  J2a = female pin header, 9 pins [form="♀ (female)" part_number=KF141R]
  U3 = TLP620-4 [package="DIP (Dual Inline) [THT]"]
  U4 = TLP620-4 [package="DIP (Dual Inline) [THT]"]
  IO1 = PCF8574N [package="DIP16 [THT]"]
  J1a = female pin header, 9 pins [form="♀ (female)" part_number=KF141R]
  J1b = female pin header, 9 pins [form="♀ (female)"]
  R17 = female pin header, 9 pins [form="♀ (female)" part_number="8x470 R"]
  R3 = Resistor [tolerance=±5% power=0.25 resistance=22 package=THT]
  R6 = Resistor [tolerance=±5% power=0.25 resistance=22 package=THT]
  R7 = Resistor [tolerance=±5% power=0.25 resistance=22 package=THT]
  R1 = Resistor [tolerance=±5% power=0.25 resistance=22 package=THT]
  R8 = Resistor [tolerance=±5% power=0.25 resistance=22 package=THT]
  R5 = Resistor [tolerance=±5% power=0.25 resistance=22 package=THT]
  R4 = Resistor [tolerance=±5% power=0.25 resistance=22 package=THT]
  R2 = Resistor [tolerance=±5% power=0.25 resistance=22 package=THT]
  R21 = Resistor [tolerance=±5% power=0.25 resistance=10k package=THT]
  R22 = Resistor [tolerance=±5% power=0.25 resistance=10k package=THT]
  Pad1 = Pad [width=2.54 height=1.27 connect=center]
  A1 = Pad [width=2.54 height=1.27 connect=center]
  A2 = Pad [width=2.54 height=1.27 connect=center]
  Pad2 = Pad [width=2.54 height=1.27 connect=center]
  R18 = female pin header, 9 pins [form="♀ (female)"]
  J4 = male pin header, 4 pins [form="♂ (male)"]
  J3 = male pin header, 4 pins [form="♂ (male)"]

nets:
  N1: U1.pin1, U1.pin3, U1.pin5, U1.pin7, U2.pin1, U2.pin3, U2.pin5, U2.pin7, J2b.pin1, J2a.pin1, R18.pin1
  N2: U1.pin2, R9.Pin_1
  N3: U1.pin4, R10.Pin_1
  N4: U1.pin6, R11.Pin_1
  N5: U1.pin8, R12.Pin_1
  GND: U1.pin9, U1.pin11, U1.pin13, U1.pin15, U2.pin9, U2.pin11, U2.pin13, U2.pin15, IO2.A0, IO2.GND, U3.pin9, U3.pin11, U3.pin13, U3.pin15, U4.pin9, U4.pin11, U4.pin13, U4.pin15, IO1.GND, R21.Pin_1, R22.Pin_1, J4.pin4, J3.pin4
  N6: U1.pin10, IO2.P3
  N7: U1.pin12, IO2.P2
  N8: U1.pin14, IO2.P1
  N9: U1.pin16, IO2.P0
  N10: U2.pin2, R13.Pin_1
  N11: U2.pin4, R14.Pin_1
  N12: U2.pin6, R15.Pin_1
  N13: U2.pin8, R16.Pin_1
  N14: U2.pin10, IO2.P7
  N15: U2.pin12, IO2.P6
  N16: U2.pin14, IO2.P5
  N17: U2.pin16, IO2.P4
  N18: IO2.A1, IO1.A1, R22.Pin_0, A2.pad
  N19: IO2.A2, IO1.A2, R21.Pin_0, A1.pad
  N20: IO2.SCL, IO2.SDA, R19.Pin_1, R20.Pin_1, IO1.SCL, IO1.SDA, J4.pin2, J4.pin3, J3.pin2, J3.pin3
  VCC: IO2.VCC, R19.Pin_0, R20.Pin_0, IO1.A0, IO1.VCC, Pad1.pad, Pad2.pad, J4.pin1, J3.pin1
  N21: J2b.pin2, R9.Pin_0, J2a.pin2, R18.pin2
  N22: J2b.pin3, R10.Pin_0, J2a.pin3, R18.pin3
  N23: J2b.pin4, R11.Pin_0, J2a.pin4, R18.pin4
  N24: J2b.pin5, R12.Pin_0, J2a.pin5, R18.pin5
  N25: J2b.pin6, R13.Pin_0, J2a.pin6, R18.pin6
  N26: J2b.pin7, R14.Pin_0, J2a.pin7, R18.pin7
  N27: J2b.pin8, R15.Pin_0, J2a.pin8, R18.pin8
  N28: J2b.pin9, R16.Pin_0, J2a.pin9, R18.pin9
  N29: U3.pin1, U3.pin3, U3.pin5, U3.pin7, U4.pin1, U4.pin3, U4.pin5, U4.pin7, J1a.pin1, J1b.pin1, R17.pin1
  N30: U3.pin2, R1.Pin_1
  N31: U3.pin4, R2.Pin_1
  N32: U3.pin6, R3.Pin_1
  N33: U3.pin8, R4.Pin_1
  N34: U3.pin10, IO1.P3
  N35: U3.pin12, IO1.P2
  N36: U3.pin14, IO1.P1
  N37: U3.pin16, IO1.P0
  N38: U4.pin2, R5.Pin_1
  N39: U4.pin4, R6.Pin_1
  N40: U4.pin6, R7.Pin_1
  N41: U4.pin8, R8.Pin_1
  N42: U4.pin10, IO1.P7
  N43: U4.pin12, IO1.P6
  N44: U4.pin14, IO1.P5
  N45: U4.pin16, IO1.P4
  N46: J1a.pin2, J1b.pin2, R17.pin2, R1.Pin_0
  N47: J1a.pin3, J1b.pin3, R17.pin3, R2.Pin_0
  N48: J1a.pin4, J1b.pin4, R17.pin4, R3.Pin_0
  N49: J1a.pin5, J1b.pin5, R17.pin5, R4.Pin_0
  N50: J1a.pin6, J1b.pin6, R17.pin6, R5.Pin_0
  N51: J1a.pin7, J1b.pin7, R17.pin7, R6.Pin_0
  N52: J1a.pin8, J1b.pin8, R17.pin8, R7.Pin_0
  N53: J1a.pin9, J1b.pin9, R17.pin9, R8.Pin_0

custom parts:
  TLP620-4: Quad Photo-transistor optically coupled to two infrared emitting diodes connected in inverse parallel.
  PCF8574N: Remote 8-Bit I/O Expander for I 2C Bus
