# Fritzing sketch occupied_sensor (saved by Fritzing 0.9.6b)
circuit board: 7.45cm x 21.8cm
breadboards: 1

parts:
  OP1 = TLP620-4 [package="DIP (Dual Inline) [THT]"]
  OP2 = TLP620-4 [package="DIP (Dual Inline) [THT]"]
  U1 = PCF8574N [package="DIP16 [THT]"]
  OP3 = TLP620-4 [package="DIP (Dual Inline) [THT]"]
  OP4 = TLP620-4 [package="DIP (Dual Inline) [THT]"]
  U2 = PCF8574N [package="DIP16 [THT]"]
  R1 = Resistor [tolerance=±5% power=0.25 resistance=22 package=THT]
  R6 = Resistor [tolerance=±5% power=0.25 resistance=22 package=THT]
  R2 = Resistor [tolerance=±5% power=0.25 resistance=22 package=THT]
  R3 = Resistor [tolerance=±5% power=0.25 resistance=22 package=THT]
  R4 = Resistor [tolerance=±5% power=0.25 resistance=22 package=THT]
  J1 = shrouded pin header, 10 pins [form="♂ (shrouded male)"]
  R7 = Resistor [tolerance=±5% power=0.25 resistance=22 package=THT]
  R8 = Resistor [tolerance=±5% power=0.25 resistance=22 package=THT]
  R9 = Resistor [tolerance=±5% power=0.25 resistance=22 package=THT]
  J2 = shrouded pin header, 10 pins [form="♂ (shrouded male)"]
  R11 = Resistor [tolerance=±5% power=0.25 resistance=22 package=THT]
  R12 = Resistor [tolerance=±5% power=0.25 resistance=22 package=THT]
  R13 = Resistor [tolerance=±5% power=0.25 resistance=22 package=THT]
  R14 = Resistor [tolerance=±5% power=0.25 resistance=22 package=THT]
  J3 = shrouded pin header, 10 pins [form="♂ (shrouded male)"]
  R16 = Resistor [tolerance=±5% power=0.25 resistance=22 package=THT]
  R17 = Resistor [tolerance=±5% power=0.25 resistance=22 package=THT]
  R18 = Resistor [tolerance=±5% power=0.25 resistance=22 package=THT]
  R19 = Resistor [tolerance=±5% power=0.25 resistance=22 package=THT]
  J4 = shrouded pin header, 10 pins [form="♂ (shrouded male)"]
  OP6 = TLP620-4 [package="DIP (Dual Inline) [THT]"]
  OP5 = TLP620-4 [package="DIP (Dual Inline) [THT]"]
  U3 = PCF8574N [package="DIP16 [THT]"]
  R26 = Resistor [tolerance=±5% power=0.25 resistance=22 package=THT]
  R28 = Resistor [tolerance=±5% power=0.25 resistance=22 package=THT]
  R27 = Resistor [tolerance=±5% power=0.25 resistance=22 package=THT]
  R29 = Resistor [tolerance=±5% power=0.25 resistance=22 package=THT]
  R22 = Resistor [tolerance=±5% power=0.25 resistance=22 package=THT]
  R24 = Resistor [tolerance=±5% power=0.25 resistance=22 package=THT]
  R23 = Resistor [tolerance=±5% power=0.25 resistance=22 package=THT]
  R21 = Resistor [tolerance=±5% power=0.25 resistance=22 package=THT]
  J5 = shrouded pin header, 10 pins [form="♂ (shrouded male)"]
  J6 = shrouded pin header, 10 pins [form="♂ (shrouded male)"]
  OP8 = TLP620-4 [package="DIP (Dual Inline) [THT]"]
  OP7 = TLP620-4 [package="DIP (Dual Inline) [THT]"]
  U4 = PCF8574N [package="DIP16 [THT]"]
  R36 = Resistor [tolerance=±5% power=0.25 resistance=22 package=THT]
  R37 = Resistor [tolerance=±5% power=0.25 resistance=22 package=THT]
  R38 = Resistor [tolerance=±5% power=0.25 resistance=22 package=THT]
  R39 = Resistor [tolerance=±5% power=0.25 resistance=22 package=THT]
  R31 = Resistor [tolerance=±5% power=0.25 resistance=22 package=THT]
  R32 = Resistor [tolerance=±5% power=0.25 resistance=22 package=THT]
  R34 = Resistor [tolerance=±5% power=0.25 resistance=22 package=THT]
  R33 = Resistor [tolerance=±5% power=0.25 resistance=22 package=THT]
  J7 = shrouded pin header, 10 pins [form="♂ (shrouded male)"]
  J8 = shrouded pin header, 10 pins [form="♂ (shrouded male)"]
  OP10 = TLP620-4 [package="DIP (Dual Inline) [THT]"]
  OP9 = TLP620-4 [package="DIP (Dual Inline) [THT]"]
  U5 = PCF8574N [package="DIP16 [THT]"]
  R48 = Resistor [tolerance=±5% power=0.25 resistance=22 package=THT]
  R46 = Resistor [tolerance=±5% power=0.25 resistance=22 package=THT]
  R47 = Resistor [tolerance=±5% power=0.25 resistance=22 package=THT]
  R49 = Resistor [tolerance=±5% power=0.25 resistance=22 package=THT]
  R43 = Resistor [tolerance=±5% power=0.25 resistance=22 package=THT]
  R41 = Resistor [tolerance=±5% power=0.25 resistance=22 package=THT]
  R44 = Resistor [tolerance=±5% power=0.25 resistance=22 package=THT]
  R42 = Resistor [tolerance=±5% power=0.25 resistance=22 package=THT]
  J9 = shrouded pin header, 10 pins [form="♂ (shrouded male)"]
  J10 = shrouded pin header, 10 pins [form="♂ (shrouded male)"]
  R89 = male pin header, 5 pins [form="♂ (male)" part_number=4*10Kohm]
  R90 = male pin header, 5 pins [form="♂ (male)" part_number=4*10Kohm]
  R45 = male pin header, 5 pins [form="♂ (male)" part_number=4*470ohm]
  R50 = male pin header, 5 pins [form="♂ (male)" part_number=4*470ohm]
  R35 = male pin header, 5 pins [form="♂ (male)" part_number=4*470ohm]
  R40 = male pin header, 5 pins [form="♂ (male)" part_number=4*470ohm]
  R5 = male pin header, 5 pins [form="♂ (male)" part_number=4*470ohm]
  R10 = male pin header, 5 pins [form="♂ (male)" part_number=4*470ohm]
  R20 = male pin header, 5 pins [form="♂ (male)" part_number=4*470ohm]
  R15 = male pin header, 5 pins [form="♂ (male)" part_number=4*470ohm]
  R30 = male pin header, 5 pins [form="♂ (male)" part_number=4*470ohm]
  R25 = male pin header, 5 pins [form="♂ (male)" part_number=4*470ohm]
  R87 = male pin header, 5 pins [form="♂ (male)" part_number=4*10Kohm]
  R88 = male pin header, 5 pins [form="♂ (male)" part_number=4*10Kohm]
  R92 = male pin header, 5 pins [form="♂ (male)" part_number=4*10Kohm]
  R91 = male pin header, 5 pins [form="♂ (male)" part_number=4*10Kohm]
  OP12 = TLP620-4 [package="DIP (Dual Inline) [THT]"]
  OP11 = TLP620-4 [package="DIP (Dual Inline) [THT]"]
  U6 = PCF8574N [package="DIP16 [THT]"]
  R59 = Resistor [tolerance=±5% power=0.25 resistance=22 package=THT]
  R57 = Resistor [tolerance=±5% power=0.25 resistance=22 package=THT]
  R56 = Resistor [tolerance=±5% power=0.25 resistance=22 package=THT]
  R58 = Resistor [tolerance=±5% power=0.25 resistance=22 package=THT]
  R52 = Resistor [tolerance=±5% power=0.25 resistance=22 package=THT]
  R54 = Resistor [tolerance=±5% power=0.25 resistance=22 package=THT]
  R51 = Resistor [tolerance=±5% power=0.25 resistance=22 package=THT]
  R53 = Resistor [tolerance=±5% power=0.25 resistance=22 package=THT]
  R55 = male pin header, 5 pins [form="♂ (male)" part_number=4*470ohm]
  R60 = male pin header, 5 pins [form="♂ (male)" part_number=4*470ohm]
  J11 = shrouded pin header, 10 pins [form="♂ (shrouded male)"]
  J12 = shrouded pin header, 10 pins [form="♂ (shrouded male)"]
  R85 = male pin header, 5 pins [form="♂ (male)" part_number=4*10Kohm]
  R86 = male pin header, 5 pins [form="♂ (male)" part_number=4*10Kohm]
  R94 = male pin header, 5 pins [form="♂ (male)" part_number=4*10Kohm]
  R93 = male pin header, 5 pins [form="♂ (male)" part_number=4*10Kohm]
  OP14 = TLP620-4 [package="DIP (Dual Inline) [THT]"]
  OP13 = TLP620-4 [package="DIP (Dual Inline) [THT]"]
  U7 = PCF8574N [package="DIP16 [THT]"]
  R69 = Resistor [tolerance=±5% power=0.25 resistance=22 package=THT]
  R67 = Resistor [tolerance=±5% power=0.25 resistance=22 package=THT]
  R66 = Resistor [tolerance=±5% power=0.25 resistance=22 package=THT]
  R68 = Resistor [tolerance=±5% power=0.25 resistance=22 package=THT]
  R62 = Resistor [tolerance=±5% power=0.25 resistance=22 package=THT]
  R64 = Resistor [tolerance=±5% power=0.25 resistance=22 package=THT]
  R61 = Resistor [tolerance=±5% power=0.25 resistance=22 package=THT]
  R63 = Resistor [tolerance=±5% power=0.25 resistance=22 package=THT]
  R65 = male pin header, 5 pins [form="♂ (male)" part_number=4*470ohm]
  R70 = male pin header, 5 pins [form="♂ (male)" part_number=4*470ohm]
  J13 = shrouded pin header, 10 pins [form="♂ (shrouded male)"]
  J14 = shrouded pin header, 10 pins [form="♂ (shrouded male)"]
  R96 = male pin header, 5 pins [form="♂ (male)" part_number=4*10Kohm]
  R95 = male pin header, 5 pins [form="♂ (male)" part_number=4*10Kohm]
  OP16 = TLP620-4 [package="DIP (Dual Inline) [THT]"]
  OP15 = TLP620-4 [package="DIP (Dual Inline) [THT]"]
  U8 = PCF8574N [package="DIP16 [THT]"]
  R79 = Resistor [tolerance=±5% power=0.25 resistance=22 package=THT]
  R77 = Resistor [tolerance=±5% power=0.25 resistance=22 package=THT]
  R76 = Resistor [tolerance=±5% power=0.25 resistance=22 package=THT]
  R78 = Resistor [tolerance=±5% power=0.25 resistance=22 package=THT]
  R72 = Resistor [tolerance=±5% power=0.25 resistance=22 package=THT]
  R74 = Resistor [tolerance=±5% power=0.25 resistance=22 package=THT]
  R71 = Resistor [tolerance=±5% power=0.25 resistance=22 package=THT]
  R73 = Resistor [tolerance=±5% power=0.25 resistance=22 package=THT]
  R75 = male pin header, 5 pins [form="♂ (male)" part_number=4*470ohm]
  R80 = male pin header, 5 pins [form="♂ (male)" part_number=4*470ohm]
  J15 = shrouded pin header, 10 pins [form="♂ (shrouded male)"]
  J16 = shrouded pin header, 10 pins [form="♂ (shrouded male)"]
  R84 = male pin header, 5 pins [form="♂ (male)" part_number=4*10Kohm]
  R83 = male pin header, 5 pins [form="♂ (male)" part_number=4*10Kohm]
  R81 = male pin header, 5 pins [form="♂ (male)" part_number=4*10Kohm]
  R82 = male pin header, 5 pins [form="♂ (male)" part_number=4*10Kohm]
  DC1 = HW-613 [package=THT]
  Q1 = FQP27P06 [package=THT]
  R97 = Resistor [tolerance=±5% power=0.25 resistance=10k package=THT]
  D1 = Zener Diode [part_number=1N4732A breakdown_voltage=9.1V package="300 mil [THT]"]
  J18 = male pin header, 3 pins [form="♂ (male)"]
  Pad3 = Pad [width=2.54 height=2.54 connect=center]
  Pad4 = Pad [width=2.54 height=2.54 connect=center]
  J20 = female pin header, 1 pin [form="♀ (female)"]
  J19 = female pin header, 1 pin [form="♀ (female)"]  # not connected
  Pad5 = Pad [width=2.54 height=2.54 connect=center]
  Pad6 = Pad [width=2.54 height=2.54 connect=center]
  Pad2 = Pad [width=2.54 height=2.54 connect=center]
  Pad1 = Pad [width=2.54 height=2.54 connect=center]
  ESP32 = DOIT Esp32 DevKit v1 (30 pins long, 11 pins width) [part_number=ESP32S-PIN30]
  LDO1 = LDO_+3V3 [package=THT]

nets:
  N1: OP1.pin1, R1.Pin_0
  N2: OP1.pin2, OP1.pin4, OP1.pin6, OP1.pin8, OP2.pin2, OP2.pin4, OP2.pin6, OP2.pin8, OP3.pin2, OP3.pin4, OP3.pin6, OP3.pin8, OP4.pin2, OP4.pin4, OP4.pin6, OP4.pin8, J1.pin1, J1.pin2, J1.pin3, J1.pin4, J1.pin5, J1.pin6, J2.pin1, J2.pin2, J2.pin3, J2.pin4, J2.pin5, J2.pin6, J3.pin1, J3.pin2, J3.pin3, J3.pin4, J3.pin5, J3.pin6, J4.pin1, J4.pin2, J4.pin3, J4.pin4, J4.pin5, J4.pin6, OP6.pin2, OP6.pin4, OP6.pin6, OP6.pin8, OP5.pin2, OP5.pin4, OP5.pin6, OP5.pin8, J5.pin1, J5.pin2, J5.pin3, J5.pin4, J5.pin5, J5.pin6, J6.pin1, J6.pin2, J6.pin3, J6.pin4, J6.pin5, J6.pin6, OP8.pin2, OP8.pin4, OP8.pin6, OP8.pin8, OP7.pin2, OP7.pin4, OP7.pin6, OP7.pin8, J7.pin1, J7.pin2, J7.pin3, J7.pin4, J7.pin5, J7.pin6, J8.pin1, J8.pin2, J8.pin3, J8.pin4, J8.pin5, J8.pin6, OP10.pin2, OP10.pin4, OP10.pin6, OP10.pin8, OP9.pin2, OP9.pin4, OP9.pin6, OP9.pin8, J9.pin1, J9.pin2, J9.pin3, J9.pin4, J9.pin5, J9.pin6, J10.pin1, J10.pin2, J10.pin3, J10.pin4, J10.pin5, J10.pin6, R45.pin5, R50.pin5, R35.pin5, R40.pin5, R5.pin5, R10.pin5, R20.pin5, R15.pin5, R30.pin5, R25.pin5, OP12.pin2, OP12.pin4, OP12.pin6, OP12.pin8, OP11.pin2, OP11.pin4, OP11.pin6, OP11.pin8, R55.pin5, R60.pin5, J11.pin1, J11.pin2, J11.pin3, J11.pin4, J11.pin5, J11.pin6, J12.pin1, J12.pin2, J12.pin3, J12.pin4, J12.pin5, J12.pin6, OP14.pin2, OP14.pin4, OP14.pin6, OP14.pin8, OP13.pin2, OP13.pin4, OP13.pin6, OP13.pin8, R65.pin5, R70.pin5, J13.pin1, J13.pin2, J13.pin3, J13.pin4, J13.pin5, J13.pin6, J14.pin1, J14.pin2, J14.pin3, J14.pin4, J14.pin5, J14.pin6, OP16.pin2, OP16.pin4, OP16.pin6, OP16.pin8, OP15.pin2, OP15.pin4, OP15.pin6, OP15.pin8, R75.pin5, R80.pin5, J15.pin1, J15.pin2, J15.pin3, J15.pin4, J15.pin5, J15.pin6, J16.pin1, J16.pin2, J16.pin3, J16.pin4, J16.pin5, J16.pin6
  N3: OP1.pin3, R2.Pin_0
  N4: OP1.pin5, R3.Pin_1
  N5: OP1.pin7, R4.Pin_1
  GND: OP1.pin9, OP1.pin11, OP1.pin13, OP1.pin15, OP2.pin9, OP2.pin11, OP2.pin13, OP2.pin15, U1.A0, U1.A1, U1.A2, U1.GND, OP3.pin9, OP3.pin11, OP3.pin13, OP3.pin15, OP4.pin9, OP4.pin11, OP4.pin13, OP4.pin15, U2.A1, U2.A2, U2.GND, OP6.pin9, OP6.pin11, OP6.pin13, OP6.pin15, OP5.pin9, OP5.pin11, OP5.pin13, OP5.pin15, U3.A0, U3.A2, U3.GND, OP8.pin9, OP8.pin11, OP8.pin13, OP8.pin15, OP7.pin9, OP7.pin11, OP7.pin13, OP7.pin15, U4.A2, U4.GND, OP10.pin9, OP10.pin11, OP10.pin13, OP10.pin15, OP9.pin9, OP9.pin11, OP9.pin13, OP9.pin15, U5.A0, U5.A1, U5.GND, OP12.pin9, OP12.pin11, OP12.pin13, OP12.pin15, OP11.pin9, OP11.pin11, OP11.pin13, OP11.pin15, U6.A1, U6.GND, OP14.pin9, OP14.pin11, OP14.pin13, OP14.pin15, OP13.pin9, OP13.pin11, OP13.pin13, OP13.pin15, U7.A0, U7.GND, OP16.pin9, OP16.pin11, OP16.pin13, OP16.pin15, OP15.pin9, OP15.pin11, OP15.pin13, OP15.pin15, U8.GND, DC1.pin2, R97.Pin_1, J18.pin1, ESP32.GND, LDO1.pin3
  N6: OP1.pin10, U1.P3, R81.pin2
  N7: OP1.pin12, U1.P2, R81.pin3
  N8: OP1.pin14, U1.P1, R81.pin4
  N9: OP1.pin16, U1.P0, R81.pin5
  N10: OP2.pin1, R6.Pin_0
  N11: OP2.pin3, R7.Pin_0
  N12: OP2.pin5, R8.Pin_1
  N13: OP2.pin7, R9.Pin_1
  N14: OP2.pin10, U1.P7, R82.pin5
  N15: OP2.pin12, U1.P6, R82.pin4
  N16: OP2.pin14, U1.P5, R82.pin3
  N17: OP2.pin16, U1.P4, R82.pin2
  SCL: U1.SCL, U2.SCL, U3.SCL, U4.SCL, U5.SCL, U6.SCL, U7.SCL, U8.SCL, Pad2.pad, ESP32.D22
  SDA: U1.SDA, U2.SDA, U3.SDA, U4.SDA, U5.SDA, U6.SDA, U7.SDA, U8.SDA, Pad4.pad, ESP32.D21
  3.3V: U1.VCC, U2.A0, U2.VCC, U3.A1, U3.VCC, U4.A0, U4.A1, U4.VCC, U5.A2, U5.VCC, R89.pin1, R90.pin1, R87.pin1, R88.pin1, R92.pin1, R91.pin1, U6.A0, U6.A2, U6.VCC, R85.pin1, R86.pin1, R94.pin1, R93.pin1, U7.A1, U7.A2, U7.VCC, R96.pin1, R95.pin1, U8.A0, U8.A1, U8.A2, U8.VCC, R84.pin1, R83.pin1, R81.pin1, R82.pin1, LDO1.pin2
  N18: OP3.pin1, R11.Pin_0
  N19: OP3.pin3, R12.Pin_0
  N20: OP3.pin5, R13.Pin_1
  N21: OP3.pin7, R14.Pin_1
  N22: OP3.pin10, U2.P3, R83.pin2
  N23: OP3.pin12, U2.P2, R83.pin3
  N24: OP3.pin14, U2.P1, R83.pin4
  N25: OP3.pin16, U2.P0, R83.pin5
  N26: OP4.pin1, R16.Pin_0
  N27: OP4.pin3, R17.Pin_0
  N28: OP4.pin5, R18.Pin_1
  N29: OP4.pin7, R19.Pin_1
  N30: OP4.pin10, U2.P7, R84.pin5
  N31: OP4.pin12, U2.P6, R84.pin4
  N32: OP4.pin14, U2.P5, R84.pin3
  N33: OP4.pin16, U2.P4, R84.pin2
  N34: R1.Pin_1, J1.pin10, R5.pin1
  N35: R6.Pin_1, J2.pin10, R10.pin1
  N36: R2.Pin_1, J1.pin9, R5.pin2
  N37: R3.Pin_0, J1.pin8, R5.pin3
  N38: R4.Pin_0, J1.pin7, R5.pin4
  N39: R7.Pin_1, J2.pin9, R10.pin2
  N40: R8.Pin_0, J2.pin8, R10.pin3
  N41: R9.Pin_0, J2.pin7, R10.pin4
  N42: R11.Pin_1, J3.pin10, R15.pin1
  N43: R12.Pin_1, J3.pin9, R15.pin2
  N44: R13.Pin_0, J3.pin8, R15.pin3
  N45: R14.Pin_0, J3.pin7, R15.pin4
  N46: R16.Pin_1, J4.pin10, R20.pin1
  N47: R17.Pin_1, J4.pin9, R20.pin2
  N48: R18.Pin_0, J4.pin8, R20.pin3
  N49: R19.Pin_0, J4.pin7, R20.pin4
  N50: OP6.pin1, R26.Pin_0
  N51: OP6.pin3, R27.Pin_0
  N52: OP6.pin5, R28.Pin_1
  N53: OP6.pin7, R29.Pin_1
  N54: OP6.pin10, U3.P7, R86.pin5
  N55: OP6.pin12, U3.P6, R86.pin4
  N56: OP6.pin14, U3.P5, R86.pin3
  N57: OP6.pin16, U3.P4, R86.pin2
  N58: OP5.pin1, R21.Pin_0
  N59: OP5.pin3, R22.Pin_0
  N60: OP5.pin5, R23.Pin_1
  N61: OP5.pin7, R24.Pin_1
  N62: OP5.pin10, U3.P3, R85.pin2
  N63: OP5.pin12, U3.P2, R85.pin3
  N64: OP5.pin14, U3.P1, R85.pin4
  N65: OP5.pin16, U3.P0, R85.pin5
  N66: R26.Pin_1, J6.pin10, R30.pin1
  N67: R28.Pin_0, J6.pin8, R30.pin3
  N68: R27.Pin_1, J6.pin9, R30.pin2
  N69: R29.Pin_0, J6.pin7, R30.pin4
  N70: R22.Pin_1, J5.pin9, R25.pin2
  N71: R24.Pin_0, J5.pin7, R25.pin4
  N72: R23.Pin_0, J5.pin8, R25.pin3
  N73: R21.Pin_1, J5.pin10, R25.pin1
  N74: OP8.pin1, R36.Pin_0
  N75: OP8.pin3, R37.Pin_0
  N76: OP8.pin5, R38.Pin_1
  N77: OP8.pin7, R39.Pin_1
  N78: OP8.pin10, U4.P7, R88.pin5
  N79: OP8.pin12, U4.P6, R88.pin4
  N80: OP8.pin14, U4.P5, R88.pin3
  N81: OP8.pin16, U4.P4, R88.pin2
  N82: OP7.pin1, R31.Pin_0
  N83: OP7.pin3, R32.Pin_0
  N84: OP7.pin5, R33.Pin_1
  N85: OP7.pin7, R34.Pin_1
  N86: OP7.pin10, U4.P3, R87.pin2
  N87: OP7.pin12, U4.P2, R87.pin3
  N88: OP7.pin14, U4.P1, R87.pin4
  N89: OP7.pin16, U4.P0, R87.pin5
  N90: R36.Pin_1, J8.pin10, R40.pin1
  N91: R37.Pin_1, J8.pin9, R40.pin2
  N92: R38.Pin_0, J8.pin8, R40.pin3
  N93: R39.Pin_0, J8.pin7, R40.pin4
  N94: R31.Pin_1, J7.pin10, R35.pin1
  N95: R32.Pin_1, J7.pin9, R35.pin2
  N96: R34.Pin_0, J7.pin7, R35.pin4
  N97: R33.Pin_0, J7.pin8, R35.pin3
  N98: OP10.pin1, R46.Pin_0
  N99: OP10.pin3, R47.Pin_0
  N100: OP10.pin5, R48.Pin_1
  N101: OP10.pin7, R49.Pin_1
  N102: OP10.pin10, U5.P7, R90.pin5
  N103: OP10.pin12, U5.P6, R90.pin4
  N104: OP10.pin14, U5.P5, R90.pin3
  N105: OP10.pin16, U5.P4, R90.pin2
  N106: OP9.pin1, R41.Pin_0
  N107: OP9.pin3, R42.Pin_0
  N108: OP9.pin5, R43.Pin_1
  N109: OP9.pin7, R44.Pin_1
  N110: OP9.pin10, U5.P3, R89.pin2
  N111: OP9.pin12, U5.P2, R89.pin3
  N112: OP9.pin14, U5.P1, R89.pin4
  N113: OP9.pin16, U5.P0, R89.pin5
  N114: R48.Pin_0, J10.pin8, R50.pin3
  N115: R46.Pin_1, J10.pin10, R50.pin1
  N116: R47.Pin_1, J10.pin9, R50.pin2
  N117: R49.Pin_0, J10.pin7, R50.pin4
  N118: R43.Pin_0, J9.pin8, R45.pin3
  N119: R41.Pin_1, J9.pin10, R45.pin1
  N120: R44.Pin_0, J9.pin7, R45.pin4
  N121: R42.Pin_1, J9.pin9, R45.pin2
  N122: R92.pin2, OP12.pin16, U6.P4
  N123: R92.pin3, OP12.pin14, U6.P5
  N124: R92.pin4, OP12.pin12, U6.P6
  N125: R92.pin5, OP12.pin10, U6.P7
  N126: R91.pin2, OP11.pin10, U6.P3
  N127: R91.pin3, OP11.pin12, U6.P2
  N128: R91.pin4, OP11.pin14, U6.P1
  N129: R91.pin5, OP11.pin16, U6.P0
  N130: OP12.pin1, R56.Pin_0
  N131: OP12.pin3, R57.Pin_0
  N132: OP12.pin5, R58.Pin_1
  N133: OP12.pin7, R59.Pin_1
  N134: OP11.pin1, R51.Pin_0
  N135: OP11.pin3, R52.Pin_0
  N136: OP11.pin5, R53.Pin_1
  N137: OP11.pin7, R54.Pin_1
  N138: R59.Pin_0, R60.pin4, J12.pin7
  N139: R57.Pin_1, R60.pin2, J12.pin9
  N140: R56.Pin_1, R60.pin1, J12.pin10
  N141: R58.Pin_0, R60.pin3, J12.pin8
  N142: R52.Pin_1, R55.pin2, J11.pin9
  N143: R54.Pin_0, R55.pin4, J11.pin7
  N144: R51.Pin_1, R55.pin1, J11.pin10
  N145: R53.Pin_0, R55.pin3, J11.pin8
  N146: R94.pin2, OP14.pin16, U7.P4
  N147: R94.pin3, OP14.pin14, U7.P5
  N148: R94.pin4, OP14.pin12, U7.P6
  N149: R94.pin5, OP14.pin10, U7.P7
  N150: R93.pin2, OP13.pin10, U7.P3
  N151: R93.pin3, OP13.pin12, U7.P2
  N152: R93.pin4, OP13.pin14, U7.P1
  N153: R93.pin5, OP13.pin16, U7.P0
  N154: OP14.pin1, R66.Pin_0
  N155: OP14.pin3, R67.Pin_0
  N156: OP14.pin5, R68.Pin_1
  N157: OP14.pin7, R69.Pin_1
  N158: OP13.pin1, R61.Pin_0
  N159: OP13.pin3, R62.Pin_0
  N160: OP13.pin5, R63.Pin_1
  N161: OP13.pin7, R64.Pin_1
  N162: R69.Pin_0, R70.pin4, J14.pin7
  N163: R67.Pin_1, R70.pin2, J14.pin9
  N164: R66.Pin_1, R70.pin1, J14.pin10
  N165: R68.Pin_0, R70.pin3, J14.pin8
  N166: R62.Pin_1, R65.pin2, J13.pin9
  N167: R64.Pin_0, R65.pin4, J13.pin7
  N168: R61.Pin_1, R65.pin1, J13.pin10
  N169: R63.Pin_0, R65.pin3, J13.pin8
  N170: R96.pin2, OP16.pin16, U8.P4
  N171: R96.pin3, OP16.pin14, U8.P5
  N172: R96.pin4, OP16.pin12, U8.P6
  N173: R96.pin5, OP16.pin10, U8.P7
  N174: R95.pin2, OP15.pin10, U8.P3
  N175: R95.pin3, OP15.pin12, U8.P2
  N176: R95.pin4, OP15.pin14, U8.P1
  N177: R95.pin5, OP15.pin16, U8.P0
  N178: OP16.pin1, R76.Pin_0
  N179: OP16.pin3, R77.Pin_0
  N180: OP16.pin5, R78.Pin_1
  N181: OP16.pin7, R79.Pin_1
  N182: OP15.pin1, R71.Pin_0
  N183: OP15.pin3, R72.Pin_0
  N184: OP15.pin5, R73.Pin_1
  N185: OP15.pin7, R74.Pin_1
  N186: R79.Pin_0, R80.pin4, J16.pin7
  N187: R77.Pin_1, R80.pin2, J16.pin9
  N188: R76.Pin_1, R80.pin1, J16.pin10
  N189: R78.Pin_0, R80.pin3, J16.pin8
  N190: R72.Pin_1, R75.pin2, J15.pin9
  N191: R74.Pin_0, R75.pin4, J15.pin7
  N192: R71.Pin_1, R75.pin1, J15.pin10
  N193: R73.Pin_0, R75.pin3, J15.pin8
  5V: DC1.pin1, J20.pin1, Pad5.pad, Pad6.pad, ESP32.VIN, LDO1.pin1
  12V: DC1.pin3, Q1.pin3, D1.cathode
  N194: DC1.pin4, J18.pin3
  N195: Q1.pin1, R97.Pin_0, D1.anode
  N196: Q1.pin2, J18.pin2
  N197: Pad3.pad, ESP32.D33
  N198: Pad1.pad, ESP32.D27

notes:
  GND
  EN
  POE
  M1
  ESP32-POE

custom parts:
  TLP620-4: Quad Photo-transistor optically coupled to two infrared emitting diodes connected in inverse parallel.
  PCF8574N: Remote 8-Bit I/O Expander for I 2C Bus
  HW-613: DC-DC Converter, max 24V input
  FQP27P06: Power Mosfet
  DOIT Esp32 DevKit v1 (30 pins long, 11 pins width): The DOIT Esp32 DevKit v1 is one of the development board created by DOIT to evaluate the ESP-WROOM-32 module. It is based on the ESP32 microcontroller that boasts Wifi, Bluetooth, Ethernet and Low Power support all in a single chip. (vanepp) made breadboard work, adjusted pin numbering and labels and reduced size of schematic and cleaned up pcb. This chip is 30pins long (2 x15) and 11 pins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
  LDO_+3V3: 1A LDOVoltageRegulator
