# Fritzing sketch Olimex-ESP32-PoE_32pins_Sketch_Sketch (saved by Fritzing 0.9.6b)
breadboards: 1

parts:
  J1 = male pin header, 6 pins [form="♂ (male)"]
  J2 = male pin header, 10 pins [form="♂ (male)"]
  VCC1 = Battery
  CPU1 = Olimex-ESP32-PoE 32pins [chip_label=ESP32-PoE]

nets:
  N1: J1.pin1, CPU1.pin5
  N2: J1.pin2, CPU1.pin6
  N3: J1.pin3, CPU1.pin7
  N4: J1.pin4, CPU1.pin8
  N5: J1.pin5, CPU1.pin9
  N6: J1.pin6, CPU1.pin10
  N7: J2.pin1, CPU1.pin11
  N8: J2.pin2, CPU1.pin12
  N9: J2.pin3, CPU1.pin13
  N10: J2.pin4, CPU1.pin14
  N11: J2.pin5, CPU1.pin15
  N12: J2.pin6, CPU1.pin16
  N13: J2.pin7, CPU1.pin17
  N14: J2.pin8, CPU1.pin18
  N15: J2.pin9, CPU1.pin19
  N16: J2.pin10, CPU1.pin20
  N17: VCC1.-, CPU1.pin32
  N18: VCC1.+, CPU1.pin31
  5V: CPU1.pin1
  GND: CPU1.pin3

custom parts:
  Olimex-ESP32-PoE 32pins: Olimex ESP32 with LAN connector
