# Fritzing sketch test (saved by Fritzing 0.9.6b)
circuit board: 8.46667cm x 5.64444cm

parts:
  CPU1 = ESP32-PoE_20 [package=THT]
  J2 = female pin header, 10 pins [form="♀ (female)"]
  J1 = male pin header, 10 pins [form="♂ (male)"]
  P1 = LDO_+3V3 [package=THT]

nets:
  N1: CPU1.pin1, J1.pin10, P1.pin1
  N2: CPU1.pin2, J1.pin9, P1.pin2
  N3: CPU1.pin3, J1.pin8, P1.pin3
  N4: CPU1.pin4, J1.pin7
  N5: CPU1.pin5, J1.pin6
  N6: CPU1.pin6, J1.pin5
  N7: CPU1.pin7, J1.pin4
  N8: CPU1.pin8, J1.pin3
  N9: CPU1.pin9, J1.pin2
  N10: CPU1.pin10, J1.pin1
  N11: CPU1.pin11, J2.pin1
  N12: CPU1.pin12, J2.pin2
  N13: CPU1.pin13, J2.pin3
  N14: CPU1.pin14, J2.pin4
  N15: CPU1.pin15, J2.pin5
  N16: CPU1.pin16, J2.pin6
  N17: CPU1.pin17, J2.pin7
  N18: CPU1.pin18, J2.pin8
  N19: CPU1.pin19, J2.pin9
  N20: CPU1.pin20, J2.pin10

custom parts:
  ESP32-PoE_20: Olimex ESP32-PoE
  LDO_+3V3: 1A LDOVoltageRegulator
