# Fritzing sketch Stripboard_49x18 (saved by Fritzing 0.9.6b)
stripboards: 1

parts:
  M1 = DOIT Esp32 DevKit v1 (30 pins long, 11 pins width) [part_number=ESP32S-PIN30]
  J1 = male pin header, 3 pins [form="♂ (male)"]
  J2 = male pin header, 3 pins [form="♂ (male)"]
  DC1 = HW-613 [package=THT]

nets:
  Gnd: M1.GND, J1.pin1, J2.pin1, DC1.pin2
  DataOut: M1.D13, J2.pin2
  +5V: M1.VIN, J2.pin3, DC1.pin1
  +12V: J1.pin2, DC1.pin3
  N1: J1.pin3, DC1.pin4

notes:
  NeoPixelBus
  Power

custom parts:
  DOIT Esp32 DevKit v1 (30 pins long, 11 pins width): The DOIT Esp32 DevKit v1 is one of the development board created by DOIT to evaluate the ESP-WROOM-32 module. It is based on the ESP32 microcontroller that boasts Wifi, Bluetooth, Ethernet and Low Power support all in a single chip. (vanepp) made breadboard work, adjusted pin numbering and labels and reduced size of schematic and cleaned up pcb. This chip is 30pins long (2 x15) and 11 pins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
  HW-613: DC-DC Converter, max 24V input
